// Logisim project 16.备份out机器输出显示.circ as structural Verilog: 1 circuit, main circuit main
module main (
  input  in_1,
  input  in_2,
  input  in_3,
  input  in_4,
  input  in_5,
  input  in_6,
  input  in_7,
  input  in_8,
  input  in_9,
  input  in_10,
  input  in_11,
  input  in_12,
  input  in_13,
  input  in_14,
  input  in_15,
  input  in_16,
  input  in_17,
  input  in_18,
  input  in_19,
  input  in_20,
  input  in_21,
  input  in_22,
  input  in_23,
  input  in_24,
  input  in_25,
  input  in_26,
  input  in_27,
  input  in_28,
  input  in_29,
  input  in_30,
  input  in_31,
  input  in_32,
  input  in_33,
  input  in_34,
  input  in_35,
  input  in_36,
  input  in_37,
  input  in_38,
  input  in_39,
  input  in_40,
  input  in_41,
  input  in_42,
  input  in_43,
  input  in_44,
  input  in_45,
  input  in_46,
  input  in_47,
  input  in_48,
  input  in_49,
  input  in_50,
  input  in_51,
  input  in_52,
  input  in_53,
  input  in_54,
  input  in_55,
  input  in_56,
  input  in_57,
  input  in_58,
  input  in_59,
  input  in_60,
  input  in_61,
  input  in_62,
  input  \开关启动模拟加入新进程 ,
  input  in_64,
  input  in_65,
  input  in_66,
  input  in_67,
  input  in_68,
  input  in_69,
  input  in_70,
  input  in_71,
  input  in_72,
  input  in_73,
  input  in_74,
  input  in_75,
  input  in_76,
  input  in_77,
  input  in_78,
  input  in_79,
  input  in_80,
  input  in_81,
  input  in_82,
  input  in_83,
  input  in_84,
  input  in_85,
  input  in_86,
  input  in_87,
  input  in_88,
  input  in_89,
  input  in_90,
  input  in_91,
  input  in_92,
  input  in_93,
  input  in_94,
  input  in_95,
  input  in_96,
  input  in_97,
  input  in_98,
  input  in_99,
  input  in_100,
  input  in_101,
  input  in_102,
  input  in_103,
  input  in_104,
  input  in_105,
  input  in_106,
  input  in_107,
  input  in_108,
  input  in_109,
  input  in_110,
  input  in_111,
  input  in_112,
  input  in_113,
  input  in_114,
  input  in_115,
  input  in_116,
  input  in_117,
  input  in_118,
  input  in_119,
  input  in_120,
  input  in_121,
  input  in_122,
  input  in_123
);

  wire and_1_out, and_2_out, and_11_out, and_12_out, and_13_out, and_14_out, and_15_out, and_16_out,
       and_17_out, and_18_out, and_19_out, and_20_out, and_21_out, and_22_out, and_23_out, and_24_out,
       and_25_out, and_26_out, and_27_out, and_28_out, and_29_out, and_30_out, and_31_out, and_32_out,
       and_33_out, and_34_out, and_35_out, and_36_out, and_37_out, and_38_out, and_39_out, and_40_out,
       and_41_out, and_42_out, and_43_out, and_44_out, and_45_out, and_46_out, and_47_out, and_48_out,
       and_49_out, and_50_out, and_51_out, and_52_out, and_53_out, and_54_out, and_55_out, and_56_out,
       and_57_out, and_58_out, and_59_out, and_60_out, and_61_out, and_62_out, and_63_out, and_64_out,
       and_65_out, and_66_out, and_67_out, and_68_out, and_69_out, and_70_out, and_71_out, and_72_out,
       and_73_out, and_74_out, and_75_out, and_76_out, and_77_out, and_78_out, and_79_out, and_80_out,
       and_81_out, and_82_out, and_83_out, and_84_out, and_85_out, and_86_out, and_87_out, and_88_out,
       and_89_out, and_90_out, and_91_out, and_92_out, and_93_out, clock_1_out, clock_2_out, clock_3_out,
       clock_4_out, clock_5_out, clock_6_out, clock_7_out, clock_8_out, clock_9_out, clock_10_out,
       clock_11_out, comparator_1_eq, comparator_6_eq, comparator_6_gt, comparator_7_gt, comparator_7_lt,
       comparator_8_eq, comparator_8_lt, comparator_9_lt, comparator_10_lt, comparator_13_eq,
       comparator_14_eq, comparator_15_gt, comparator_15_lt, comparator_16_gt, comparator_16_lt,
       comparator_17_gt, comparator_17_lt, comparator_18_gt, comparator_18_lt, comparator_19_gt,
       comparator_19_lt, comparator_20_gt, comparator_20_lt, comparator_21_gt, comparator_21_lt,
       comparator_22_gt, comparator_22_lt, comparator_23_gt, comparator_23_lt, comparator_24_gt,
       comparator_24_lt, comparator_25_gt, comparator_25_lt, comparator_26_gt, comparator_26_lt,
       comparator_27_eq, comparator_28_eq, comparator_29_eq, comparator_29_lt, comparator_30_eq,
       comparator_31_eq, comparator_32_eq, comparator_33_eq, comparator_34_eq, comparator_35_eq,
       comparator_36_eq, comparator_37_eq, comparator_38_eq, comparator_39_eq, comparator_40_eq,
       comparator_41_eq, comparator_41_gt, comparator_42_eq, comparator_42_gt, comparator_43_eq,
       comparator_43_gt, comparator_44_eq, comparator_44_gt, comparator_45_eq, comparator_45_gt,
       comparator_46_eq, comparator_46_gt, comparator_47_eq, comparator_48_eq, comparator_49_eq,
       comparator_50_eq, comparator_51_eq, comparator_52_eq, comparator_53_eq, comparator_54_eq,
       comparator_55_eq, comparator_55_gt, comparator_56_eq, comparator_56_gt, comparator_57_eq,
       comparator_58_eq, comparator_59_eq, comparator_60_eq, comparator_61_eq, comparator_62_eq,
       comparator_63_eq, comparator_64_eq, comparator_65_eq, comparator_66_eq, comparator_67_eq,
       comparator_68_eq, comparator_69_eq, comparator_70_gt, comparator_71_eq, comparator_72_gt,
       comparator_73_eq, comparator_73_gt, comparator_74_eq, comparator_74_gt, comparator_75_eq,
       comparator_75_gt, comparator_76_eq, comparator_77_eq, comparator_78_eq, comparator_79_eq,
       comparator_80_eq, comparator_80_lt, comparator_81_eq, comparator_81_gt, comparator_82_eq,
       comparator_83_eq, counter_1_q, counter_4_q, counter_13_q, counter_16_q, counter_17_q, counter_39_q,
       decoder_1_out0, decoder_1_out1, decoder_1_out2, decoder_1_out3, decoder_1_out4, decoder_1_out5,
       decoder_1_out6, decoder_1_out7, decoder_2_out0, decoder_2_out1, decoder_2_out2, decoder_2_out3,
       decoder_2_out4, decoder_2_out5, decoder_2_out6, decoder_2_out7, decoder_3_out0, decoder_3_out1,
       decoder_3_out2, decoder_3_out3, decoder_4_out0, decoder_4_out1, decoder_4_out2, decoder_4_out3,
       decoder_5_out1, decoder_5_out2, decoder_5_out3, decoder_5_out4, decoder_5_out5, decoder_6_out1,
       decoder_6_out2, decoder_6_out3, decoder_6_out4, decoder_6_out5, decoder_7_out1, decoder_7_out2,
       decoder_7_out3, decoder_7_out4, decoder_7_out5, decoder_8_out1, decoder_8_out2, decoder_8_out3,
       decoder_8_out4, decoder_8_out5, decoder_9_out1, decoder_9_out2, decoder_9_out3, decoder_9_out4,
       decoder_9_out5, decoder_10_out1, decoder_10_out2, decoder_10_out3, decoder_10_out4, decoder_10_out5,
       decoder_11_out1, decoder_11_out2, decoder_11_out3, decoder_11_out4, decoder_11_out5, decoder_12_out1,
       decoder_12_out2, decoder_12_out3, decoder_12_out4, decoder_12_out5, decoder_13_out0, decoder_13_out1,
       decoder_13_out2, decoder_13_out3, decoder_13_out4, decoder_14_out0, decoder_14_out1, decoder_14_out2,
       decoder_14_out3, decoder_14_out4, decoder_15_out0, decoder_15_out1, decoder_15_out2, decoder_15_out3,
       decoder_16_out4, decoder_16_out5, decoder_16_out6, decoder_16_out7, decoder_17_out4, decoder_17_out5,
       decoder_17_out6, decoder_17_out7, decoder_18_out0, decoder_18_out1, decoder_18_out7, decoder_19_out0,
       decoder_19_out1, decoder_19_out3, decoder_20_out4, decoder_20_out5, decoder_20_out6, decoder_20_out7,
       decoder_21_out0, decoder_21_out1, decoder_21_out2, decoder_21_out3, decoder_22_out0, decoder_22_out1,
       decoder_22_out2, decoder_22_out3, decoder_22_out4, decoder_22_out5, decoder_22_out6, decoder_23_out0,
       decoder_23_out1, decoder_23_out2, decoder_23_out3, decoder_23_out4, decoder_23_out5, decoder_23_out6,
       decoder_23_out7, decoder_24_out0, decoder_24_out1, decoder_24_out2, decoder_24_out3, decoder_24_out4,
       decoder_24_out5, decoder_24_out6, decoder_24_out7, decoder_25_out0, decoder_25_out1, decoder_25_out2,
       decoder_25_out3, decoder_25_out4, decoder_25_out5, decoder_25_out6, decoder_25_out7,
       demultiplexer_2_out0, demultiplexer_2_out1, demultiplexer_3_out0, demultiplexer_3_out1,
       demultiplexer_4_out0, demultiplexer_4_out1, demultiplexer_5_out0, demultiplexer_5_out1,
       demultiplexer_6_out0, demultiplexer_6_out1, demultiplexer_7_out0, demultiplexer_7_out1,
       demultiplexer_8_out0, demultiplexer_8_out1, demultiplexer_13_out0, demultiplexer_13_out1,
       demultiplexer_16_out0, demultiplexer_16_out1, digital_oscilloscope_4_p3, multiplexer_54_out,
       multiplexer_70_out, multiplexer_97_out, multiplexer_98_out, multiplexer_112_out, multiplexer_114_out,
       multiplexer_122_out, multiplexer_132_out, multiplexer_143_out, not_1_out, not_2_out, not_3_out,
       not_4_out, not_5_out, not_6_out, not_7_out, not_8_out, not_9_out, not_10_out, not_11_out, not_12_out,
       not_13_out, not_15_out, not_25_out, not_26_out, not_27_out, not_28_out, not_29_out, not_30_out,
       not_31_out, not_32_out, not_48_out, not_49_out, not_50_out, not_51_out, not_52_out, not_53_out,
       not_54_out, not_56_out, not_57_out, not_59_out, not_60_out, not_61_out, not_62_out, not_63_out,
       not_64_out, not_65_out, not_66_out, not_67_out, not_68_out, not_69_out, not_70_out, not_71_out,
       not_72_out, not_73_out, not_74_out, not_75_out, not_76_out, not_77_out, not_78_out, not_79_out,
       not_80_out, not_81_out, not_83_out, not_84_out, not_85_out, not_86_out, not_87_out, not_88_out,
       not_89_out, not_90_out, not_91_out, not_92_out, not_93_out, not_94_out, not_95_out, not_96_out,
       not_97_out, not_98_out, not_99_out, not_100_out, not_101_out, not_102_out, not_103_out, not_104_out,
       not_105_out, not_107_out, not_108_out, not_109_out, not_110_out, not_111_out, not_112_out,
       not_113_out, not_114_out, not_115_out, not_116_out, not_117_out, not_118_out, not_119_out,
       not_120_out, not_121_out, not_122_out, not_123_out, not_124_out, not_125_out, not_126_out,
       not_127_out, not_128_out, not_129_out, not_130_out, not_131_out, not_132_out, not_133_out,
       not_134_out, not_135_out, or_1_out, or_2_out, or_3_out, or_4_out, or_5_out, or_6_out, or_7_out,
       or_8_out, or_20_out, or_21_out, or_22_out, or_23_out, or_24_out, or_25_out, or_26_out, or_27_out,
       or_28_out, or_29_out, or_30_out, or_31_out, or_32_out, or_33_out, or_34_out, or_35_out, or_36_out,
       or_37_out, or_38_out, or_39_out, or_40_out, or_41_out, or_42_out, or_43_out, or_44_out, or_45_out,
       or_46_out, or_47_out, or_48_out, or_49_out, or_50_out, or_51_out, or_52_out, or_53_out, or_54_out,
       or_55_out, or_56_out, or_57_out, or_58_out, or_59_out, or_60_out, or_61_out, or_62_out, or_63_out,
       or_64_out, or_65_out, or_66_out, or_67_out, or_68_out, or_69_out, or_70_out, or_71_out, or_72_out,
       or_73_out, or_74_out, or_75_out, or_76_out, or_77_out, or_78_out, or_79_out, or_80_out, or_81_out,
       or_82_out, or_83_out, or_84_out, or_85_out, or_86_out, or_87_out, or_88_out, or_89_out, or_90_out,
       or_91_out, or_92_out, or_93_out, or_94_out, or_95_out, or_96_out, or_97_out, or_98_out, or_99_out,
       or_100_out, or_101_out, or_102_out, or_103_out, or_104_out, or_105_out, or_106_out, or_107_out,
       or_108_out, or_109_out, or_110_out, or_111_out, or_112_out, or_113_out, or_114_out, or_115_out,
       or_116_out, or_117_out, or_118_out, or_119_out, or_120_out, or_121_out, or_122_out, or_123_out,
       or_124_out, or_125_out, or_126_out, or_127_out, or_128_out, or_129_out, or_130_out, or_131_out,
       or_132_out, or_133_out, or_134_out, or_135_out, or_136_out, or_137_out, or_138_out, or_139_out,
       or_140_out, or_141_out, or_142_out, or_143_out, priority_encoder_1_gs, priority_encoder_2_gs,
       priority_encoder_5_gs, priority_encoder_6_gs, priority_encoder_7_gs, priority_encoder_9_gs,
       priority_encoder_10_gs, priority_encoder_11_gs, priority_encoder_12_gs, register_4_q, register_20_q,
       register_21_q, register_22_q, register_23_q, register_24_q, register_26_q, register_28_q,
       register_31_q, register_32_q, register_33_q, register_34_q, register_35_q, register_42_q,
       register_43_q, register_46_q, register_117_q, register_118_q, register_119_q, register_120_q,
       register_121_q, register_122_q, register_123_q, register_124_q, register_144_q, register_146_q,
       register_147_q, register_148_q, register_149_q, register_159_q, register_160_q, register_161_q,
       register_162_q, register_172_q, register_176_q, register_184_q, register_188_q, register_190_q,
       rom_2_data, rom_3_data, slider_25_out, slider_26_out, slider_34_out, slider_35_out, slider_54_out,
       slider_64_out, undriven_4, undriven_6, undriven_7, undriven_8, undriven_10, undriven_11, undriven_12,
       undriven_26, undriven_27, undriven_28, undriven_31, undriven_35, undriven_36, undriven_37,
       undriven_38, undriven_43, undriven_44, undriven_45, undriven_46, undriven_53, undriven_54,
       undriven_56, undriven_58, undriven_59, undriven_61, undriven_62, undriven_63, undriven_64,
       undriven_66, undriven_70, undriven_71, undriven_74, undriven_78;
  wire [1:0] comparator_2_eq, priority_encoder_2_out, slider_9_out, undriven_52;
  wire [2:0] counter_6_q, counter_8_q, counter_9_q, counter_12_q, counter_55_q, demultiplexer_11_out0,
       demultiplexer_11_out1, demultiplexer_11_out2, demultiplexer_11_out3, demultiplexer_11_out4,
       demultiplexer_11_out5, demultiplexer_11_out6, demultiplexer_11_out7, demultiplexer_18_out1,
       demultiplexer_21_out0, demultiplexer_21_out1, demultiplexer_24_out1, demultiplexer_26_out1,
       multiplexer_11_out, multiplexer_12_out, multiplexer_13_out, multiplexer_15_out, multiplexer_16_out,
       multiplexer_56_out, multiplexer_109_out, multiplexer_110_out, multiplexer_111_out,
       multiplexer_113_out, multiplexer_128_out, multiplexer_130_out, multiplexer_131_out,
       multiplexer_133_out_2, multiplexer_133_out_4, multiplexer_133_out_5, multiplexer_133_out_6,
       multiplexer_138_out, multiplexer_139_out, multiplexer_142_out, multiplexer_147_out,
       multiplexer_151_out, multiplexer_153_out, multiplexer_154_out, multiplexer_155_out,
       priority_encoder_1_out, priority_encoder_3_out, priority_encoder_4_out, priority_encoder_5_out,
       priority_encoder_6_out, priority_encoder_7_out, priority_encoder_8_out, priority_encoder_9_out,
       priority_encoder_10_out, priority_encoder_11_out, priority_encoder_12_out, register_3_q,
       register_175_q, register_183_q, register_187_q, register_189_q, rom_6_data, rom_7_data, rom_8_data,
       slider_13_out, slider_14_out, slider_15_out, slider_16_out, slider_29_out, slider_30_out,
       slider_31_out, slider_32_out, slider_49_out, slider_52_out, slider_57_out, slider_58_out,
       slider_62_out, slider_63_out, slider_73_out, slider_80_out, slider_82_out, slider_83_out, undriven_3,
       undriven_9, undriven_73, undriven_76, undriven_77;
  wire [3:0] bitadder_1_out, multiplexer_14_out, multiplexer_32_out, multiplexer_33_out, multiplexer_41_out,
       multiplexer_43_out, multiplexer_133_out, multiplexer_133_out_7, multiplexer_140_out,
       multiplexer_140_out_2, multiplexer_140_out_3, multiplexer_140_out_4, multiplexer_140_out_5,
       multiplexer_140_out_6, multiplexer_140_out_7, multiplexer_140_out_8, slider_65_out, slider_81_out,
       undriven_5;
  wire [3:3] multiplexer_16_out_2;
  wire [4:0] joystick_1_x, joystick_1_y;
  wire [4:4] not_33_out, not_38_out, not_43_out;
  wire [5:4] not_35_out, not_40_out, not_45_out;
  wire [5:5] not_34_out, not_39_out, not_44_out;
  wire [6:0] dipswitch_1_p1, dipswitch_2_p2, dipswitch_3_p1, dipswitch_4_p8, keyboard_1_data, register_47_q,
       register_48_q, register_49_q, register_50_q, register_51_q, register_52_q, register_53_q,
       register_54_q, register_55_q, register_56_q, register_57_q, register_58_q, register_59_q,
       register_60_q, register_61_q, register_62_q, register_63_q, register_64_q, register_65_q,
       register_66_q, register_67_q, register_68_q, register_69_q, register_70_q, register_71_q,
       register_72_q, register_73_q, register_74_q, register_75_q, register_76_q, register_77_q,
       register_78_q, register_79_q, register_80_q, register_81_q, register_82_q, register_83_q,
       register_84_q, register_85_q, register_86_q, register_87_q, register_88_q, register_89_q,
       register_90_q, register_91_q, register_92_q, register_93_q, register_94_q, register_95_q,
       register_96_q, register_130_q, register_131_q, undriven_15, undriven_16, undriven_17, undriven_18,
       undriven_22, undriven_25;
  wire [6:6] not_37_out, not_42_out, not_47_out;
  wire [7:0] adder_1_out, adder_2_out, adder_3_out, adder_4_out, adder_6_out, and_3_out, counter_2_q,
       counter_3_q, counter_5_q, counter_7_q, counter_10_q, counter_14_q, counter_15_q, counter_18_q,
       counter_19_q, counter_20_q, counter_21_q, counter_22_q, counter_23_q, counter_24_q, counter_25_q,
       counter_27_q, counter_28_q, counter_30_q, counter_31_q, counter_32_q, counter_33_q, counter_34_q,
       counter_36_q, counter_37_q, counter_38_q, counter_40_q, counter_41_q, counter_42_q, counter_43_q,
       counter_44_q, counter_45_q, counter_46_q, counter_47_q, counter_48_q, counter_49_q, counter_50_q,
       counter_51_q, counter_52_q, counter_53_q, counter_56_q, counter_57_q, demultiplexer_1_out0,
       demultiplexer_1_out1, demultiplexer_1_out2, demultiplexer_1_out3, demultiplexer_1_out4,
       demultiplexer_1_out5, demultiplexer_1_out6, demultiplexer_1_out7, demultiplexer_9_out0,
       demultiplexer_9_out1, demultiplexer_9_out2, demultiplexer_9_out4, demultiplexer_9_out5,
       demultiplexer_9_out6, demultiplexer_9_out7, demultiplexer_10_out0, demultiplexer_10_out1,
       demultiplexer_15_out0, demultiplexer_15_out1, demultiplexer_17_out0, demultiplexer_17_out1,
       demultiplexer_17_out2, demultiplexer_17_out3, demultiplexer_17_out4, demultiplexer_17_out5,
       demultiplexer_17_out6, demultiplexer_17_out7, demultiplexer_20_out0, demultiplexer_20_out1,
       demultiplexer_20_out2, demultiplexer_20_out3, demultiplexer_20_out4, demultiplexer_20_out5,
       demultiplexer_20_out6, demultiplexer_20_out7, demultiplexer_23_out0, demultiplexer_23_out1,
       demultiplexer_23_out2, demultiplexer_23_out3, demultiplexer_23_out4, demultiplexer_23_out5,
       demultiplexer_23_out6, demultiplexer_23_out7, digital_oscilloscope_2_p2, multiplexer_4_out,
       multiplexer_5_out, multiplexer_6_out, multiplexer_7_out, multiplexer_8_out, multiplexer_9_out,
       multiplexer_10_out, multiplexer_17_out, multiplexer_18_out, multiplexer_19_out, multiplexer_20_out,
       multiplexer_21_out, multiplexer_22_out, multiplexer_23_out, multiplexer_24_out, multiplexer_25_out,
       multiplexer_26_out, multiplexer_27_out, multiplexer_28_out, multiplexer_29_out, multiplexer_30_out,
       multiplexer_31_out, multiplexer_34_out, multiplexer_35_out, multiplexer_36_out, multiplexer_37_out,
       multiplexer_38_out, multiplexer_39_out, multiplexer_40_out, multiplexer_44_out, multiplexer_45_out,
       multiplexer_46_out, multiplexer_47_out, multiplexer_48_out, multiplexer_49_out, multiplexer_50_out,
       multiplexer_51_out, multiplexer_53_out, multiplexer_57_out, multiplexer_58_out, multiplexer_59_out,
       multiplexer_60_out, multiplexer_61_out, multiplexer_62_out, multiplexer_63_out, multiplexer_64_out,
       multiplexer_65_out, multiplexer_66_out, multiplexer_67_out, multiplexer_68_out, multiplexer_69_out,
       multiplexer_71_out, multiplexer_72_out, multiplexer_73_out, multiplexer_74_out, multiplexer_75_out,
       multiplexer_76_out, multiplexer_77_out, multiplexer_78_out, multiplexer_79_out, multiplexer_91_out,
       multiplexer_95_out, multiplexer_96_out, multiplexer_100_out, multiplexer_101_out, multiplexer_102_out,
       multiplexer_103_out, multiplexer_104_out, multiplexer_105_out, multiplexer_106_out,
       multiplexer_123_out, multiplexer_133_out_8, multiplexer_134_out, multiplexer_135_out,
       multiplexer_136_out, multiplexer_144_out, multiplexer_145_out, multiplexer_146_out,
       multiplexer_149_out, multiplexer_150_out, multiplexer_152_out, negator_1_out, not_17_out, or_12_out,
       ram_1_data, ram_2_data, ram_5_data, register_1_q, register_2_q, register_5_q, register_6_q,
       register_7_q, register_8_q, register_9_q, register_10_q, register_11_q, register_12_q, register_13_q,
       register_14_q, register_15_q, register_16_q, register_17_q, register_18_q, register_29_q,
       register_30_q, register_36_q, register_37_q, register_38_q, register_39_q, register_40_q,
       register_41_q, register_45_q, register_97_q, register_98_q, register_99_q, register_100_q,
       register_101_q, register_102_q, register_103_q, register_104_q, register_105_q, register_106_q,
       register_115_q, register_116_q, register_125_q, register_127_q, register_129_q, register_132_q,
       register_134_q, register_135_q, register_136_q, register_137_q, register_150_q, register_151_q,
       register_152_q, register_153_q, register_158_q, register_177_q, register_178_q, register_179_q,
       register_181_q, register_182_q, register_185_q, register_186_q, rom_1_data, rom_14_data, rom_15_data,
       rom_16_data, rom_17_data, rom_18_data, rom_19_data, rom_20_data, rom_21_data, shifter_1_out,
       slider_1_out, slider_2_out, slider_3_out, slider_4_out, slider_5_out, slider_6_out, slider_7_out,
       slider_8_out, slider_10_out, slider_11_out, slider_12_out, slider_17_out, slider_18_out,
       slider_19_out, slider_20_out, slider_21_out, slider_27_out, slider_33_out, slider_36_out,
       slider_37_out, slider_38_out, slider_39_out, slider_40_out, slider_41_out, slider_42_out,
       slider_43_out, slider_44_out, slider_45_out, slider_46_out, slider_47_out, slider_48_out,
       slider_53_out, slider_56_out, slider_59_out, slider_60_out, slider_61_out, slider_66_out,
       slider_67_out, slider_68_out, slider_69_out, slider_70_out, slider_71_out, slider_72_out,
       slider_74_out, slider_75_out, slider_76_out, slider_77_out, slider_78_out, slider_79_out,
       subtractor_1_out, subtractor_2_out, subtractor_3_out, undriven, undriven_2, undriven_13, undriven_14,
       undriven_20, undriven_21, undriven_24, undriven_29, undriven_30, undriven_32, undriven_33,
       undriven_34, undriven_39, undriven_40, undriven_41, undriven_42, undriven_55, undriven_57,
       undriven_67, undriven_68, undriven_72, undriven_75;
  wire [7:3] counter_55_q_2;
  wire [7:7] comparator_3_gt, comparator_4_eq, comparator_5_lt, or_9_out, or_10_out, or_11_out;
  wire [15:8] multiplexer_137_out_2;
  wire [19:7] multiplexer_133_out_3;
  wire [31:0] demultiplexer_14_out0, demultiplexer_14_out1, demultiplexer_19_out0, demultiplexer_19_out1,
       demultiplexer_22_out0, demultiplexer_22_out1, demultiplexer_25_out0, demultiplexer_25_out1,
       multiplexer_1_out, multiplexer_2_out, multiplexer_3_out, multiplexer_80_out, multiplexer_81_out,
       multiplexer_82_out, multiplexer_83_out, multiplexer_84_out, multiplexer_85_out, multiplexer_86_out,
       multiplexer_87_out, multiplexer_88_out, multiplexer_89_out, multiplexer_90_out, multiplexer_92_out,
       multiplexer_93_out, multiplexer_94_out, multiplexer_99_out, multiplexer_115_out, multiplexer_116_out,
       multiplexer_117_out, multiplexer_118_out, multiplexer_120_out, multiplexer_124_out,
       multiplexer_125_out, multiplexer_126_out, multiplexer_127_out, multiplexer_129_out,
       multiplexer_137_out, multiplexer_148_out, ram_3_data, ram_4_data, register_19_q, register_27_q,
       register_44_q, register_107_q, register_108_q, register_109_q, register_110_q, register_111_q,
       register_112_q, register_113_q, register_114_q, register_126_q, register_133_q, register_138_q,
       register_139_q, register_140_q, register_141_q, register_142_q, register_143_q, register_145_q,
       register_154_q, register_155_q, register_156_q, register_157_q, register_163_q, register_164_q,
       register_165_q, register_166_q, register_167_q, register_168_q, register_169_q, register_170_q,
       register_171_q, register_173_q, register_174_q, register_180_q, rom_12_data, rom_13_data, rom_23_data,
       rom_24_data, rom_25_data, rom_26_data, rom_27_data, rom_28_data, rom_29_data, rom_30_data,
       rom_31_data, rom_32_data, rom_33_data, slider_22_out, slider_23_out, slider_24_out, slider_50_out,
       slider_55_out, undriven_19, undriven_23, undriven_47, undriven_48, undriven_49, undriven_50,
       undriven_51, undriven_60, undriven_65, undriven_69;

  ROM #(.addrWidth(8), .dataWidth(8), .Select("low")) rom_1 (.addr(undriven), .data(rom_1_data));
  ROM #(.addrWidth(8), .dataWidth(1), .Select("low")) rom_2 (.addr(undriven), .data(rom_2_data));
  ROM #(.addrWidth(8), .dataWidth(1), .Select("low")) rom_3 (.addr(undriven), .data(rom_3_data));
  ROM #(.addrWidth(8), .dataWidth(1), .Select("low")) rom_4 (.addr(undriven));  // open: data
  ROM #(.addrWidth(8), .dataWidth(1), .Select("low")) rom_5 (.addr(undriven));  // open: data
  ROM #(.addrWidth(8), .dataWidth(3), .Select("low")) rom_6 (.addr(undriven), .data(rom_6_data));
  ROM #(.addrWidth(8), .dataWidth(3), .Select("low")) rom_7 (.addr(undriven), .data(rom_7_data));
  ROM #(.addrWidth(8), .dataWidth(3), .Select("low")) rom_8 (.addr(undriven), .data(rom_8_data));
  ROM #(.addrWidth(8), .dataWidth(3), .Select("low")) rom_9 (.addr(undriven));  // open: data
  ROM #(.addrWidth(8), .dataWidth(3), .Select("low")) rom_10 (.addr(undriven));  // open: data
  ROM #(.addrWidth(8), .dataWidth(1), .Select("low")) rom_11 (.addr(undriven));  // open: data
  Multiplexer #(.select(1), .width(32), .disabled("Z"), .enable("false")) multiplexer_1 (
    .in0(multiplexer_2_out), .in1(register_27_q), .out(multiplexer_1_out), .sel(register_4_q));
  Multiplexer #(.select(1), .width(32), .disabled("Z"), .enable("false")) multiplexer_2 (
    .in0(register_19_q), .in1(register_133_q), .out(multiplexer_2_out), .sel(register_35_q));
  Demultiplexer #(.select(3), .width(8), .tristate("false"), .disabled("Z"), .enable("false")) demultiplexer_1 (
    .out0(demultiplexer_1_out0), .out1(demultiplexer_1_out1), .out2(demultiplexer_1_out2),
    .out3(demultiplexer_1_out3), .out4(demultiplexer_1_out4), .out5(demultiplexer_1_out5),
    .out6(demultiplexer_1_out6), .out7(demultiplexer_1_out7), .in(undriven_2), .sel(undriven_3));
  or or_1 (or_1_out, and_13_out, in_73);
  Multiplexer #(.select(1), .width(32), .disabled("Z"), .enable("false")) multiplexer_3 (
    .in0(multiplexer_1_out), .in1({32{1'b0}}), .out(multiplexer_3_out), .sel(counter_1_q));
  not not_1 (not_1_out, and_27_out);
  // NOT_Gate not_2 has open pins: in=open, out=not_2_out
  Counter #(.width(1), .max('h1), .ongoal("wrap"), .trigger("rising"), .behavior("new")) counter_1 (
    .Q(counter_1_q), .clk(and_27_out));  // open: load, D, count, carry, clr, preset, down
  Decoder #(.select(3), .tristate("false"), .disabled("Z"), .enable("false")) decoder_1 (
    .out0(decoder_1_out0), .out1(decoder_1_out1), .out2(decoder_1_out2), .out3(decoder_1_out3),
    .out4(decoder_1_out4), .out5(decoder_1_out5), .out6(decoder_1_out6), .out7(decoder_1_out7),
    .sel(undriven_3));
  Multiplexer #(.select(1), .width(8), .disabled("Z"), .enable("false")) multiplexer_4 (
    .in0(multiplexer_40_out), .in1(multiplexer_53_out), .out(multiplexer_4_out), .sel(not_3_out));
  Multiplexer #(.select(1), .width(8), .disabled("Z"), .enable("false")) multiplexer_5 (
    .in0(multiplexer_40_out), .in1(multiplexer_53_out), .out(multiplexer_5_out), .sel(not_3_out));
  Multiplexer #(.select(1), .width(8), .disabled("Z"), .enable("false")) multiplexer_6 (
    .in0(multiplexer_40_out), .in1(multiplexer_53_out), .out(multiplexer_6_out), .sel(not_3_out));
  Decoder #(.select(3), .tristate("false"), .disabled("Z"), .enable("false")) decoder_2 (
    .out0(decoder_2_out0), .out1(decoder_2_out1), .out2(decoder_2_out2), .out3(decoder_2_out3),
    .out4(decoder_2_out4), .out5(decoder_2_out5), .out6(decoder_2_out6), .out7(decoder_2_out7),
    .sel(multiplexer_11_out));
  Multiplexer #(.select(1), .width(8), .disabled("Z"), .enable("false")) multiplexer_7 (
    .in0(multiplexer_40_out), .in1(multiplexer_53_out), .out(multiplexer_7_out), .sel(not_3_out));
  Multiplexer #(.select(1), .width(8), .disabled("Z"), .enable("false")) multiplexer_8 (
    .in0(multiplexer_40_out), .in1(multiplexer_53_out), .out(multiplexer_8_out), .sel(not_3_out));
  Multiplexer #(.select(1), .width(8), .disabled("Z"), .enable("false")) multiplexer_9 (
    .in0(multiplexer_40_out), .in1(multiplexer_53_out), .out(multiplexer_9_out), .sel(not_3_out));
  Multiplexer #(.select(1), .width(8), .disabled("Z"), .enable("false")) multiplexer_10 (
    .in0(multiplexer_40_out), .in1(multiplexer_53_out), .out(multiplexer_10_out), .sel(not_3_out));
  Multiplexer #(.select(2), .width(3), .disabled("Z"), .enable("false")) multiplexer_11 (
    .in0(multiplexer_16_out), .in1(multiplexer_16_out), .in2(3'b000), .in3(multiplexer_16_out),
    .out(multiplexer_11_out), .sel(comparator_2_eq));
  not not_3 (not_3_out, or_6_out);
  not not_4 (not_4_out, counter_1_q);
  Priority_Encoder #(.select(3), .disabled("Z")) priority_encoder_1 (
    .in0(or_1_out), .in1(in_74), .in2(in_76), .in3(in_77), .in4(in_78), .in5(in_79), .in6(in_81),
    .in7(in_82), .out(priority_encoder_1_out), .gs(priority_encoder_1_gs));  // open: en_out, en_in
  // Probe on multiplexer_40_out
  // Probe on decoder_2_out0
  Counter #(.width(8), .max('hff), .ongoal("wrap"), .trigger("rising"), .behavior("new")) counter_2 (
    .load(multiplexer_54_out), .D(multiplexer_69_out), .count(not_4_out), .Q(counter_2_q), .clk(and_27_out));  // open: carry, clr, preset, down
  Multiplexer #(.select(1), .width(3), .disabled("Z"), .enable("false")) multiplexer_12 (
    .in0(3'b000), .in1(multiplexer_13_out), .out(multiplexer_12_out), .sel(not_11_out));
  Multiplexer #(.select(1), .width(3), .disabled("Z"), .enable("false")) multiplexer_13 (
    .in0(3'b000), .in1(priority_encoder_1_out), .out(multiplexer_13_out), .sel(priority_encoder_1_gs));
  and and_1 (and_1_out, not_11_out, priority_encoder_1_gs);
  Register #(.width(8), .trigger("rising"), .Select("low")) register_1 (
    .D(demultiplexer_1_out6), .en(decoder_1_out6), .Q(register_1_q), .clk(and_27_out));  // open: clr
  Register #(.width(8), .trigger("rising"), .Select("low")) register_2 (
    .D(demultiplexer_1_out7), .en(decoder_1_out7), .Q(register_2_q), .clk(and_27_out), .clr(and_27_out));
  Register #(.width(3), .trigger("rising"), .Select("low")) register_3 (
    .D(multiplexer_12_out), .en(priority_encoder_1_gs), .Q(register_3_q), .clk(and_27_out));  // open: clr
  Register #(.width(1), .trigger("rising"), .Select("low")) register_4 (
    .D(and_1_out), .en(or_2_out), .Q(register_4_q), .clk(and_27_out));  // open: clr
  Demultiplexer #(.select(1), .width(1), .tristate("false"), .disabled("Z"), .enable("false")) demultiplexer_2 (
    .out0(demultiplexer_2_out0), .out1(demultiplexer_2_out1), .in(decoder_2_out1), .sel(not_5_out));
  Register #(.width(8), .trigger("rising"), .Select("low")) register_5 (
    .D(multiplexer_4_out), .en(demultiplexer_2_out1), .Q(register_5_q), .clk(and_27_out), .cs(1'b0));  // open: clr, preset
  Demultiplexer #(.select(1), .width(1), .tristate("false"), .disabled("Z"), .enable("false")) demultiplexer_3 (
    .out0(demultiplexer_3_out0), .out1(demultiplexer_3_out1), .in(decoder_2_out2), .sel(not_5_out));
  Register #(.width(8), .trigger("rising"), .Select("low")) register_6 (
    .D(multiplexer_5_out), .en(demultiplexer_3_out1), .Q(register_6_q), .clk(and_27_out), .cs(1'b0));  // open: clr, preset
  Demultiplexer #(.select(1), .width(1), .tristate("false"), .disabled("Z"), .enable("false")) demultiplexer_4 (
    .out0(demultiplexer_4_out0), .out1(demultiplexer_4_out1), .in(decoder_2_out3), .sel(not_5_out));
  Register #(.width(8), .trigger("rising"), .Select("low")) register_7 (
    .D(multiplexer_6_out), .en(demultiplexer_4_out1), .Q(register_7_q), .clk(and_27_out), .cs(1'b0));  // open: clr, preset
  Demultiplexer #(.select(1), .width(1), .tristate("false"), .disabled("Z"), .enable("false")) demultiplexer_5 (
    .out0(demultiplexer_5_out0), .out1(demultiplexer_5_out1), .in(decoder_2_out4), .sel(not_5_out));
  Register #(.width(8), .trigger("rising"), .Select("low")) register_8 (
    .D(multiplexer_7_out), .en(demultiplexer_5_out1), .Q(register_8_q), .clk(and_27_out), .cs(1'b0));  // open: clr, preset
  Demultiplexer #(.select(1), .width(1), .tristate("false"), .disabled("Z"), .enable("false")) demultiplexer_6 (
    .out0(demultiplexer_6_out0), .out1(demultiplexer_6_out1), .in(decoder_2_out5), .sel(not_5_out));
  Register #(.width(8), .trigger("rising"), .Select("low")) register_9 (
    .D(multiplexer_8_out), .en(demultiplexer_6_out1), .Q(register_9_q), .clk(and_27_out), .cs(1'b0));  // open: clr, preset
  Demultiplexer #(.select(1), .width(1), .tristate("false"), .disabled("Z"), .enable("false")) demultiplexer_7 (
    .out0(demultiplexer_7_out0), .out1(demultiplexer_7_out1), .in(decoder_2_out6), .sel(not_5_out));
  Register #(.width(8), .trigger("rising"), .Select("low")) register_10 (
    .D(multiplexer_9_out), .en(demultiplexer_7_out1), .Q(register_10_q), .clk(and_27_out), .cs(1'b0));  // open: clr, preset
  Demultiplexer #(.select(1), .width(1), .tristate("false"), .disabled("Z"), .enable("false")) demultiplexer_8 (
    .out0(demultiplexer_8_out0), .out1(demultiplexer_8_out1), .in(decoder_2_out7), .sel(not_5_out));
  Register #(.width(8), .trigger("rising"), .Select("low")) register_11 (
    .D(multiplexer_10_out), .en(demultiplexer_8_out1), .Q(register_11_q), .clk(and_27_out), .cs(1'b0));  // open: clr, preset
  not not_5 (not_5_out, multiplexer_16_out_2[3]);
  Multiplexer #(.select(2), .width(4), .disabled("Z"), .enable("false")) multiplexer_14 (
    .in0(4'b0000), .in1(multiplexer_3_out[3:0]), .in2(multiplexer_3_out[3:0]), .in3(multiplexer_3_out[11:8]),
    .out(multiplexer_14_out), .sel(multiplexer_3_out[29:28]));
  ROM #(.addrWidth(8), .dataWidth(32), .Select("low")) rom_12 (.addr(counter_2_q), .data(rom_12_data));
  Slider #(.width(8), .Direction("left_to_right"), .value('h0)) slider_1 (.out(slider_1_out));
  Slider #(.width(8), .Direction("left_to_right"), .value('h40)) slider_2 (.out(slider_2_out));
  Slider #(.width(8), .Direction("left_to_right"), .value('h7a)) slider_3 (.out(slider_3_out));
  Slider #(.width(8), .Direction("left_to_right"), .value('ha1)) slider_4 (.out(slider_4_out));
  Slider #(.width(8), .Direction("left_to_right"), .value('hc9)) slider_5 (.out(slider_5_out));
  Slider #(.width(8), .Direction("left_to_right"), .value('h40)) slider_6 (.out(slider_6_out));
  Multiplexer #(.select(1), .width(3), .disabled("Z"), .enable("false")) multiplexer_15 (
    .in0(3'b000), .in1(register_3_q), .out(multiplexer_15_out), .sel(register_4_q));
  or or_2 (or_2_out, or_3_out, not_7_out);
  Register #(.width(8), .trigger("rising"), .Select("low")) register_12 (
    .D(multiplexer_4_out), .en(demultiplexer_2_out0), .Q(register_12_q), .clk(and_27_out));  // open: clr
  Register #(.width(8), .trigger("rising"), .Select("low")) register_13 (
    .D(multiplexer_5_out), .en(demultiplexer_3_out0), .Q(register_13_q), .clk(and_27_out));  // open: clr
  Register #(.width(8), .trigger("rising"), .Select("low")) register_14 (
    .D(multiplexer_6_out), .en(demultiplexer_4_out0), .Q(register_14_q), .clk(and_27_out));  // open: clr
  Register #(.width(8), .trigger("rising"), .Select("low")) register_15 (
    .D(multiplexer_7_out), .en(demultiplexer_5_out0), .Q(register_15_q), .clk(and_27_out));  // open: clr
  Register #(.width(8), .trigger("rising"), .Select("low")) register_16 (
    .D(multiplexer_8_out), .en(demultiplexer_6_out0), .Q(register_16_q), .clk(and_27_out));  // open: clr
  Register #(.width(8), .trigger("rising"), .Select("low")) register_17 (
    .D(multiplexer_9_out), .en(demultiplexer_7_out0), .Q(register_17_q), .clk(and_27_out));  // open: clr
  Register #(.width(8), .trigger("rising"), .Select("low")) register_18 (
    .D(multiplexer_10_out), .en(demultiplexer_8_out0), .Q(register_18_q), .clk(and_27_out));  // open: clr
  Multiplexer #(.select(1), .width(4), .disabled("Z"), .enable("false")) multiplexer_16 (
    .in0(multiplexer_14_out), .in1(4'b0000), .out({multiplexer_16_out_2[3], multiplexer_16_out}), .sel(in_18));
  Slider #(.width(8), .Direction("left_to_right"), .value('hff)) slider_7 (.out(slider_7_out));
  Register #(.width(32), .trigger("rising"), .Select("low")) register_19 (
    .D(rom_12_data), .Q(register_19_q), .clk(not_6_out));  // open: en, clr
  not not_6 (not_6_out, and_27_out);
  Multiplexer #(.select(3), .width(8), .disabled("Z"), .enable("false")) multiplexer_17 (
    .in0(slider_1_out), .in1(slider_2_out), .in2(slider_3_out), .in3(slider_4_out), .in4(slider_5_out),
    .in5(slider_6_out), .in6(register_1_q), .in7(register_2_q), .out(multiplexer_17_out),
    .sel(multiplexer_15_out));
  not not_7 (not_7_out, register_4_q);
  Multiplexer #(.select(1), .width(8), .disabled("Z"), .enable("false")) multiplexer_18 (
    .in0(register_12_q), .in1(register_5_q), .out(multiplexer_18_out), .sel(not_8_out));
  Multiplexer #(.select(1), .width(8), .disabled("Z"), .enable("false")) multiplexer_19 (
    .in0(register_12_q), .in1(register_5_q), .out(multiplexer_19_out), .sel(not_9_out));
  Multiplexer #(.select(1), .width(8), .disabled("Z"), .enable("false")) multiplexer_20 (
    .in0(register_13_q), .in1(register_6_q), .out(multiplexer_20_out), .sel(not_8_out));
  Multiplexer #(.select(1), .width(8), .disabled("Z"), .enable("false")) multiplexer_21 (
    .in0(register_13_q), .in1(register_6_q), .out(multiplexer_21_out), .sel(not_9_out));
  Multiplexer #(.select(1), .width(8), .disabled("Z"), .enable("false")) multiplexer_22 (
    .in0(register_14_q), .in1(register_7_q), .out(multiplexer_22_out), .sel(not_8_out));
  Multiplexer #(.select(1), .width(8), .disabled("Z"), .enable("false")) multiplexer_23 (
    .in0(register_14_q), .in1(register_7_q), .out(multiplexer_23_out), .sel(not_9_out));
  Multiplexer #(.select(1), .width(8), .disabled("Z"), .enable("false")) multiplexer_24 (
    .in0(register_15_q), .in1(register_8_q), .out(multiplexer_24_out), .sel(not_8_out));
  Multiplexer #(.select(1), .width(8), .disabled("Z"), .enable("false")) multiplexer_25 (
    .in0(register_15_q), .in1(register_8_q), .out(multiplexer_25_out), .sel(not_9_out));
  Multiplexer #(.select(1), .width(8), .disabled("Z"), .enable("false")) multiplexer_26 (
    .in0(register_16_q), .in1(register_9_q), .out(multiplexer_26_out), .sel(not_8_out));
  Multiplexer #(.select(1), .width(8), .disabled("Z"), .enable("false")) multiplexer_27 (
    .in0(register_16_q), .in1(register_9_q), .out(multiplexer_27_out), .sel(not_9_out));
  Multiplexer #(.select(1), .width(8), .disabled("Z"), .enable("false")) multiplexer_28 (
    .in0(register_17_q), .in1(register_10_q), .out(multiplexer_28_out), .sel(not_8_out));
  Multiplexer #(.select(1), .width(8), .disabled("Z"), .enable("false")) multiplexer_29 (
    .in0(register_17_q), .in1(register_10_q), .out(multiplexer_29_out), .sel(not_9_out));
  Multiplexer #(.select(1), .width(8), .disabled("Z"), .enable("false")) multiplexer_30 (
    .in0(register_18_q), .in1(register_11_q), .out(multiplexer_30_out), .sel(not_8_out));
  Multiplexer #(.select(1), .width(8), .disabled("Z"), .enable("false")) multiplexer_31 (
    .in0(register_18_q), .in1(register_11_q), .out(multiplexer_31_out), .sel(not_9_out));
  not not_8 (not_8_out, multiplexer_32_out[3]);
  not not_9 (not_9_out, multiplexer_33_out[3]);
  Multiplexer #(.select(2), .width(4), .disabled("Z"), .enable("false")) multiplexer_32 (
    .in0(4'b0000), .in1(4'b0000), .in2(multiplexer_3_out[7:4]), .in3(multiplexer_3_out[7:4]),
    .out(multiplexer_32_out), .sel(multiplexer_3_out[29:28]));
  not not_10 (not_10_out, in_71);
  Register #(.width(1), .trigger("rising"), .Select("low")) register_20 (
    .D(undriven_4), .en(not_12_out), .Q(register_20_q), .clk(and_27_out));  // open: clr
  not not_11 (not_11_out, or_3_out);
  or or_3 (or_3_out, in_75, multiplexer_61_out[6]);
  Multiplexer #(.select(2), .width(4), .disabled("Z"), .enable("false")) multiplexer_33 (
    .in0(4'b0000), .in1(multiplexer_3_out[3:0]), .in2(multiplexer_3_out[3:0]), .in3(multiplexer_3_out[3:0]),
    .out(multiplexer_33_out), .sel(multiplexer_3_out[29:28]));
  Multiplexer #(.select(1), .width(8), .disabled("Z"), .enable("false")) multiplexer_34 (
    .in0(multiplexer_78_out), .in1(multiplexer_3_out[11:4]), .out(multiplexer_34_out),
    .sel(multiplexer_57_out[0]));
  Comparator #(.width(8), .mode("unsigned")) comparator_1 (
    .a(slider_7_out), .b(rom_15_data), .eq(comparator_1_eq));  // open: gt, lt
  Register #(.width(1), .trigger("rising"), .Select("low")) register_21 (
    .D(and_2_out), .en(register_20_q), .Q(register_21_q), .clk(and_27_out));  // open: clr
  and and_2 (and_2_out, not_12_out, register_20_q);
  or or_4 (or_4_out, or_3_out, register_4_q);
  or or_5 (or_5_out, or_3_out, not_15_out);
  Multiplexer #(.select(1), .width(8), .disabled("Z"), .enable("false")) multiplexer_35 (
    .in0(multiplexer_34_out), .in1(counter_2_q), .out(multiplexer_35_out), .sel(multiplexer_57_out[6]));
  or or_6 (or_6_out, multiplexer_57_out[0], multiplexer_57_out[6], priority_encoder_2_gs, multiplexer_57_out[5]);
  Multiplexer #(.select(1), .width(8), .disabled("Z"), .enable("false")) multiplexer_36 (
    .in0(multiplexer_69_out), .in1(multiplexer_17_out), .out(multiplexer_36_out), .sel(or_8_out));
  not not_12 (not_12_out, register_22_q);
  Register #(.width(1), .trigger("rising"), .Select("low")) register_22 (
    .D(register_21_q), .en(register_20_q), .Q(register_22_q), .clk(and_27_out));  // open: clr
  Register #(.width(1), .trigger("rising"), .Select("low")) register_23 (
    .D(not_7_out), .en(or_5_out), .Q(register_23_q), .clk(and_27_out));  // open: clr
  Multiplexer #(.select(3), .width(8), .disabled("Z"), .enable("false")) multiplexer_37 (
    .in0({8{1'b0}}), .in1(multiplexer_18_out), .in2(multiplexer_20_out), .in3(multiplexer_22_out),
    .in4(multiplexer_24_out), .in5(multiplexer_26_out), .in6(multiplexer_28_out), .in7(multiplexer_30_out),
    .out(multiplexer_37_out), .sel(multiplexer_32_out[2:0]));
  Multiplexer #(.select(3), .width(8), .disabled("Z"), .enable("false")) multiplexer_38 (
    .in0({8{1'b0}}), .in1(multiplexer_19_out), .in2(multiplexer_21_out), .in3(multiplexer_23_out),
    .in4(multiplexer_25_out), .in5(multiplexer_27_out), .in6(multiplexer_29_out), .in7(multiplexer_31_out),
    .out(multiplexer_38_out), .sel(multiplexer_33_out[2:0]));
  Adder #(.width(8)) adder_1 (.a(register_17_q), .b(register_18_q), .out(adder_1_out));  // open: cin, cout
  Multiplexer #(.select(1), .width(8), .disabled("Z"), .enable("false")) multiplexer_39 (
    .in0({8{1'b0}}), .in1(multiplexer_35_out), .out(multiplexer_39_out), .sel(or_6_out));
  or or_7 (or_7_out, multiplexer_54_out, or_8_out);
  Counter #(.width(8), .max('hff), .ongoal("wrap"), .trigger("rising"), .behavior("new")) counter_3 (
    .load(or_7_out), .D(multiplexer_36_out), .count(not_4_out), .Q(counter_3_q), .clk(and_27_out));  // open: carry, clr, preset, down
  not not_13 (not_13_out, register_23_q);
  Multiplexer #(.select(2), .width(8), .disabled("Z"), .enable("false")) multiplexer_40 (
    .in0({8{1'b0}}), .in1(multiplexer_39_out), .in2({8{1'b0}}), .in3({8{1'b0}}), .out(multiplexer_40_out),
    .sel(multiplexer_3_out[29:28]));
  // NOT_Gate not_14 has open pins: in=or_8_out, out=open
  not not_15 (not_15_out, register_24_q);
  Register #(.width(1), .trigger("rising"), .Select("low")) register_24 (
    .D(not_13_out), .Q(register_24_q), .clk(and_27_out));  // open: en, clr
  Adder #(.width(8)) adder_2 (
    .a(multiplexer_37_out), .b(multiplexer_38_out), .out(adder_2_out), .cin(in_5));  // open: cout
  Subtractor #(.width(8)) subtractor_1 (
    .a(multiplexer_37_out), .b(multiplexer_38_out), .out(subtractor_1_out), .bin(in_6));  // open: bout
  Shifter #(.width(8), .shift("ll")) shifter_1 (
    .in(multiplexer_37_out), .\dist (multiplexer_38_out[2:0]), .out(shifter_1_out));
  and and_3 (and_3_out[0], multiplexer_37_out[0], multiplexer_38_out[0]);
  and and_4 (and_3_out[1], multiplexer_37_out[1], multiplexer_38_out[1]);
  and and_5 (and_3_out[2], multiplexer_37_out[2], multiplexer_38_out[2]);
  and and_6 (and_3_out[3], multiplexer_37_out[3], multiplexer_38_out[3]);
  and and_7 (and_3_out[4], multiplexer_37_out[4], multiplexer_38_out[4]);
  and and_8 (and_3_out[5], multiplexer_37_out[5], multiplexer_38_out[5]);
  and and_9 (and_3_out[6], multiplexer_37_out[6], multiplexer_38_out[6]);
  and and_10 (and_3_out[7], multiplexer_37_out[7], multiplexer_38_out[7]);
  Multiplexer #(.select(2), .width(4), .disabled("Z"), .enable("false")) multiplexer_41 (
    .in0(4'b0000), .in1(4'b0000), .in2(multiplexer_3_out[11:8]), .in3(4'b0000), .out(multiplexer_41_out),
    .sel(multiplexer_3_out[29:28]));
  Register #(.width(8), .trigger("rising"), .Select("low")) register_25 (
    .D(counter_3_q), .en(not_7_out), .clk(and_27_out));  // open: Q, clr
  or or_8 (or_8_out, register_26_q, and_11_out);
  and and_11 (and_11_out, register_4_q, register_23_q);
  Comparator #(.width(8), .mode("twosComplement")) comparator_2 (
    .a(register_5_q), .b(slider_8_out), .eq(comparator_2_eq[0]));  // open: gt, lt
  Slider #(.width(8), .Direction("left_to_right"), .value('hff)) slider_8 (.out(slider_8_out));
  Comparator #(.width(8), .mode("unsigned")) comparator_3 (
    .a(multiplexer_37_out), .b(multiplexer_38_out), .gt(comparator_3_gt[7]));  // open: eq, lt
  Comparator #(.width(8), .mode("unsigned")) comparator_4 (
    .a(multiplexer_37_out), .b(multiplexer_38_out), .eq(comparator_4_eq[7]));  // open: gt, lt
  Comparator #(.width(8), .mode("unsigned")) comparator_5 (
    .a(multiplexer_37_out), .b(multiplexer_38_out), .lt(comparator_5_lt[7]));  // open: gt, eq
  BitAdder #(.width(8)) bitadder_1 (.in0(multiplexer_38_out), .out(bitadder_1_out));
  Comparator #(.width(8), .mode("unsigned")) comparator_6 (
    .a(multiplexer_37_out), .b(multiplexer_38_out), .gt(comparator_6_gt), .eq(comparator_6_eq));  // open: lt
  Comparator #(.width(8), .mode("unsigned")) comparator_7 (
    .a(multiplexer_37_out), .b(multiplexer_38_out), .gt(comparator_7_gt), .lt(comparator_7_lt));  // open: eq
  or or_9 (or_9_out[7], comparator_7_gt, comparator_7_lt);
  Comparator #(.width(8), .mode("unsigned")) comparator_8 (
    .a(multiplexer_37_out), .b(multiplexer_38_out), .eq(comparator_8_eq), .lt(comparator_8_lt));  // open: gt
  Comparator #(.width(8), .mode("unsigned")) comparator_9 (
    .a(counter_2_q), .b(adder_1_out), .lt(comparator_9_lt));  // open: gt, eq
  Comparator #(.width(8), .mode("unsigned")) comparator_10 (
    .a(register_17_q), .b(counter_2_q), .lt(comparator_10_lt));  // open: gt, eq
  Slider #(.width(2), .Direction("left_to_right"), .value('h0)) slider_9 (.out(slider_9_out));
  Register #(.width(1), .trigger("rising"), .Select("low")) register_26 (
    .D(and_11_out), .Q(register_26_q), .clk(and_27_out));  // open: en, clr
  LED #(.active("true")) led_1 (.in(and_27_out));
  // NOT_Gate not_16 has open pins: in=comparator_2_eq[0], out=open
  Multiplexer #(.select(1), .width(8), .disabled("Z"), .enable("false")) multiplexer_42 (
    .in0(multiplexer_37_out), .in1(multiplexer_38_out));  // open: out, sel
  or or_10 (or_10_out[7], comparator_6_gt, comparator_6_eq);
  or or_11 (or_11_out[7], comparator_8_eq, comparator_8_lt);
  Comparator #(.width(2), .mode("unsigned")) comparator_11 (
    .a(slider_9_out), .b(multiplexer_3_out[29:28]));  // open: gt, eq, lt
  ROM #(.addrWidth(8), .dataWidth(32), .Select("low")) rom_13 (.addr(counter_3_q), .data(rom_13_data));
  // Digital_Oscilloscope #(.nState(35), .frontlines("rising"), .showclock("true")) digital_oscilloscope_1: pin names not known; wires that end beside it: multiplexer_37_out[0], multiplexer_37_out[1], multiplexer_37_out[2], multiplexer_37_out[3], multiplexer_37_out[4], multiplexer_37_out[5], multiplexer_37_out[6], multiplexer_37_out[7], multiplexer_38_out[0], multiplexer_38_out[1]
  Negator #(.width(8)) negator_1 (.in(multiplexer_38_out), .out(negator_1_out));
  or or_12 (or_12_out[0], multiplexer_37_out[0], multiplexer_38_out[0]);
  or or_13 (or_12_out[1], multiplexer_37_out[1], multiplexer_38_out[1]);
  or or_14 (or_12_out[2], multiplexer_37_out[2], multiplexer_38_out[2]);
  or or_15 (or_12_out[3], multiplexer_37_out[3], multiplexer_38_out[3]);
  or or_16 (or_12_out[4], multiplexer_37_out[4], multiplexer_38_out[4]);
  or or_17 (or_12_out[5], multiplexer_37_out[5], multiplexer_38_out[5]);
  or or_18 (or_12_out[6], multiplexer_37_out[6], multiplexer_38_out[6]);
  or or_19 (or_12_out[7], multiplexer_37_out[7], multiplexer_38_out[7]);
  Register #(.width(32), .trigger("rising"), .Select("low")) register_27 (
    .D(rom_13_data), .Q(register_27_q), .clk(and_27_out));  // open: en, clr
  not not_17 (not_17_out[0], multiplexer_38_out[0]);
  not not_18 (not_17_out[1], multiplexer_38_out[1]);
  not not_19 (not_17_out[2], multiplexer_38_out[2]);
  not not_20 (not_17_out[3], multiplexer_38_out[3]);
  not not_21 (not_17_out[4], multiplexer_38_out[4]);
  not not_22 (not_17_out[5], multiplexer_38_out[5]);
  not not_23 (not_17_out[6], multiplexer_38_out[6]);
  not not_24 (not_17_out[7], multiplexer_38_out[7]);
  not not_25 (not_25_out, and_12_out);
  and and_12 (and_12_out, comparator_9_lt, comparator_10_lt);
  Register #(.width(1), .trigger("rising"), .Select("low")) register_28 (
    .D(multiplexer_61_out[3]), .en(multiplexer_61_out[3]), .Q(register_28_q), .clk(and_27_out));  // open: clr
  Multiplexer #(.select(2), .width(4), .disabled("Z"), .enable("false")) multiplexer_43 (
    .in0(4'b0000), .in1(multiplexer_3_out[27:24]), .in2(multiplexer_3_out[27:24]), .in3(4'b0000),
    .out(multiplexer_43_out), .sel(multiplexer_3_out[29:28]));
  and and_13 (and_13_out, not_25_out, register_28_q);
  Comparator #(.width(4), .mode("unsigned")) comparator_12 (.b(undriven_5));  // open: a, gt, eq, lt
  Multiplexer #(.select(1), .width(8), .disabled("Z"), .enable("false")) multiplexer_44 (
    .in0(negator_1_out), .in1(multiplexer_38_out), .out(multiplexer_44_out), .sel(multiplexer_3_out[15]));
  Multiplexer #(.select(1), .width(8), .disabled("Z"), .enable("false")) multiplexer_45 (
    .in0(adder_2_out), .in1({8{comparator_3_gt[7]}}), .out(multiplexer_45_out), .sel(multiplexer_3_out[15]));
  Multiplexer #(.select(1), .width(8), .disabled("Z"), .enable("false")) multiplexer_46 (
    .in0(subtractor_1_out), .in1({8{comparator_4_eq[7]}}), .out(multiplexer_46_out),
    .sel(multiplexer_3_out[15]));
  Multiplexer #(.select(1), .width(8), .disabled("Z"), .enable("false")) multiplexer_47 (
    .in0(shifter_1_out), .in1({8{comparator_5_lt[7]}}), .out(multiplexer_47_out), .sel(multiplexer_3_out[15]));
  Multiplexer #(.select(1), .width(8), .disabled("Z"), .enable("false")) multiplexer_48 (
    .in0({8{1'b1}}), .in1({4'b0000, bitadder_1_out}), .out(multiplexer_48_out), .sel(multiplexer_3_out[15]));
  Multiplexer #(.select(1), .width(8), .disabled("Z"), .enable("false")) multiplexer_49 (
    .in0(and_3_out), .in1({8{or_10_out[7]}}), .out(multiplexer_49_out), .sel(multiplexer_3_out[15]));
  Multiplexer #(.select(1), .width(8), .disabled("Z"), .enable("false")) multiplexer_50 (
    .in0(or_12_out), .in1({8{or_9_out[7]}}), .out(multiplexer_50_out), .sel(multiplexer_3_out[15]));
  Multiplexer #(.select(1), .width(8), .disabled("Z"), .enable("false")) multiplexer_51 (
    .in0(not_17_out), .in1({8{or_11_out[7]}}), .out(multiplexer_51_out), .sel(multiplexer_3_out[15]));
  Decoder #(.select(2), .tristate("false"), .disabled("Z"), .enable("false")) decoder_3 (
    .out0(decoder_3_out0), .out1(decoder_3_out1), .out2(decoder_3_out2), .out3(decoder_3_out3),
    .sel(multiplexer_3_out[29:28]));
  Multiplexer #(.select(3), .width(8), .disabled("Z"), .enable("false")) multiplexer_52 (
    .in0(multiplexer_44_out), .in1(multiplexer_45_out), .in2(multiplexer_46_out), .in3(multiplexer_47_out),
    .in4(multiplexer_48_out), .in5(multiplexer_49_out), .in6(multiplexer_50_out), .in7(multiplexer_51_out));  // open: out, sel
  Multiplexer #(.select(3), .width(8), .disabled("Z"), .enable("false")) multiplexer_53 (
    .in0(multiplexer_44_out), .in1(multiplexer_45_out), .in2(multiplexer_46_out), .in3(multiplexer_47_out),
    .in4(multiplexer_48_out), .in5(multiplexer_49_out), .in6(multiplexer_50_out), .in7(multiplexer_51_out),
    .out(multiplexer_53_out), .sel(multiplexer_3_out[14:12]));
  not not_26 (not_26_out, decoder_3_out0);
  not not_27 (not_27_out, decoder_3_out1);
  not not_28 (not_28_out, decoder_3_out2);
  not not_29 (not_29_out, decoder_3_out3);
  Multiplexer #(.select(2), .width(1), .disabled("Z"), .enable("false")) multiplexer_54 (
    .in0(or_23_out), .in1(or_23_out), .in2(1'b0), .in3(or_23_out), .out(multiplexer_54_out),
    .sel(comparator_2_eq));
  Multiplexer #(.select(1), .width(1), .disabled("Z"), .enable("false")) multiplexer_55 (
    .in0(undriven_6), .in1(1'b0), .sel(and_14_out));  // open: out
  and and_14 (and_14_out, undriven_7, undriven_8);
  ROM #(.addrWidth(8), .dataWidth(8), .Select("low")) rom_14 (
    .addr(multiplexer_3_out[23:16]), .data(rom_14_data), .sel(not_26_out));
  not not_30 (not_30_out, not_26_out);
  ROM #(.addrWidth(8), .dataWidth(8), .Select("low")) rom_15 (
    .addr(multiplexer_3_out[23:16]), .data(rom_15_data), .sel(not_27_out));
  not not_31 (not_31_out, not_27_out);
  ROM #(.addrWidth(8), .dataWidth(8), .Select("low")) rom_16 (
    .addr(multiplexer_3_out[23:16]), .data(rom_16_data), .sel(not_28_out));
  not not_32 (not_32_out, not_28_out);
  ROM #(.addrWidth(8), .dataWidth(8), .Select("low")) rom_17 (
    .addr(multiplexer_3_out[23:16]), .data(rom_17_data), .sel(not_29_out));
  Demultiplexer #(.select(3), .width(8), .tristate("false"), .disabled("Z"), .enable("false")) demultiplexer_9 (
    .out0(demultiplexer_9_out0), .out1(demultiplexer_9_out1), .out2(demultiplexer_9_out2),
    .out4(demultiplexer_9_out4), .out5(demultiplexer_9_out5), .out6(demultiplexer_9_out6),
    .out7(demultiplexer_9_out7), .in(multiplexer_53_out), .sel(multiplexer_56_out));  // open: out3
  Multiplexer #(.select(2), .width(3), .disabled("Z"), .enable("false")) multiplexer_56 (
    .in0(multiplexer_43_out[2:0]), .in1(multiplexer_43_out[2:0]), .in2(3'b000),
    .in3(multiplexer_43_out[2:0]), .out(multiplexer_56_out), .sel(comparator_2_eq));
  // Probe on demultiplexer_9_out0
  Register #(.width(8), .trigger("rising"), .Select("low")) register_29 (
    .D(demultiplexer_9_out1), .en(1'b1), .Q(register_29_q), .clk(undriven_10));  // open: clr
  Slider #(.width(8), .Direction("left_to_right"), .value('h1)) slider_10 (.out(slider_10_out));
  Comparator #(.width(8), .mode("unsigned")) comparator_13 (
    .a(slider_10_out), .b(demultiplexer_9_out4), .eq(comparator_13_eq));  // open: gt, lt
  Register #(.width(8), .trigger("rising"), .Select("low")) register_30 (
    .D(register_29_q), .en(1'b1), .Q(register_30_q), .clk(undriven_10));  // open: clr
  Slider #(.width(8), .Direction("left_to_right"), .value('hff)) slider_11 (.out(slider_11_out));
  not not_33 (not_33_out[4], in_20);
  not not_34 (not_34_out[5], in_21);
  not not_35 (not_35_out[4], in_23);
  not not_36 (not_35_out[5], in_23);
  not not_37 (not_37_out[6], in_27);
  not not_38 (not_38_out[4], in_31);
  not not_39 (not_39_out[5], in_37);
  not not_40 (not_40_out[4], in_43);
  not not_41 (not_40_out[5], in_43);
  not not_42 (not_42_out[6], in_47);
  not not_43 (not_43_out[4], in_51);
  not not_44 (not_44_out[5], in_55);
  not not_45 (not_45_out[4], in_57);
  not not_46 (not_45_out[5], in_57);
  not not_47 (not_47_out[6], in_59);
  Counter #(.width(1), .max('h1), .ongoal("wrap"), .trigger("rising"), .behavior("new")) counter_4 (
    .Q(counter_4_q), .clk(undriven_11));  // open: load, D, count, carry, clr, preset, down
  Register #(.width(1), .trigger("rising"), .Select("low")) register_31 (
    .D(comparator_13_eq), .en(1'b1), .Q(register_31_q), .clk(undriven_10), .clr(register_33_q));
  Register #(.width(1), .trigger("rising"), .Select("low")) register_32 (
    .D(comparator_14_eq), .en(1'b1), .Q(register_32_q), .clk(undriven_10), .clr(register_34_q));
  Comparator #(.width(8), .mode("unsigned")) comparator_14 (
    .a(demultiplexer_9_out4), .b(slider_11_out), .eq(comparator_14_eq));  // open: gt, lt
  Comparator #(.width(8), .mode("unsigned")) comparator_15 (
    .a(multiplexer_3_out[23:16]), .b({{3{in_20}}, not_33_out[4], {4{in_20}}}), .gt(comparator_15_gt),
    .lt(comparator_15_lt));  // open: eq
  Comparator #(.width(8), .mode("unsigned")) comparator_16 (
    .a(multiplexer_3_out[23:16]), .b({{2{in_21}}, not_34_out[5], {5{in_21}}}), .gt(comparator_16_gt),
    .lt(comparator_16_lt));  // open: eq
  Comparator #(.width(8), .mode("unsigned")) comparator_17 (
    .a(multiplexer_3_out[23:16]), .b({{2{in_23}}, not_35_out, {4{in_23}}}), .gt(comparator_17_gt),
    .lt(comparator_17_lt));  // open: eq
  Comparator #(.width(8), .mode("unsigned")) comparator_18 (
    .a(multiplexer_3_out[23:16]), .b({in_27, not_37_out[6], {6{in_27}}}), .gt(comparator_18_gt),
    .lt(comparator_18_lt));  // open: eq
  Comparator #(.width(8), .mode("unsigned")) comparator_19 (
    .a(multiplexer_3_out[23:16]), .b({{3{in_31}}, not_38_out[4], {4{in_31}}}), .gt(comparator_19_gt),
    .lt(comparator_19_lt));  // open: eq
  Comparator #(.width(8), .mode("unsigned")) comparator_20 (
    .a(multiplexer_3_out[23:16]), .b({{2{in_37}}, not_39_out[5], {5{in_37}}}), .gt(comparator_20_gt),
    .lt(comparator_20_lt));  // open: eq
  Comparator #(.width(8), .mode("unsigned")) comparator_21 (
    .a(multiplexer_3_out[23:16]), .b({{2{in_43}}, not_40_out, {4{in_43}}}), .gt(comparator_21_gt),
    .lt(comparator_21_lt));  // open: eq
  Comparator #(.width(8), .mode("unsigned")) comparator_22 (
    .a(multiplexer_3_out[23:16]), .b({in_47, not_42_out[6], {6{in_47}}}), .gt(comparator_22_gt),
    .lt(comparator_22_lt));  // open: eq
  Comparator #(.width(8), .mode("unsigned")) comparator_23 (
    .a(multiplexer_3_out[23:16]), .b({{3{in_51}}, not_43_out[4], {4{in_51}}}), .gt(comparator_23_gt),
    .lt(comparator_23_lt));  // open: eq
  Comparator #(.width(8), .mode("unsigned")) comparator_24 (
    .a(multiplexer_3_out[23:16]), .b({{2{in_55}}, not_44_out[5], {5{in_55}}}), .gt(comparator_24_gt),
    .lt(comparator_24_lt));  // open: eq
  Comparator #(.width(8), .mode("unsigned")) comparator_25 (
    .a(multiplexer_3_out[23:16]), .b({{2{in_57}}, not_45_out, {4{in_57}}}), .gt(comparator_25_gt),
    .lt(comparator_25_lt));  // open: eq
  Comparator #(.width(8), .mode("unsigned")) comparator_26 (
    .a(multiplexer_3_out[23:16]), .b({in_59, not_47_out[6], {6{in_59}}}), .gt(comparator_26_gt),
    .lt(comparator_26_lt));  // open: eq
  Register #(.width(1), .trigger("rising"), .Select("low")) register_33 (
    .D(register_31_q), .en(1'b1), .Q(register_33_q), .clk(undriven_10));  // open: clr
  RAM #(.addrWidth(8), .dataWidth(8), .bus("separate"), .Select("low")) ram_1 (
    .addr(register_30_q), .din(demultiplexer_9_out2), .data(ram_1_data), .str(register_31_q),
    .clk(undriven_10), .ld(register_32_q));  // open: sel, clr
  Register #(.width(1), .trigger("rising"), .Select("low")) register_34 (
    .D(register_32_q), .en(1'b1), .Q(register_34_q), .clk(undriven_10));  // open: clr
  and and_15 (and_15_out, comparator_15_lt, not_31_out);
  and and_16 (and_16_out, comparator_15_gt, comparator_16_lt, not_31_out);
  and and_17 (and_17_out, comparator_16_gt, comparator_17_lt, not_31_out);
  and and_18 (and_18_out, comparator_17_gt, comparator_18_lt, not_31_out);
  and and_19 (and_19_out, comparator_19_lt, not_30_out);
  and and_20 (and_20_out, comparator_19_gt, comparator_20_lt, not_30_out);
  and and_21 (and_21_out, comparator_20_gt, comparator_21_lt, not_30_out);
  and and_22 (and_22_out, comparator_21_gt, comparator_22_lt, not_30_out);
  and and_23 (and_23_out, comparator_23_lt, not_32_out);
  and and_24 (and_24_out, comparator_23_gt, comparator_24_lt, not_32_out);
  and and_25 (and_25_out, comparator_24_gt, comparator_25_lt, not_32_out);
  and and_26 (and_26_out, comparator_25_gt, comparator_26_lt, not_32_out);
  Demultiplexer #(.select(1), .width(8), .tristate("false"), .disabled("Z"), .enable("false")) demultiplexer_10 (
    .out0(demultiplexer_10_out0), .out1(demultiplexer_10_out1));  // open: in, sel
  Multiplexer #(.select(1), .width(8), .disabled("Z"), .enable("false")) multiplexer_57 (
    .in0({8{1'b0}}), .in1(rom_15_data), .out(multiplexer_57_out), .sel(and_15_out));
  Multiplexer #(.select(1), .width(8), .disabled("Z"), .enable("false")) multiplexer_58 (
    .in0({8{1'b0}}), .in1(rom_15_data), .out(multiplexer_58_out), .sel(and_16_out));
  Multiplexer #(.select(1), .width(8), .disabled("Z"), .enable("false")) multiplexer_59 (
    .in0({8{1'b0}}), .in1(rom_15_data), .out(multiplexer_59_out), .sel(and_17_out));
  Multiplexer #(.select(1), .width(8), .disabled("Z"), .enable("false")) multiplexer_60 (
    .in0({8{1'b0}}), .in1(rom_15_data), .out(multiplexer_60_out), .sel(and_18_out));
  Multiplexer #(.select(1), .width(8), .disabled("Z"), .enable("false")) multiplexer_61 (
    .in0({8{1'b0}}), .in1(rom_14_data),
    .out({multiplexer_61_out[7:6], comparator_2_eq[1], multiplexer_61_out[4:0]}), .sel(and_19_out));
  Multiplexer #(.select(1), .width(8), .disabled("Z"), .enable("false")) multiplexer_62 (
    .in0({8{1'b0}}), .in1(rom_14_data), .out(multiplexer_62_out), .sel(and_20_out));
  Multiplexer #(.select(1), .width(8), .disabled("Z"), .enable("false")) multiplexer_63 (
    .in0({8{1'b0}}), .in1(rom_14_data), .out(multiplexer_63_out), .sel(and_21_out));
  Multiplexer #(.select(1), .width(8), .disabled("Z"), .enable("false")) multiplexer_64 (
    .in0({8{1'b0}}), .in1(rom_14_data), .out(multiplexer_64_out), .sel(and_22_out));
  Multiplexer #(.select(1), .width(8), .disabled("Z"), .enable("false")) multiplexer_65 (
    .in0({8{1'b0}}), .in1(rom_16_data), .out(multiplexer_65_out), .sel(and_23_out));
  Multiplexer #(.select(1), .width(8), .disabled("Z"), .enable("false")) multiplexer_66 (
    .in0({8{1'b0}}), .in1(rom_16_data), .out(multiplexer_66_out), .sel(and_24_out));
  Multiplexer #(.select(1), .width(8), .disabled("Z"), .enable("false")) multiplexer_67 (
    .in0({8{1'b0}}), .in1(rom_16_data), .out(multiplexer_67_out), .sel(and_25_out));
  Multiplexer #(.select(1), .width(8), .disabled("Z"), .enable("false")) multiplexer_68 (
    .in0({8{1'b0}}), .in1(rom_16_data), .out(multiplexer_68_out), .sel(and_26_out));
  // Probe on demultiplexer_10_out0
  // Probe on demultiplexer_10_out1
  not not_48 (not_48_out, in_3);
  Clock #(.highDuration(1), .lowDuration(1)) clock_1 (.out(clock_1_out));
  not not_49 (not_49_out, and_27_out);
  Priority_Encoder #(.select(2), .disabled("Z")) priority_encoder_2 (
    .in0(multiplexer_57_out[1]), .in1(multiplexer_57_out[2]), .in2(multiplexer_57_out[3]),
    .in3(multiplexer_57_out[4]), .out(priority_encoder_2_out), .gs(priority_encoder_2_gs));  // open: en_out, en_in
  or or_20 (or_20_out, multiplexer_61_out[0], multiplexer_61_out[1], multiplexer_61_out[2]);
  or or_21 (or_21_out, multiplexer_61_out[4], comparator_2_eq[1], or_20_out);
  or or_22 (or_22_out, multiplexer_61_out[6], multiplexer_61_out[6], or_21_out);
  Multiplexer #(.select(1), .width(8), .disabled("Z"), .enable("false")) multiplexer_69 (
    .in0(demultiplexer_9_out7), .in1(multiplexer_3_out[7:0]), .out(multiplexer_69_out), .sel(or_22_out));
  Slider #(.width(8), .Direction("left_to_right"), .value('h0)) slider_12 (.out(slider_12_out));
  and and_27 (and_27_out, not_48_out, clock_1_out);
  or or_23 (or_23_out, multiplexer_58_out[0], or_22_out);
  not not_50 (not_50_out, multiplexer_61_out[4]);
  Counter #(.width(8), .max('hff), .ongoal("wrap"), .trigger("rising"), .behavior("new")) counter_5 (
    .load(comparator_27_eq), .D(slider_12_out), .count(comparator_29_eq), .Q(counter_5_q), .clk(clock_2_out));  // open: carry, clr, preset, down
  Multiplexer #(.select(1), .width(1), .disabled("Z"), .enable("false")) multiplexer_70 (
    .in0(multiplexer_61_out[1]), .in1(not_50_out), .out(multiplexer_70_out), .sel(multiplexer_61_out[4]));
  Multiplexer #(.select(1), .width(8), .disabled("Z"), .enable("false")) multiplexer_71 (
    .in0(counter_5_q), .in1(register_8_q), .out(multiplexer_71_out), .sel(multiplexer_59_out[1]));
  or or_24 (or_24_out, multiplexer_61_out[4], multiplexer_61_out[1]);
  Comparator #(.width(8), .mode("unsigned")) comparator_27 (
    .a(counter_5_q), .b(8'h7), .eq(comparator_27_eq));  // open: gt, lt
  Register #(.width(1), .trigger("rising"), .Select("low")) register_35 (
    .D(multiplexer_70_out), .en(or_24_out), .Q(register_35_q), .clk(and_27_out));  // open: clr
  // Digital_Oscilloscope #(.nState(35), .frontlines("rising"), .showclock("true")) digital_oscilloscope_2: pin names not known; wires that end beside it: and_27_out, digital_oscilloscope_2_p2[0], digital_oscilloscope_2_p2[1], digital_oscilloscope_2_p2[2], digital_oscilloscope_2_p2[3], digital_oscilloscope_2_p2[4], digital_oscilloscope_2_p2[5], digital_oscilloscope_2_p2[6], digital_oscilloscope_2_p2[7], comparator_14_eq, register_32_q
  // Digital_Oscilloscope #(.nState(35), .frontlines("rising"), .showclock("true")) digital_oscilloscope_3: pin names not known; wires that end beside it: digital_oscilloscope_2_p2, demultiplexer_9_out1[2], demultiplexer_9_out1[3], demultiplexer_9_out1[4], demultiplexer_9_out1[5], demultiplexer_9_out1[6], demultiplexer_9_out1[7], and_27_out, demultiplexer_9_out1[0], demultiplexer_9_out1[1], demultiplexer_9_out1[2], demultiplexer_9_out1[3], demultiplexer_9_out1[4], demultiplexer_9_out1[5], demultiplexer_9_out1[6], demultiplexer_9_out1[7], comparator_13_eq, register_31_q
  Comparator #(.width(3), .mode("unsigned")) comparator_28 (
    .a(undriven_9), .b(slider_13_out), .eq(comparator_28_eq));  // open: gt, lt
  Slider #(.width(3), .Direction("left_to_right"), .value('h2)) slider_13 (.out(slider_13_out));
  or or_25 (or_25_out, comparator_28_eq, in_9);
  // Digital_Oscilloscope #(.nState(35), .frontlines("rising"), .showclock("true")) digital_oscilloscope_4: pin names not known; wires that end beside it: comparator_14_eq, and_27_out, digital_oscilloscope_4_p3
  Multiplexer #(.select(1), .width(8), .disabled("Z"), .enable("false")) multiplexer_72 (
    .in0({8{1'b0}}), .in1(counter_2_q), .out(multiplexer_72_out), .sel(register_35_q));
  and and_28 (and_28_out, not_51_out, clock_2_out);
  not not_51 (not_51_out, multiplexer_59_out[1]);
  Decoder #(.select(3), .tristate("false"), .disabled("Z"), .enable("false")) decoder_4 (
    .out0(decoder_4_out0), .out1(decoder_4_out1), .out2(decoder_4_out2), .out3(decoder_4_out3),
    .sel(counter_6_q));  // open: out4, out5, out6, out7
  Counter #(.width(3), .max('h7), .ongoal("wrap"), .trigger("rising"), .behavior("new")) counter_6 (
    .count(or_25_out), .Q(counter_6_q), .clk(and_27_out), .clr(register_42_q));  // open: load, D, carry, preset, down
  RAM #(.addrWidth(8), .dataWidth(8), .bus("separate"), .Select("low")) ram_2 (
    .addr(multiplexer_71_out), .din(demultiplexer_9_out5), .data(ram_2_data), .str(multiplexer_59_out[1]),
    .clk(not_52_out), .ld(and_28_out));  // open: sel, clr
  not not_52 (not_52_out, clock_2_out);
  and and_29 (and_29_out, decoder_4_out3, digital_oscilloscope_4_p3);
  Multiplexer #(.select(1), .width(8), .disabled("Z"), .enable("false")) multiplexer_73 (
    .in0(demultiplexer_10_out0), .in1(counter_57_q), .out(multiplexer_73_out), .sel(or_97_out));
  Subtractor #(.width(8)) subtractor_2 (.a(ram_2_data), .b(undriven_13), .out(subtractor_2_out));  // open: bin, bout
  Register #(.width(8), .trigger("rising"), .Select("low")) register_36 (
    .D(demultiplexer_9_out2), .en(and_29_out), .Q(register_36_q), .clk(and_27_out), .clr(register_42_q));
  and and_30 (and_30_out, decoder_4_out2, digital_oscilloscope_4_p3);
  Slider #(.width(3), .Direction("left_to_right"), .value('h1)) slider_14 (.out(slider_14_out));
  Clock #(.highDuration(1), .lowDuration(1)) clock_2 (.out(clock_2_out));
  Register #(.width(8), .trigger("rising"), .Select("low")) register_37 (
    .D(demultiplexer_9_out2), .en(and_30_out), .Q(register_37_q), .clk(and_27_out), .clr(register_42_q));
  ROM #(.addrWidth(8), .dataWidth(8), .Select("low")) rom_18 (.addr(ram_2_data), .data(rom_18_data));
  Counter #(.width(8), .max('hff), .ongoal("wrap"), .trigger("rising"), .behavior("new")) counter_7 (
    .Q(counter_7_q), .clk(clock_2_out));  // open: load, D, count, carry, clr, preset, down
  Counter #(.width(3), .max('h7), .ongoal("wrap"), .trigger("rising"), .behavior("new")) counter_8 (
    .load(comparator_29_eq), .D(slider_14_out), .count(or_27_out), .Q(counter_8_q), .clk(clock_2_out));  // open: carry, clr, preset, down
  Register #(.width(8), .trigger("rising"), .Select("low")) register_38 (
    .D(demultiplexer_9_out2), .en(and_31_out), .Q(register_38_q), .clk(and_27_out), .clr(register_42_q));
  and and_31 (and_31_out, decoder_4_out1, digital_oscilloscope_4_p3);
  Register #(.width(8), .trigger("rising"), .Select("low")) register_39 (
    .D(demultiplexer_9_out2), .en(and_32_out), .Q(register_39_q), .clk(and_27_out), .clr(register_42_q));
  and and_32 (and_32_out, decoder_4_out0, digital_oscilloscope_4_p3);
  Slider #(.width(3), .Direction("left_to_right"), .value('h5)) slider_15 (.out(slider_15_out));
  and and_33 (and_33_out, digital_oscilloscope_4_p3, and_34_out);
  and and_34 (and_34_out, not_53_out, in_17);
  not not_53 (not_53_out, undriven_12);
  Adder #(.width(8)) adder_3 (.a(rom_18_data), .b(subtractor_3_out), .out(adder_3_out));  // open: cin, cout
  Subtractor #(.width(8)) subtractor_3 (
    .a({{5{1'b0}}, counter_8_q}), .b(8'h1), .out(subtractor_3_out));  // open: bin, bout
  Comparator #(.width(3), .mode("unsigned")) comparator_29 (
    .a(counter_8_q), .b(slider_15_out), .eq(comparator_29_eq), .lt(comparator_29_lt));  // open: gt
  Slider #(.width(3), .Direction("left_to_right"), .value('h1)) slider_16 (.out(slider_16_out));
  Register #(.width(8), .trigger("rising"), .Select("low")) register_40 (
    .D(demultiplexer_9_out1), .en(digital_oscilloscope_4_p3), .Q(register_40_q), .clk(and_27_out),
    .clr(or_26_out));
  or or_26 (or_26_out, register_43_q, register_42_q);
  not not_54 (not_54_out, in_17);
  Register #(.width(8), .trigger("rising"), .Select("low")) register_41 (.Q(register_41_q));  // open: D, en, clk, clr
  // NOT_Gate not_55 has open pins: in=in_17, out=open
  Demultiplexer #(.select(3), .width(3), .tristate("false"), .disabled("Z"), .enable("false")) demultiplexer_11 (
    .out0(demultiplexer_11_out0), .out1(demultiplexer_11_out1), .out2(demultiplexer_11_out2),
    .out3(demultiplexer_11_out3), .out4(demultiplexer_11_out4), .out5(demultiplexer_11_out5),
    .out6(demultiplexer_11_out6), .out7(demultiplexer_11_out7), .in(counter_8_q), .sel(counter_9_q));
  or or_27 (or_27_out, comparator_29_eq, comparator_29_lt);
  Counter #(.width(3), .max('h7), .ongoal("wrap"), .trigger("rising"), .behavior("new")) counter_9 (
    .count(comparator_29_eq), .Q(counter_9_q), .clk(clock_2_out));  // open: load, D, carry, clr, preset, down
  Slider #(.width(8), .Direction("left_to_right"), .value('h1)) slider_17 (.out(slider_17_out));
  Multiplexer #(.select(1), .width(8), .disabled("Z"), .enable("false")) multiplexer_74 (
    .in0(multiplexer_73_out), .in1(register_40_q), .out(multiplexer_74_out), .sel(or_28_out));
  or or_28 (or_28_out, comparator_30_eq, comparator_31_eq);
  Slider #(.width(8), .Direction("left_to_right"), .value('hff)) slider_18 (.out(slider_18_out));
  and and_35 (and_35_out, not_54_out, in_14);
  Counter #(.width(8), .max('hff), .ongoal("wrap"), .trigger("rising"), .behavior("new")) counter_10 (
    .load(in_16), .D(register_41_q), .count(in_14), .Q(counter_10_q), .clk(and_27_out), .down(not_56_out));  // open: carry, clr, preset
  not not_56 (not_56_out, in_17);
  Comparator #(.width(8), .mode("unsigned")) comparator_30 (
    .a(slider_17_out), .b(demultiplexer_9_out4), .eq(comparator_30_eq));  // open: gt, lt
  Multiplexer #(.select(1), .width(8), .disabled("Z"), .enable("false")) multiplexer_75 (
    .in0(multiplexer_74_out), .in1(counter_10_q), .out(multiplexer_75_out), .sel(in_14));
  or or_29 (or_29_out, comparator_30_eq, and_35_out);
  Comparator #(.width(8), .mode("unsigned")) comparator_31 (
    .a(demultiplexer_9_out4), .b(slider_18_out), .eq(comparator_31_eq));  // open: gt, lt
  Slider #(.width(8), .Direction("left_to_right"), .value('h1)) slider_19 (.out(slider_19_out));
  // DipSwitch #(.NSwitches(7)) dipswitch_1: pin names not known; wires that end beside it: dipswitch_1_p1[0], dipswitch_1_p1[1], dipswitch_1_p1[2], dipswitch_1_p1[3], dipswitch_1_p1[4], dipswitch_1_p1[5]
  DotMatrix #(.inputtype("column"), .matrixcols(5), .matrixrows(7), .persist(0), .dotshape("square")) dotmatrix_1 ();  // open: col0, col1, col2, col3, col4
  Register #(.width(1), .trigger("rising"), .Select("low")) register_42 (
    .D(comparator_30_eq), .en(digital_oscilloscope_4_p3), .Q(register_42_q), .clk(and_27_out),
    .clr(register_42_q));
  or or_30 (or_30_out, in_17, or_31_out);
  Comparator #(.width(8), .mode("unsigned")) comparator_32 (
    .a(slider_19_out), .b(undriven_14), .eq(comparator_32_eq));  // open: gt, lt
  // Probe on multiplexer_73_out
  ROM #(.addrWidth(8), .dataWidth(8), .Select("low")) rom_19 (.data(rom_19_data));  // open: addr
  // DipSwitch #(.NSwitches(7)) dipswitch_2: pin names not known; wires that end beside it: dipswitch_1_p1[6], dipswitch_2_p2[0], dipswitch_2_p2[1], dipswitch_2_p2[2], dipswitch_2_p2[3], dipswitch_2_p2[4], dipswitch_2_p2[5], dipswitch_2_p2[6]
  ROM #(.addrWidth(8), .dataWidth(8), .Select("low")) rom_20 (.addr(adder_3_out), .data(rom_20_data));
  RAM #(.addrWidth(8), .dataWidth(32), .bus("separate"), .Select("low")) ram_3 (
    .addr(multiplexer_75_out), .din({register_36_q, register_37_q, register_38_q, register_39_q}),
    .data(ram_3_data), .str(or_29_out), .clk(and_27_out), .ld(or_30_out));  // open: sel, clr
  or or_31 (or_31_out, and_33_out, comparator_31_eq);
  Register #(.width(1), .trigger("rising"), .Select("low")) register_43 (
    .D(comparator_31_eq), .en(digital_oscilloscope_4_p3), .Q(register_43_q), .clk(and_27_out),
    .clr(register_43_q));
  // DipSwitch #(.NSwitches(7)) dipswitch_3: pin names not known; wires that end beside it: dipswitch_3_p1[0], dipswitch_3_p1[1], dipswitch_3_p1[2], dipswitch_3_p1[3], dipswitch_3_p1[4], dipswitch_3_p1[5], dipswitch_3_p1[6]
  Register #(.width(32), .trigger("rising"), .Select("low")) register_44 (
    .D(ram_3_data), .en(and_33_out), .Q(register_44_q), .clk(and_27_out));  // open: clr
  Counter #(.width(8), .max('hff), .ongoal("wrap"), .trigger("rising"), .behavior("new")) counter_11 (
    .load(comparator_32_eq), .D(8'h8c), .clk(and_27_out), .clr(in_15));  // open: count, Q, carry, preset, down
  Register #(.width(8), .trigger("rising"), .Select("low")) register_45 (
    .D(rom_19_data), .Q(register_45_q));  // open: en, clk, clr
  LED #(.active("true")) led_2 ();  // open: in
  or or_32 (or_32_out, multiplexer_62_out[4], multiplexer_62_out[2]);
  DotMatrix #(.inputtype("column"), .matrixcols(5), .matrixrows(7), .persist(0), .dotshape("square")) dotmatrix_2 ();  // open: col0, col1, col2, col3, col4
  DotMatrix #(.inputtype("column"), .matrixcols(5), .matrixrows(7), .persist(0), .dotshape("square")) dotmatrix_3 (.col0(dipswitch_1_p1));  // open: col1, col2, col3, col4
  // DotMatrix #(.inputtype("select"), .matrixcols(7), .matrixrows(7), .persist(0), .dotshape("square")) dotmatrix_4: pin names not known; wires that end beside it: dipswitch_2_p2, dipswitch_3_p1
  Decoder #(.select(3), .tristate("false"), .disabled("Z"), .enable("false")) decoder_5 (
    .out1(decoder_5_out1), .out2(decoder_5_out2), .out3(decoder_5_out3), .out4(decoder_5_out4),
    .out5(decoder_5_out5), .sel(demultiplexer_11_out0));  // open: out0, out6, out7
  Decoder #(.select(3), .tristate("false"), .disabled("Z"), .enable("false")) decoder_6 (
    .out1(decoder_6_out1), .out2(decoder_6_out2), .out3(decoder_6_out3), .out4(decoder_6_out4),
    .out5(decoder_6_out5), .sel(demultiplexer_11_out1));  // open: out0, out6, out7
  Decoder #(.select(3), .tristate("false"), .disabled("Z"), .enable("false")) decoder_7 (
    .out1(decoder_7_out1), .out2(decoder_7_out2), .out3(decoder_7_out3), .out4(decoder_7_out4),
    .out5(decoder_7_out5), .sel(demultiplexer_11_out2));  // open: out0, out6, out7
  Decoder #(.select(3), .tristate("false"), .disabled("Z"), .enable("false")) decoder_8 (
    .out1(decoder_8_out1), .out2(decoder_8_out2), .out3(decoder_8_out3), .out4(decoder_8_out4),
    .out5(decoder_8_out5), .sel(demultiplexer_11_out3));  // open: out0, out6, out7
  Decoder #(.select(3), .tristate("false"), .disabled("Z"), .enable("false")) decoder_9 (
    .out1(decoder_9_out1), .out2(decoder_9_out2), .out3(decoder_9_out3), .out4(decoder_9_out4),
    .out5(decoder_9_out5), .sel(demultiplexer_11_out4));  // open: out0, out6, out7
  Decoder #(.select(3), .tristate("false"), .disabled("Z"), .enable("false")) decoder_10 (
    .out1(decoder_10_out1), .out2(decoder_10_out2), .out3(decoder_10_out3), .out4(decoder_10_out4),
    .out5(decoder_10_out5), .sel(demultiplexer_11_out5));  // open: out0, out6, out7
  Decoder #(.select(3), .tristate("false"), .disabled("Z"), .enable("false")) decoder_11 (
    .out1(decoder_11_out1), .out2(decoder_11_out2), .out3(decoder_11_out3), .out4(decoder_11_out4),
    .out5(decoder_11_out5), .sel(demultiplexer_11_out6));  // open: out0, out6, out7
  Decoder #(.select(3), .tristate("false"), .disabled("Z"), .enable("false")) decoder_12 (
    .out1(decoder_12_out1), .out2(decoder_12_out2), .out3(decoder_12_out3), .out4(decoder_12_out4),
    .out5(decoder_12_out5), .sel(demultiplexer_11_out7));  // open: out0, out6, out7
  Decoder #(.select(3), .tristate("false"), .disabled("Z"), .enable("false")) decoder_13 (
    .out0(decoder_13_out0), .out1(decoder_13_out1), .out2(decoder_13_out2), .out3(decoder_13_out3),
    .out4(decoder_13_out4));  // open: out5, out6, out7, sel
  Decoder #(.select(3), .tristate("false"), .disabled("Z"), .enable("false")) decoder_14 (
    .out0(decoder_14_out0), .out1(decoder_14_out1), .out2(decoder_14_out2), .out3(decoder_14_out3),
    .out4(decoder_14_out4));  // open: out5, out6, out7, sel
  Demultiplexer #(.select(1), .width(32), .tristate("false"), .disabled("Z"), .enable("false")) demultiplexer_12 ();  // open: out0, out1, in, sel
  not not_57 (not_57_out, in_24);
  Multiplexer #(.select(1), .width(8), .disabled("Z"), .enable("false")) multiplexer_76 (
    .in0({8{1'b0}}), .in1(demultiplexer_9_out2), .out(multiplexer_76_out), .sel(multiplexer_59_out[0]));
  or or_33 (or_33_out, multiplexer_59_out[0], in_22);
  Register #(.width(1), .trigger("rising"), .Select("low")) register_46 (
    .D(or_34_out), .en(not_57_out), .Q(register_46_q), .clk(and_27_out));  // open: clr
  // NOT_Gate not_58 has open pins: in=register_46_q, out=open
  or or_34 (or_34_out, multiplexer_62_out[0], or_32_out);
  or or_35 (or_35_out, multiplexer_62_out[0], multiplexer_62_out[1]);
  Adder #(.width(8)) adder_4 (.a(demultiplexer_9_out6), .b(8'h1), .out(adder_4_out));  // open: cin, cout
  // DipSwitch #(.NSwitches(7)) dipswitch_4: pin names not known; wires that end beside it: register_45_q, dipswitch_4_p8[6], dipswitch_4_p8[5], dipswitch_4_p8[4], dipswitch_4_p8[3], dipswitch_4_p8[2], dipswitch_4_p8[1], dipswitch_4_p8[0]
  Clock #(.highDuration(1), .lowDuration(1)) clock_3 (.out(clock_3_out));
  Register #(.width(7), .trigger("rising"), .Select("low")) register_47 (
    .D(rom_20_data[6:0]), .en(decoder_5_out1), .Q(register_47_q), .clk(clock_2_out));  // open: clr
  Register #(.width(7), .trigger("rising"), .Select("low")) register_48 (
    .D(rom_20_data[6:0]), .en(decoder_5_out2), .Q(register_48_q), .clk(clock_2_out));  // open: clr
  Register #(.width(7), .trigger("rising"), .Select("low")) register_49 (
    .D(rom_20_data[6:0]), .en(decoder_5_out3), .Q(register_49_q), .clk(clock_2_out));  // open: clr
  Register #(.width(7), .trigger("rising"), .Select("low")) register_50 (
    .D(rom_20_data[6:0]), .en(decoder_5_out4), .Q(register_50_q), .clk(clock_2_out));  // open: clr
  Register #(.width(7), .trigger("rising"), .Select("low")) register_51 (
    .D(rom_20_data[6:0]), .en(decoder_5_out5), .Q(register_51_q), .clk(clock_2_out));  // open: clr
  Register #(.width(7), .trigger("rising"), .Select("low")) register_52 (
    .D(rom_20_data[6:0]), .en(decoder_6_out1), .Q(register_52_q), .clk(clock_2_out));  // open: clr
  Register #(.width(7), .trigger("rising"), .Select("low")) register_53 (
    .D(rom_20_data[6:0]), .en(decoder_6_out2), .Q(register_53_q), .clk(clock_2_out));  // open: clr
  Register #(.width(7), .trigger("rising"), .Select("low")) register_54 (
    .D(rom_20_data[6:0]), .en(decoder_6_out3), .Q(register_54_q), .clk(clock_2_out));  // open: clr
  Register #(.width(7), .trigger("rising"), .Select("low")) register_55 (
    .D(rom_20_data[6:0]), .en(decoder_6_out4), .Q(register_55_q), .clk(clock_2_out));  // open: clr
  Register #(.width(7), .trigger("rising"), .Select("low")) register_56 (
    .D(rom_20_data[6:0]), .en(decoder_6_out5), .Q(register_56_q), .clk(clock_2_out));  // open: clr
  Register #(.width(7), .trigger("rising"), .Select("low")) register_57 (
    .D(rom_20_data[6:0]), .en(decoder_7_out1), .Q(register_57_q), .clk(clock_2_out));  // open: clr
  Register #(.width(7), .trigger("rising"), .Select("low")) register_58 (
    .D(rom_20_data[6:0]), .en(decoder_7_out2), .Q(register_58_q), .clk(clock_2_out));  // open: clr
  Register #(.width(7), .trigger("rising"), .Select("low")) register_59 (
    .D(rom_20_data[6:0]), .en(decoder_7_out3), .Q(register_59_q), .clk(clock_2_out));  // open: clr
  Register #(.width(7), .trigger("rising"), .Select("low")) register_60 (
    .D(rom_20_data[6:0]), .en(decoder_7_out4), .Q(register_60_q), .clk(clock_2_out));  // open: clr
  Register #(.width(7), .trigger("rising"), .Select("low")) register_61 (
    .D(rom_20_data[6:0]), .en(decoder_7_out5), .Q(register_61_q), .clk(clock_2_out));  // open: clr
  Register #(.width(7), .trigger("rising"), .Select("low")) register_62 (
    .D(rom_20_data[6:0]), .en(decoder_8_out1), .Q(register_62_q), .clk(clock_2_out));  // open: clr
  Register #(.width(7), .trigger("rising"), .Select("low")) register_63 (
    .D(rom_20_data[6:0]), .en(decoder_8_out2), .Q(register_63_q), .clk(clock_2_out));  // open: clr
  Register #(.width(7), .trigger("rising"), .Select("low")) register_64 (
    .D(rom_20_data[6:0]), .en(decoder_8_out3), .Q(register_64_q), .clk(clock_2_out));  // open: clr
  Register #(.width(7), .trigger("rising"), .Select("low")) register_65 (
    .D(rom_20_data[6:0]), .en(decoder_8_out4), .Q(register_65_q), .clk(clock_2_out));  // open: clr
  Register #(.width(7), .trigger("rising"), .Select("low")) register_66 (
    .D(rom_20_data[6:0]), .en(decoder_8_out5), .Q(register_66_q), .clk(clock_2_out));  // open: clr
  Register #(.width(7), .trigger("rising"), .Select("low")) register_67 (
    .D(rom_20_data[6:0]), .en(decoder_9_out1), .Q(register_67_q), .clk(clock_2_out));  // open: clr
  Register #(.width(7), .trigger("rising"), .Select("low")) register_68 (
    .D(rom_20_data[6:0]), .en(decoder_9_out2), .Q(register_68_q), .clk(clock_2_out));  // open: clr
  Register #(.width(7), .trigger("rising"), .Select("low")) register_69 (
    .D(rom_20_data[6:0]), .en(decoder_9_out3), .Q(register_69_q), .clk(clock_2_out));  // open: clr
  Register #(.width(7), .trigger("rising"), .Select("low")) register_70 (
    .D(rom_20_data[6:0]), .en(decoder_9_out4), .Q(register_70_q), .clk(clock_2_out));  // open: clr
  Register #(.width(7), .trigger("rising"), .Select("low")) register_71 (
    .D(rom_20_data[6:0]), .en(decoder_9_out5), .Q(register_71_q), .clk(clock_2_out));  // open: clr
  Register #(.width(7), .trigger("rising"), .Select("low")) register_72 (
    .D(rom_20_data[6:0]), .en(decoder_10_out1), .Q(register_72_q), .clk(clock_2_out));  // open: clr
  Register #(.width(7), .trigger("rising"), .Select("low")) register_73 (
    .D(rom_20_data[6:0]), .en(decoder_10_out2), .Q(register_73_q), .clk(clock_2_out));  // open: clr
  Register #(.width(7), .trigger("rising"), .Select("low")) register_74 (
    .D(rom_20_data[6:0]), .en(decoder_10_out3), .Q(register_74_q), .clk(clock_2_out));  // open: clr
  Register #(.width(7), .trigger("rising"), .Select("low")) register_75 (
    .D(rom_20_data[6:0]), .en(decoder_10_out4), .Q(register_75_q), .clk(clock_2_out));  // open: clr
  Register #(.width(7), .trigger("rising"), .Select("low")) register_76 (
    .D(rom_20_data[6:0]), .en(decoder_10_out5), .Q(register_76_q), .clk(clock_2_out));  // open: clr
  Register #(.width(7), .trigger("rising"), .Select("low")) register_77 (
    .D(rom_20_data[6:0]), .en(decoder_11_out1), .Q(register_77_q), .clk(clock_2_out));  // open: clr
  Register #(.width(7), .trigger("rising"), .Select("low")) register_78 (
    .D(rom_20_data[6:0]), .en(decoder_11_out2), .Q(register_78_q), .clk(clock_2_out));  // open: clr
  Register #(.width(7), .trigger("rising"), .Select("low")) register_79 (
    .D(rom_20_data[6:0]), .en(decoder_11_out3), .Q(register_79_q), .clk(clock_2_out));  // open: clr
  Register #(.width(7), .trigger("rising"), .Select("low")) register_80 (
    .D(rom_20_data[6:0]), .en(decoder_11_out4), .Q(register_80_q), .clk(clock_2_out));  // open: clr
  Register #(.width(7), .trigger("rising"), .Select("low")) register_81 (
    .D(rom_20_data[6:0]), .en(decoder_11_out5), .Q(register_81_q), .clk(clock_2_out));  // open: clr
  Register #(.width(7), .trigger("rising"), .Select("low")) register_82 (
    .D(rom_20_data[6:0]), .en(decoder_12_out1), .Q(register_82_q), .clk(clock_2_out));  // open: clr
  Register #(.width(7), .trigger("rising"), .Select("low")) register_83 (
    .D(rom_20_data[6:0]), .en(decoder_12_out2), .Q(register_83_q), .clk(clock_2_out));  // open: clr
  Register #(.width(7), .trigger("rising"), .Select("low")) register_84 (
    .D(rom_20_data[6:0]), .en(decoder_12_out3), .Q(register_84_q), .clk(clock_2_out));  // open: clr
  Register #(.width(7), .trigger("rising"), .Select("low")) register_85 (
    .D(rom_20_data[6:0]), .en(decoder_12_out4), .Q(register_85_q), .clk(clock_2_out));  // open: clr
  Register #(.width(7), .trigger("rising"), .Select("low")) register_86 (
    .D(rom_20_data[6:0]), .en(decoder_12_out5), .Q(register_86_q), .clk(clock_2_out));  // open: clr
  Register #(.width(7), .trigger("rising"), .Select("low")) register_87 (
    .D(undriven_15), .en(decoder_13_out0), .Q(register_87_q), .clk(clock_2_out));  // open: clr
  Register #(.width(7), .trigger("rising"), .Select("low")) register_88 (
    .D(undriven_15), .en(decoder_13_out1), .Q(register_88_q), .clk(clock_2_out));  // open: clr
  Register #(.width(7), .trigger("rising"), .Select("low")) register_89 (
    .D(undriven_15), .en(decoder_13_out2), .Q(register_89_q), .clk(clock_2_out));  // open: clr
  Register #(.width(7), .trigger("rising"), .Select("low")) register_90 (
    .D(undriven_15), .en(decoder_13_out3), .Q(register_90_q), .clk(clock_2_out));  // open: clr
  Register #(.width(7), .trigger("rising"), .Select("low")) register_91 (
    .D(undriven_15), .en(decoder_13_out4), .Q(register_91_q), .clk(clock_2_out));  // open: clr
  Register #(.width(7), .trigger("rising"), .Select("low")) register_92 (
    .D(undriven_15), .en(decoder_14_out0), .Q(register_92_q), .clk(clock_2_out));  // open: clr
  Register #(.width(7), .trigger("rising"), .Select("low")) register_93 (
    .D(undriven_15), .en(decoder_14_out1), .Q(register_93_q), .clk(clock_2_out));  // open: clr
  Register #(.width(7), .trigger("rising"), .Select("low")) register_94 (
    .D(undriven_15), .en(decoder_14_out2), .Q(register_94_q), .clk(clock_2_out));  // open: clr
  Register #(.width(7), .trigger("rising"), .Select("low")) register_95 (
    .D(undriven_15), .en(decoder_14_out3), .Q(register_95_q), .clk(clock_2_out));  // open: clr
  Register #(.width(7), .trigger("rising"), .Select("low")) register_96 (
    .D(undriven_15), .en(decoder_14_out4), .Q(register_96_q), .clk(clock_2_out));  // open: clr
  Demultiplexer #(.select(1), .width(1), .tristate("false"), .disabled("Z"), .enable("false")) demultiplexer_13 (
    .out0(demultiplexer_13_out0), .out1(demultiplexer_13_out1), .in(or_70_out), .sel(multiplexer_96_out[0]));
  Demultiplexer #(.select(1), .width(32), .tristate("false"), .disabled("Z"), .enable("false")) demultiplexer_14 (
    .out0(demultiplexer_14_out0), .out1(demultiplexer_14_out1), .in(ram_4_data), .sel(multiplexer_96_out[0]));
  Demultiplexer #(.select(1), .width(8), .tristate("false"), .disabled("Z"), .enable("false")) demultiplexer_15 (
    .out0(demultiplexer_15_out0), .out1(demultiplexer_15_out1), .in(multiplexer_96_out),
    .sel(multiplexer_96_out[0]));
  Demultiplexer #(.select(1), .width(1), .tristate("false"), .disabled("Z"), .enable("false")) demultiplexer_16 (
    .out0(demultiplexer_16_out0), .out1(demultiplexer_16_out1), .in(or_79_out), .sel(multiplexer_96_out[0]));
  Decoder #(.select(3), .tristate("false"), .disabled("Z"), .enable("false")) decoder_15 (
    .out0(decoder_15_out0), .out1(decoder_15_out1), .out2(decoder_15_out2), .out3(decoder_15_out3),
    .sel(counter_12_q));  // open: out4, out5, out6, out7
  or or_36 (or_36_out, or_33_out, or_34_out);
  Counter #(.width(3), .max('h7), .ongoal("wrap"), .trigger("rising"), .behavior("new")) counter_12 (
    .load(or_34_out), .D(3'b000), .count(or_36_out), .Q(counter_12_q), .clk(and_27_out));  // open: carry, clr, preset, down
  Counter #(.width(1), .max('h1), .ongoal("wrap"), .trigger("rising"), .behavior("new")) counter_13 (
    .Q(counter_13_q), .clk(and_27_out));  // open: load, D, count, carry, clr, preset, down
  Subtractor #(.width(8)) subtractor_4 ();  // open: a, b, out, bin, bout
  Keyboard #(.Char_bit_width(7), .buflen(32), .trigger("rising")) keyboard_1 (
    .clk(clock_3_out), .data(keyboard_1_data));  // open: re, clr, avail
  DotMatrix #(.inputtype("column"), .matrixcols(5), .matrixrows(7), .persist(0), .dotshape("square")) dotmatrix_5 ();  // open: col0, col1, col2, col3, col4
  and and_36 (and_36_out, decoder_15_out3, multiplexer_59_out[0]);
  or or_37 (or_37_out, and_36_out, or_34_out);
  and and_37 (and_37_out, or_37_out, not_59_out);
  not not_59 (not_59_out, counter_13_q);
  or or_38 (or_38_out, or_32_out, multiplexer_57_out[7], multiplexer_62_out[3]);
  Counter #(.width(8), .max('hff), .ongoal("wrap"), .trigger("rising"), .behavior("new")) counter_14 (
    .load(multiplexer_57_out[7]), .D(demultiplexer_9_out6), .count(or_38_out), .Q(counter_14_q),
    .clk(and_27_out), .down(not_60_out));  // open: carry, clr, preset
  not not_60 (not_60_out, multiplexer_62_out[3]);
  or or_39 (or_39_out, or_32_out, multiplexer_57_out[7], multiplexer_62_out[3]);
  Counter #(.width(8), .max('hff), .ongoal("wrap"), .trigger("rising"), .behavior("new")) counter_15 (
    .load(multiplexer_57_out[7]), .D(adder_4_out), .count(or_39_out), .Q(counter_15_q), .clk(and_27_out),
    .down(not_61_out));  // open: carry, clr, preset
  not not_61 (not_61_out, multiplexer_62_out[3]);
  Adder #(.width(8)) adder_5 ();  // open: a, b, out, cin, cout
  DotMatrix #(.inputtype("column"), .matrixcols(5), .matrixrows(7), .persist(0), .dotshape("square")) dotmatrix_6 (.col0(undriven_16));  // open: col1, col2, col3, col4
  DotMatrix #(.inputtype("column"), .matrixcols(5), .matrixrows(7), .persist(0), .dotshape("square")) dotmatrix_7 ();  // open: col0, col1, col2, col3, col4
  Slider #(.width(8), .Direction("left_to_right"), .value('h0)) slider_20 (.out(slider_20_out));
  and and_38 (and_38_out, demultiplexer_13_out0, decoder_16_out7);
  or or_40 (or_40_out, and_38_out, comparator_33_eq);
  and and_39 (and_39_out, demultiplexer_13_out0, decoder_16_out6);
  or or_41 (or_41_out, and_39_out, comparator_34_eq);
  and and_40 (and_40_out, demultiplexer_13_out0, decoder_16_out5);
  or or_42 (or_42_out, and_40_out, comparator_35_eq);
  and and_41 (and_41_out, demultiplexer_13_out0, decoder_16_out4);
  or or_43 (or_43_out, and_41_out, comparator_36_eq);
  Slider #(.width(8), .Direction("left_to_right"), .value('h0)) slider_21 (.out(slider_21_out));
  and and_42 (and_42_out, demultiplexer_13_out1, decoder_17_out7);
  or or_44 (or_44_out, and_42_out, comparator_37_eq);
  and and_43 (and_43_out, demultiplexer_13_out1, decoder_17_out6);
  or or_45 (or_45_out, and_43_out, comparator_38_eq);
  and and_44 (and_44_out, demultiplexer_13_out1, decoder_17_out5);
  or or_46 (or_46_out, and_44_out, comparator_39_eq);
  and and_45 (and_45_out, demultiplexer_13_out1, decoder_17_out4);
  or or_47 (or_47_out, and_45_out, comparator_40_eq);
  Register #(.width(8), .trigger("rising"), .Select("low")) register_97 (
    .D(multiplexer_76_out), .en(and_37_out), .Q(register_97_q), .clk(and_27_out));  // open: clr
  Bit_Extender #(.in_width(8), .out_width(32), .\type ("zero")) bit_extender_1 ();  // open: in, out
  Counter #(.width(1), .max('h1), .ongoal("wrap"), .trigger("rising"), .behavior("new")) counter_16 (
    .Q(counter_16_q), .clk(and_27_out));  // open: load, D, count, carry, clr, preset, down
  or or_48 (or_48_out, or_32_out, multiplexer_62_out[3]);
  LED #(.active("true")) led_3 (.in(or_48_out));
  LED #(.active("true")) led_4 (.in(or_48_out));
  Counter #(.width(1), .max('h1), .ongoal("wrap"), .trigger("rising"), .behavior("new")) counter_17 (
    .Q(counter_17_q), .clk(and_27_out));  // open: load, D, count, carry, clr, preset, down
  LED #(.active("true")) led_5 (.in(or_49_out));
  LED #(.active("true")) led_6 (.in(or_49_out));
  or or_49 (or_49_out, or_32_out, multiplexer_62_out[3]);
  TTY #(.Char_bit_width(7), .rows(8), .cols(32), .trigger("rising")) tty_1 (
    .data(keyboard_1_data), .clk(clock_3_out));  // open: we, clr
  DotMatrix #(.inputtype("column"), .matrixcols(5), .matrixrows(7), .persist(0), .dotshape("square")) dotmatrix_8 ();  // open: col0, col1, col2, col3, col4
  or or_50 (or_50_out, or_40_out, and_51_out);
  Counter #(.width(8), .max('hff), .ongoal("wrap"), .trigger("rising"), .behavior("new")) counter_18 (
    .load(or_50_out), .D(slider_20_out), .count(demultiplexer_13_out0), .Q(counter_18_q), .clk(and_27_out));  // open: carry, clr, preset, down
  or or_51 (or_51_out, and_51_out, and_38_out);
  or or_52 (or_52_out, or_41_out, and_52_out);
  Counter #(.width(8), .max('hff), .ongoal("wrap"), .trigger("rising"), .behavior("new")) counter_19 (
    .load(or_52_out), .D(slider_20_out), .count(demultiplexer_13_out0), .Q(counter_19_q), .clk(and_27_out));  // open: carry, clr, preset, down
  or or_53 (or_53_out, and_52_out, and_39_out);
  or or_54 (or_54_out, or_42_out, and_53_out);
  Counter #(.width(8), .max('hff), .ongoal("wrap"), .trigger("rising"), .behavior("new")) counter_20 (
    .load(or_54_out), .D(slider_20_out), .count(demultiplexer_13_out0), .Q(counter_20_q), .clk(and_27_out));  // open: carry, clr, preset, down
  or or_55 (or_55_out, and_53_out, and_40_out);
  or or_56 (or_56_out, or_43_out, and_54_out);
  Counter #(.width(8), .max('hff), .ongoal("wrap"), .trigger("rising"), .behavior("new")) counter_21 (
    .load(or_56_out), .D(slider_20_out), .count(demultiplexer_13_out0), .Q(counter_21_q), .clk(and_27_out));  // open: carry, clr, preset, down
  or or_57 (or_57_out, and_54_out, and_41_out);
  or or_58 (or_58_out, or_44_out, and_55_out);
  Counter #(.width(8), .max('hff), .ongoal("wrap"), .trigger("rising"), .behavior("new")) counter_22 (
    .load(or_58_out), .D(slider_21_out), .count(demultiplexer_13_out1), .Q(counter_22_q), .clk(and_27_out));  // open: carry, clr, preset, down
  or or_59 (or_59_out, and_55_out, and_42_out);
  or or_60 (or_60_out, or_45_out, and_56_out);
  Counter #(.width(8), .max('hff), .ongoal("wrap"), .trigger("rising"), .behavior("new")) counter_23 (
    .load(or_60_out), .D(slider_21_out), .count(demultiplexer_13_out1), .Q(counter_23_q), .clk(and_27_out));  // open: carry, clr, preset, down
  or or_61 (or_61_out, and_56_out, and_43_out);
  or or_62 (or_62_out, or_46_out, and_57_out);
  Counter #(.width(8), .max('hff), .ongoal("wrap"), .trigger("rising"), .behavior("new")) counter_24 (
    .load(or_62_out), .D(slider_21_out), .count(demultiplexer_13_out1), .Q(counter_24_q), .clk(and_27_out));  // open: carry, clr, preset, down
  or or_63 (or_63_out, and_57_out, and_44_out);
  or or_64 (or_64_out, or_47_out, and_58_out);
  Counter #(.width(8), .max('hff), .ongoal("wrap"), .trigger("rising"), .behavior("new")) counter_25 (
    .load(or_64_out), .D(slider_21_out), .count(demultiplexer_13_out1), .Q(counter_25_q), .clk(and_27_out));  // open: carry, clr, preset, down
  or or_65 (or_65_out, and_58_out, and_45_out);
  and and_46 (and_46_out, decoder_15_out2, multiplexer_59_out[0]);
  Register #(.width(8), .trigger("rising"), .Select("low")) register_98 (
    .D(multiplexer_76_out), .en(and_47_out), .Q(register_98_q), .clk(and_27_out));  // open: clr
  or or_66 (or_66_out, and_46_out, or_34_out);
  and and_47 (and_47_out, or_66_out, not_59_out);
  not not_62 (not_62_out, and_27_out);
  LED #(.active("true")) led_7 (.in(or_48_out));
  LED #(.active("true")) led_8 (.in(or_49_out));
  not not_63 (not_63_out, multiplexer_57_out[5]);
  LED #(.active("true")) led_9 (.in(dipswitch_4_p8[0]));
  LED #(.active("true")) led_10 (.in(dipswitch_4_p8[1]));
  LED #(.active("true")) led_11 (.in(dipswitch_4_p8[2]));
  LED #(.active("true")) led_12 (.in(dipswitch_4_p8[3]));
  LED #(.active("true")) led_13 (.in(dipswitch_4_p8[4]));
  LED #(.active("true")) led_14 (.in(dipswitch_4_p8[5]));
  DotMatrix #(.inputtype("column"), .matrixcols(5), .matrixrows(7), .persist(0), .dotshape("square")) dotmatrix_9 (.col0(dipswitch_4_p8));  // open: col1, col2, col3, col4
  LED #(.active("true")) led_15 (.in(dipswitch_4_p8[6]));
  DotMatrix #(.inputtype("column"), .matrixcols(5), .matrixrows(7), .persist(0), .dotshape("square")) dotmatrix_10 (.col0(undriven_17));  // open: col1, col2, col3, col4
  DotMatrix #(.inputtype("column"), .matrixcols(5), .matrixrows(7), .persist(0), .dotshape("square")) dotmatrix_11 ();  // open: col0, col1, col2, col3, col4
  Register #(.width(8), .trigger("rising"), .Select("low")) register_99 (
    .D(demultiplexer_15_out0), .en(or_51_out), .Q(register_99_q), .clk(and_27_out));  // open: clr
  Register #(.width(8), .trigger("rising"), .Select("low")) register_100 (
    .D(demultiplexer_15_out0), .en(or_53_out), .Q(register_100_q), .clk(and_27_out));  // open: clr
  Register #(.width(8), .trigger("rising"), .Select("low")) register_101 (
    .D(demultiplexer_15_out0), .en(or_55_out), .Q(register_101_q), .clk(and_27_out));  // open: clr
  Register #(.width(8), .trigger("rising"), .Select("low")) register_102 (
    .D(demultiplexer_15_out0), .en(or_57_out), .Q(register_102_q), .clk(and_27_out));  // open: clr
  Register #(.width(8), .trigger("rising"), .Select("low")) register_103 (
    .D(demultiplexer_15_out1), .en(or_59_out), .Q(register_103_q), .clk(and_27_out));  // open: clr
  Register #(.width(8), .trigger("rising"), .Select("low")) register_104 (
    .D(demultiplexer_15_out1), .en(or_61_out), .Q(register_104_q), .clk(and_27_out));  // open: clr
  Register #(.width(8), .trigger("rising"), .Select("low")) register_105 (
    .D(demultiplexer_15_out1), .en(or_63_out), .Q(register_105_q), .clk(and_27_out));  // open: clr
  Register #(.width(8), .trigger("rising"), .Select("low")) register_106 (
    .D(demultiplexer_15_out1), .en(or_65_out), .Q(register_106_q), .clk(and_27_out));  // open: clr
  and and_48 (and_48_out, decoder_15_out1, multiplexer_59_out[0]);
  or or_67 (or_67_out, and_48_out, or_34_out);
  and and_49 (and_49_out, or_67_out, not_59_out);
  Counter #(.width(8), .max('hff), .ongoal("wrap"), .trigger("rising"), .behavior("new")) counter_26 ();  // open: load, D, count, Q, carry, clk, clr, preset, down
  and and_50 (and_50_out, or_35_out, not_62_out);
  Multiplexer #(.select(1), .width(8), .disabled("Z"), .enable("false")) multiplexer_77 (
    .in0(counter_14_q), .in1(counter_15_q), .out(multiplexer_77_out), .sel(multiplexer_62_out[3]));
  Multiplexer #(.select(1), .width(8), .disabled("Z"), .enable("false")) multiplexer_78 (
    .in0(counter_14_q), .in1(multiplexer_106_out), .out(multiplexer_78_out), .sel(not_63_out));
  DotMatrix #(.inputtype("column"), .matrixcols(5), .matrixrows(7), .persist(0), .dotshape("circle")) dotmatrix_12 (.col0(dipswitch_4_p8));  // open: col1, col2, col3, col4
  DotMatrix #(.inputtype("column"), .matrixcols(5), .matrixrows(7), .persist(0), .dotshape("square")) dotmatrix_13 ();  // open: col0, col1, col2, col3, col4
  DotMatrix #(.inputtype("column"), .matrixcols(5), .matrixrows(7), .persist(0), .dotshape("square")) dotmatrix_14 (.col0(undriven_18));  // open: col1, col2, col3, col4
  Slider #(.width(32), .Direction("left_to_right"), .value('h0)) slider_22 (.out(slider_22_out));
  Comparator #(.width(8), .mode("unsigned")) comparator_33 (
    .a(demultiplexer_15_out0), .b(register_99_q), .eq(comparator_33_eq));  // open: gt, lt
  Register #(.width(32), .trigger("rising"), .Select("low")) register_107 (
    .D(demultiplexer_14_out0), .en(or_51_out), .Q(register_107_q), .clk(and_27_out));  // open: clr
  not not_64 (not_64_out, register_117_q);
  and and_51 (and_51_out, not_64_out, demultiplexer_13_out0, comparator_33_eq);
  Comparator #(.width(8), .mode("unsigned")) comparator_34 (
    .a(demultiplexer_15_out0), .b(register_100_q), .eq(comparator_34_eq));  // open: gt, lt
  Register #(.width(32), .trigger("rising"), .Select("low")) register_108 (
    .D(demultiplexer_14_out0), .en(or_53_out), .Q(register_108_q), .clk(and_27_out));  // open: clr
  and and_52 (and_52_out, demultiplexer_13_out0, not_65_out, comparator_34_eq);
  not not_65 (not_65_out, register_118_q);
  Comparator #(.width(8), .mode("unsigned")) comparator_35 (
    .a(demultiplexer_15_out0), .b(register_101_q), .eq(comparator_35_eq));  // open: gt, lt
  Register #(.width(32), .trigger("rising"), .Select("low")) register_109 (
    .D(demultiplexer_14_out0), .en(or_55_out), .Q(register_109_q), .clk(and_27_out));  // open: clr
  and and_53 (and_53_out, demultiplexer_13_out0, comparator_35_eq, not_66_out);
  not not_66 (not_66_out, register_119_q);
  Comparator #(.width(8), .mode("unsigned")) comparator_36 (
    .a(demultiplexer_15_out0), .b(register_102_q), .eq(comparator_36_eq));  // open: gt, lt
  Register #(.width(32), .trigger("rising"), .Select("low")) register_110 (
    .D(demultiplexer_14_out0), .en(or_57_out), .Q(register_110_q), .clk(and_27_out));  // open: clr
  and and_54 (and_54_out, demultiplexer_13_out0, comparator_36_eq, not_67_out);
  not not_67 (not_67_out, register_120_q);
  Slider #(.width(32), .Direction("left_to_right"), .value('h0)) slider_23 (.out(slider_23_out));
  Comparator #(.width(8), .mode("unsigned")) comparator_37 (
    .a(demultiplexer_15_out1), .b(register_103_q), .eq(comparator_37_eq));  // open: gt, lt
  Register #(.width(32), .trigger("rising"), .Select("low")) register_111 (
    .D(demultiplexer_14_out1), .en(or_59_out), .Q(register_111_q), .clk(and_27_out));  // open: clr
  not not_68 (not_68_out, register_121_q);
  and and_55 (and_55_out, not_68_out, demultiplexer_13_out1, comparator_37_eq);
  Comparator #(.width(8), .mode("unsigned")) comparator_38 (
    .a(demultiplexer_15_out1), .b(register_104_q), .eq(comparator_38_eq));  // open: gt, lt
  Register #(.width(32), .trigger("rising"), .Select("low")) register_112 (
    .D(demultiplexer_14_out1), .en(or_61_out), .Q(register_112_q), .clk(and_27_out));  // open: clr
  not not_69 (not_69_out, register_122_q);
  and and_56 (and_56_out, demultiplexer_13_out1, not_69_out, comparator_38_eq);
  Comparator #(.width(8), .mode("unsigned")) comparator_39 (
    .a(demultiplexer_15_out1), .b(register_105_q), .eq(comparator_39_eq));  // open: gt, lt
  Register #(.width(32), .trigger("rising"), .Select("low")) register_113 (
    .D(demultiplexer_14_out1), .en(or_63_out), .Q(register_113_q), .clk(and_27_out));  // open: clr
  and and_57 (and_57_out, demultiplexer_13_out1, comparator_39_eq, not_70_out);
  not not_70 (not_70_out, register_123_q);
  Comparator #(.width(8), .mode("unsigned")) comparator_40 (
    .a(demultiplexer_15_out1), .b(register_106_q), .eq(comparator_40_eq));  // open: gt, lt
  Register #(.width(32), .trigger("rising"), .Select("low")) register_114 (
    .D(demultiplexer_14_out1), .en(or_65_out), .Q(register_114_q), .clk(and_27_out));  // open: clr
  and and_58 (and_58_out, demultiplexer_13_out1, comparator_40_eq, not_71_out);
  not not_71 (not_71_out, register_124_q);
  and and_59 (and_59_out, decoder_15_out0, multiplexer_59_out[0]);
  Register #(.width(8), .trigger("rising"), .Select("low")) register_115 (
    .D(multiplexer_76_out), .en(and_49_out), .Q(register_115_q), .clk(and_27_out));  // open: clr
  or or_68 (or_68_out, and_59_out, or_34_out);
  and and_60 (and_60_out, or_68_out, not_59_out);
  Multiplexer #(.select(1), .width(8), .disabled("Z"), .enable("false")) multiplexer_79 (
    .in0(multiplexer_72_out), .in1(multiplexer_3_out[7:0]), .out(multiplexer_79_out), .sel(and_50_out));
  DotMatrix #(.inputtype("column"), .matrixcols(5), .matrixrows(7), .persist(0), .dotshape("square")) dotmatrix_15 ();  // open: col0, col1, col2, col3, col4
  DotMatrix #(.inputtype("column"), .matrixcols(5), .matrixrows(7), .persist(0), .dotshape("square")) dotmatrix_16 (
    .col0(register_47_q), .col1(register_48_q), .col2(register_49_q), .col3(register_50_q),
    .col4(register_51_q));
  and and_61 (and_61_out, demultiplexer_16_out0, comparator_33_eq);
  Multiplexer #(.select(1), .width(32), .disabled("Z"), .enable("false")) multiplexer_80 (
    .in0(slider_22_out), .in1(register_107_q), .out(multiplexer_80_out), .sel(comparator_33_eq));
  and and_62 (and_62_out, demultiplexer_16_out0, comparator_34_eq);
  Multiplexer #(.select(1), .width(32), .disabled("Z"), .enable("false")) multiplexer_81 (
    .in0(slider_22_out), .in1(register_108_q), .out(multiplexer_81_out), .sel(comparator_34_eq));
  and and_63 (and_63_out, demultiplexer_16_out0, comparator_35_eq);
  Multiplexer #(.select(1), .width(32), .disabled("Z"), .enable("false")) multiplexer_82 (
    .in0(slider_22_out), .in1(register_109_q), .out(multiplexer_82_out), .sel(comparator_35_eq));
  and and_64 (and_64_out, demultiplexer_16_out0, comparator_36_eq);
  Multiplexer #(.select(1), .width(32), .disabled("Z"), .enable("false")) multiplexer_83 (
    .in0(slider_22_out), .in1(register_110_q), .out(multiplexer_83_out), .sel(comparator_36_eq));
  and and_65 (and_65_out, demultiplexer_16_out1, comparator_37_eq);
  Multiplexer #(.select(1), .width(32), .disabled("Z"), .enable("false")) multiplexer_84 (
    .in0(slider_23_out), .in1(register_111_q), .out(multiplexer_84_out), .sel(comparator_37_eq));
  and and_66 (and_66_out, demultiplexer_16_out1, comparator_38_eq);
  Multiplexer #(.select(1), .width(32), .disabled("Z"), .enable("false")) multiplexer_85 (
    .in0(slider_23_out), .in1(register_112_q), .out(multiplexer_85_out), .sel(comparator_38_eq));
  and and_67 (and_67_out, demultiplexer_16_out1, comparator_39_eq);
  Multiplexer #(.select(1), .width(32), .disabled("Z"), .enable("false")) multiplexer_86 (
    .in0(slider_23_out), .in1(register_113_q), .out(multiplexer_86_out), .sel(comparator_39_eq));
  and and_68 (and_68_out, demultiplexer_16_out1, comparator_40_eq);
  Multiplexer #(.select(1), .width(32), .disabled("Z"), .enable("false")) multiplexer_87 (
    .in0(slider_23_out), .in1(register_114_q), .out(multiplexer_87_out), .sel(comparator_40_eq));
  Register #(.width(8), .trigger("rising"), .Select("low")) register_116 (
    .D(multiplexer_76_out), .en(and_60_out), .Q(register_116_q), .clk(and_27_out));  // open: clr
  Multiplexer #(.select(1), .width(32), .disabled("Z"), .enable("false")) multiplexer_88 (
    .in0({register_97_q, register_98_q, register_115_q, register_116_q}), .in1({{24{1'b0}}, counter_2_q}),
    .out(multiplexer_88_out), .sel(multiplexer_62_out[4]));
  or or_69 (or_69_out, or_32_out, multiplexer_62_out[0]);
  or or_70 (or_70_out, multiplexer_62_out[1], multiplexer_62_out[3]);
  DotMatrix #(.inputtype("column"), .matrixcols(5), .matrixrows(7), .persist(0), .dotshape("square")) dotmatrix_17 ();  // open: col0, col1, col2, col3, col4
  DotMatrix #(.inputtype("column"), .matrixcols(5), .matrixrows(7), .persist(0), .dotshape("square")) dotmatrix_18 (.col0(undriven_22));  // open: col1, col2, col3, col4
  DotMatrix #(.inputtype("column"), .matrixcols(5), .matrixrows(7), .persist(0), .dotshape("square")) dotmatrix_19 (
    .col0(register_52_q), .col1(register_53_q), .col2(register_54_q), .col3(register_55_q),
    .col4(register_56_q));
  Decoder #(.select(3), .tristate("false"), .disabled("Z"), .enable("false")) decoder_16 (
    .out4(decoder_16_out4), .out5(decoder_16_out5), .out6(decoder_16_out6), .out7(decoder_16_out7),
    .sel(multiplexer_109_out));  // open: out0, out1, out2, out3
  not not_72 (not_72_out, and_61_out);
  not not_73 (not_73_out, and_62_out);
  not not_74 (not_74_out, and_63_out);
  not not_75 (not_75_out, and_64_out);
  Decoder #(.select(3), .tristate("false"), .disabled("Z"), .enable("false")) decoder_17 (
    .out4(decoder_17_out4), .out5(decoder_17_out5), .out6(decoder_17_out6), .out7(decoder_17_out7),
    .sel(multiplexer_110_out));  // open: out0, out1, out2, out3
  not not_76 (not_76_out, and_65_out);
  not not_77 (not_77_out, and_66_out);
  not not_78 (not_78_out, and_67_out);
  not not_79 (not_79_out, and_68_out);
  not not_80 (not_80_out, in_36);
  Counter #(.width(8), .max('hff), .ongoal("wrap"), .trigger("rising"), .behavior("new")) counter_27 (
    .load(in_36), .D(undriven_21), .count(in_35), .Q(counter_27_q), .clk(and_27_out), .down(in_38));  // open: carry, clr, preset
  LED #(.active("true")) led_16 (.in(dipswitch_4_p8[6]));
  LED #(.active("true")) led_17 (.in(dipswitch_4_p8[5]));
  LED #(.active("true")) led_18 (.in(dipswitch_4_p8[4]));
  LED #(.active("true")) led_19 (.in(dipswitch_4_p8[3]));
  LED #(.active("true")) led_20 (.in(dipswitch_4_p8[2]));
  LED #(.active("true")) led_21 (.in(dipswitch_4_p8[1]));
  LED #(.active("true")) led_22 (.in(dipswitch_4_p8[0]));
  DotMatrix #(.inputtype("column"), .matrixcols(5), .matrixrows(7), .persist(0), .dotshape("square")) dotmatrix_20 ();  // open: col0, col1, col2, col3, col4
  DotMatrix #(.inputtype("column"), .matrixcols(5), .matrixrows(7), .persist(0), .dotshape("square")) dotmatrix_21 (
    .col0(register_57_q), .col1(register_58_q), .col2(register_59_q), .col3(register_60_q),
    .col4(register_61_q));
  DotMatrix #(.inputtype("column"), .matrixcols(5), .matrixrows(7), .persist(0), .dotshape("square")) dotmatrix_22 (
    .col0(register_62_q), .col1(register_63_q), .col2(register_64_q), .col3(register_65_q),
    .col4(register_66_q));
  or or_71 (or_71_out, and_61_out, or_51_out);
  or or_72 (or_72_out, and_62_out, or_53_out);
  or or_73 (or_73_out, and_63_out, or_55_out);
  or or_74 (or_74_out, and_64_out, or_57_out);
  or or_75 (or_75_out, and_65_out, or_59_out);
  or or_76 (or_76_out, and_66_out, or_61_out);
  or or_77 (or_77_out, and_67_out, or_63_out);
  or or_78 (or_78_out, and_68_out, or_65_out);
  Slider #(.width(32), .Direction("left_to_right"), .value('h0)) slider_24 (.out(slider_24_out));
  Multiplexer #(.select(1), .width(32), .disabled("Z"), .enable("false")) multiplexer_89 (
    .in0(slider_24_out), .in1(ram_4_data), .out(multiplexer_89_out), .sel(or_70_out));
  Multiplexer #(.select(1), .width(32), .disabled("Z"), .enable("false")) multiplexer_90 (
    .in0({register_97_q, register_98_q, register_115_q, register_116_q}), .in1(undriven_19),
    .out(multiplexer_90_out), .sel(in_25));
  Multiplexer #(.select(1), .width(8), .disabled("Z"), .enable("false")) multiplexer_91 (
    .in0(multiplexer_79_out), .in1(undriven_20), .out(multiplexer_91_out), .sel(in_25));
  and and_69 (and_69_out, in_35, not_80_out);
  DotMatrix #(.inputtype("column"), .matrixcols(5), .matrixrows(7), .persist(0), .dotshape("square")) dotmatrix_23 (.col0(undriven_25));  // open: col1, col2, col3, col4
  DotMatrix #(.inputtype("column"), .matrixcols(5), .matrixrows(7), .persist(0), .dotshape("square")) dotmatrix_24 ();  // open: col0, col1, col2, col3, col4
  DotMatrix #(.inputtype("column"), .matrixcols(5), .matrixrows(7), .persist(0), .dotshape("square")) dotmatrix_25 (
    .col0(register_67_q), .col1(register_68_q), .col2(register_69_q), .col3(register_70_q),
    .col4(register_71_q));
  Slider #(.width(1), .Direction("left_to_right"), .value('h0)) slider_25 (.out(slider_25_out));
  Register #(.width(1), .trigger("rising"), .Select("low")) register_117 (
    .D(not_72_out), .en(or_71_out), .Q(register_117_q), .clk(and_27_out));  // open: clr
  Register #(.width(1), .trigger("rising"), .Select("low")) register_118 (
    .D(not_73_out), .en(or_72_out), .Q(register_118_q), .clk(and_27_out));  // open: clr
  Register #(.width(1), .trigger("rising"), .Select("low")) register_119 (
    .D(not_74_out), .en(or_73_out), .Q(register_119_q), .clk(and_27_out));  // open: clr
  Register #(.width(1), .trigger("rising"), .Select("low")) register_120 (
    .D(not_75_out), .en(or_74_out), .Q(register_120_q), .clk(and_27_out));  // open: clr
  Slider #(.width(1), .Direction("left_to_right"), .value('h0)) slider_26 (.out(slider_26_out));
  Register #(.width(1), .trigger("rising"), .Select("low")) register_121 (
    .D(not_76_out), .en(or_75_out), .Q(register_121_q), .clk(and_27_out));  // open: clr
  Register #(.width(1), .trigger("rising"), .Select("low")) register_122 (
    .D(not_77_out), .en(or_76_out), .Q(register_122_q), .clk(and_27_out));  // open: clr
  Register #(.width(1), .trigger("rising"), .Select("low")) register_123 (
    .D(not_78_out), .en(or_77_out), .Q(register_123_q), .clk(and_27_out));  // open: clr
  Register #(.width(1), .trigger("rising"), .Select("low")) register_124 (
    .D(not_79_out), .en(or_78_out), .Q(register_124_q), .clk(and_27_out));  // open: clr
  Multiplexer #(.select(1), .width(32), .disabled("Z"), .enable("false")) multiplexer_92 (
    .in0(multiplexer_120_out), .in1(multiplexer_89_out), .out(multiplexer_92_out), .sel(multiplexer_122_out));
  Multiplexer #(.select(1), .width(32), .disabled("Z"), .enable("false")) multiplexer_93 (
    .in0(multiplexer_90_out), .in1(undriven_23), .out(multiplexer_93_out), .sel(in_26));
  Multiplexer #(.select(1), .width(32), .disabled("Z"), .enable("false")) multiplexer_94 (
    .in0(multiplexer_93_out), .in1(multiplexer_88_out), .out(multiplexer_94_out), .sel(or_32_out));
  Multiplexer #(.select(1), .width(8), .disabled("Z"), .enable("false")) multiplexer_95 (
    .in0(multiplexer_91_out), .in1(undriven_24), .out(multiplexer_95_out), .sel(in_26));
  Multiplexer #(.select(1), .width(8), .disabled("Z"), .enable("false")) multiplexer_96 (
    .in0(multiplexer_95_out), .in1(multiplexer_77_out), .out(multiplexer_96_out), .sel(or_48_out));
  not not_81 (not_81_out, in_38);
  Counter #(.width(8), .max('hff), .ongoal("wrap"), .trigger("rising"), .behavior("new")) counter_28 (.Q(counter_28_q));  // open: load, D, count, carry, clk, clr, preset, down
  ROM #(.addrWidth(8), .dataWidth(8), .Select("low")) rom_21 (.data(rom_21_data));  // open: addr
  DotMatrix #(.inputtype("column"), .matrixcols(5), .matrixrows(7), .persist(0), .dotshape("square")) dotmatrix_26 ();  // open: col0, col1, col2, col3, col4
  DotMatrix #(.inputtype("column"), .matrixcols(5), .matrixrows(7), .persist(0), .dotshape("square")) dotmatrix_27 ();  // open: col0, col1, col2, col3, col4
  DotMatrix #(.inputtype("column"), .matrixcols(5), .matrixrows(7), .persist(0), .dotshape("square")) dotmatrix_28 (
    .col0(register_72_q), .col1(register_73_q), .col2(register_74_q), .col3(register_75_q),
    .col4(register_76_q));
  DotMatrix #(.inputtype("column"), .matrixcols(5), .matrixrows(7), .persist(0), .dotshape("square")) dotmatrix_29 (
    .col0(register_77_q), .col1(register_78_q), .col2(register_79_q), .col3(register_80_q),
    .col4(register_81_q));
  Multiplexer #(.select(3), .width(1), .disabled("Z"), .enable("false")) multiplexer_97 (
    .in0(slider_25_out), .in1(slider_25_out), .in2(slider_25_out), .in3(slider_25_out), .in4(register_120_q),
    .in5(register_119_q), .in6(register_118_q), .in7(register_117_q), .out(multiplexer_97_out),
    .sel(multiplexer_111_out));
  Multiplexer #(.select(3), .width(1), .disabled("Z"), .enable("false")) multiplexer_98 (
    .in0(slider_26_out), .in1(slider_26_out), .in2(slider_26_out), .in3(slider_26_out), .in4(register_124_q),
    .in5(register_123_q), .in6(register_122_q), .in7(register_121_q), .out(multiplexer_98_out),
    .sel(multiplexer_113_out));
  Register #(.width(8), .trigger("rising"), .Select("low")) register_125 (
    .D(multiplexer_92_out[31:24]), .en(or_70_out), .Q(register_125_q), .clk(and_27_out), .clr(in_10));
  Register #(.width(32), .trigger("rising"), .Select("low")) register_126 (
    .D(multiplexer_99_out), .en(or_70_out), .Q(register_126_q), .clk(and_27_out));  // open: clr
  Multiplexer #(.select(1), .width(32), .disabled("Z"), .enable("false")) multiplexer_99 (
    .in0(multiplexer_92_out), .in1(multiplexer_89_out), .out(multiplexer_99_out), .sel(multiplexer_122_out));
  DotMatrix #(.inputtype("column"), .matrixcols(5), .matrixrows(7), .persist(0), .dotshape("square")) dotmatrix_30 (
    .col0(register_82_q), .col1(register_83_q), .col2(register_84_q), .col3(register_85_q),
    .col4(register_86_q));
  DotMatrix #(.inputtype("column"), .matrixcols(5), .matrixrows(7), .persist(0), .dotshape("square")) dotmatrix_31 (
    .col0(register_87_q), .col1(register_88_q), .col2(register_89_q), .col3(register_90_q),
    .col4(register_91_q));
  Register #(.width(8), .trigger("rising"), .Select("low")) register_127 (
    .D(multiplexer_92_out[23:16]), .en(or_70_out), .Q(register_127_q), .clk(and_27_out), .clr(in_10));
  // NOT_Gate not_82 has open pins: in=and_27_out, out=open
  or or_79 (or_79_out, or_69_out, in_45);
  Decoder #(.select(3), .tristate("false"), .disabled("Z"), .enable("false")) decoder_18 (
    .out0(decoder_18_out0), .out1(decoder_18_out1), .out7(decoder_18_out7), .sel(counter_28_q[2:0]));  // open: out2, out3, out4, out5, out6
  Register #(.width(8), .trigger("rising"), .Select("low")) register_128 ();  // open: D, en, Q, clk, clr
  DotMatrix #(.inputtype("column"), .matrixcols(5), .matrixrows(7), .persist(0), .dotshape("square")) dotmatrix_32 (
    .col0(register_92_q), .col1(register_93_q), .col2(register_94_q), .col3(register_95_q),
    .col4(register_96_q));
  not not_83 (not_83_out, and_27_out);
  not not_84 (not_84_out, and_27_out);
  and and_70 (and_70_out, counter_1_q, register_35_q);
  LED #(.active("true")) led_23 ();  // open: in
  or or_80 (or_80_out, comparator_41_gt, comparator_41_eq);
  Comparator #(.width(8), .mode("unsigned")) comparator_41 (
    .a(counter_18_q), .b(counter_19_q), .gt(comparator_41_gt), .eq(comparator_41_eq));  // open: lt
  not not_85 (not_85_out, or_80_out);
  Comparator #(.width(8), .mode("unsigned")) comparator_42 (
    .a(multiplexer_100_out), .b(multiplexer_101_out), .gt(comparator_42_gt), .eq(comparator_42_eq));  // open: lt
  not not_86 (not_86_out, or_81_out);
  Comparator #(.width(8), .mode("unsigned")) comparator_43 (
    .a(counter_20_q), .b(counter_21_q), .gt(comparator_43_gt), .eq(comparator_43_eq));  // open: lt
  or or_81 (or_81_out, comparator_43_gt, comparator_43_eq);
  or or_82 (or_82_out, comparator_44_gt, comparator_44_eq);
  Comparator #(.width(8), .mode("unsigned")) comparator_44 (
    .a(counter_22_q), .b(counter_23_q), .gt(comparator_44_gt), .eq(comparator_44_eq));  // open: lt
  not not_87 (not_87_out, or_82_out);
  Comparator #(.width(8), .mode("unsigned")) comparator_45 (
    .a(multiplexer_102_out), .b(multiplexer_103_out), .gt(comparator_45_gt), .eq(comparator_45_eq));  // open: lt
  or or_83 (or_83_out, comparator_46_gt, comparator_46_eq);
  Comparator #(.width(8), .mode("unsigned")) comparator_46 (
    .a(counter_24_q), .b(counter_25_q), .gt(comparator_46_gt), .eq(comparator_46_eq));  // open: lt
  not not_88 (not_88_out, or_83_out);
  Register #(.width(8), .trigger("rising"), .Select("low")) register_129 (
    .D(multiplexer_92_out[15:8]), .en(or_70_out), .Q(register_129_q), .clk(and_27_out), .clr(in_10));
  or or_84 (or_84_out, and_70_out, or_70_out);
  DotMatrix #(.inputtype("column"), .matrixcols(5), .matrixrows(7), .persist(0), .dotshape("square")) dotmatrix_33 (
    .col0(register_130_q), .col1(register_131_q));  // open: col2, col3, col4
  Register #(.width(7), .trigger("rising"), .Select("low")) register_130 (
    .D(rom_21_data[6:0]), .en(decoder_18_out0), .Q(register_130_q));  // open: clk, clr
  Register #(.width(7), .trigger("rising"), .Select("low")) register_131 (
    .en(decoder_18_out1), .Q(register_131_q));  // open: D, clk, clr
  Multiplexer #(.select(1), .width(8), .disabled("Z"), .enable("false")) multiplexer_100 (
    .in0(counter_18_q), .in1(counter_19_q), .out(multiplexer_100_out), .sel(not_85_out));
  not not_89 (not_89_out, or_85_out);
  or or_85 (or_85_out, comparator_42_gt, comparator_42_eq);
  Multiplexer #(.select(1), .width(8), .disabled("Z"), .enable("false")) multiplexer_101 (
    .in0(counter_20_q), .in1(counter_21_q), .out(multiplexer_101_out), .sel(not_86_out));
  Multiplexer #(.select(1), .width(8), .disabled("Z"), .enable("false")) multiplexer_102 (
    .in0(counter_22_q), .in1(counter_23_q), .out(multiplexer_102_out), .sel(not_87_out));
  or or_86 (or_86_out, comparator_45_gt, comparator_45_eq);
  not not_90 (not_90_out, or_86_out);
  Multiplexer #(.select(1), .width(8), .disabled("Z"), .enable("false")) multiplexer_103 (
    .in0(counter_24_q), .in1(counter_25_q), .out(multiplexer_103_out), .sel(not_88_out));
  Register #(.width(8), .trigger("rising"), .Select("low")) register_132 (
    .D(multiplexer_92_out[7:0]), .en(or_70_out), .Q(register_132_q), .clk(and_27_out), .clr(in_10));
  RAM #(.addrWidth(8), .dataWidth(32), .bus("separate"), .Select("low")) ram_4 (
    .addr(multiplexer_96_out), .din(multiplexer_94_out), .data(ram_4_data), .str(or_79_out),
    .sel(undriven_26), .clk(and_27_out), .ld(or_84_out));  // open: clr
  Multiplexer #(.select(1), .width(8), .disabled("Z"), .enable("false")) multiplexer_104 (
    .in0(multiplexer_100_out), .in1(multiplexer_101_out), .out(multiplexer_104_out), .sel(not_89_out));
  Multiplexer #(.select(1), .width(8), .disabled("Z"), .enable("false")) multiplexer_105 (
    .in0(multiplexer_102_out), .in1(multiplexer_103_out), .out(multiplexer_105_out), .sel(not_90_out));
  Multiplexer #(.select(2), .width(8), .disabled("Z"), .enable("false")) multiplexer_106 (
    .in0(register_132_q), .in1(register_129_q), .in2(register_127_q), .in3(register_125_q),
    .out(multiplexer_106_out), .sel(priority_encoder_2_out));
  Comparator #(.width(8), .mode("unsigned")) comparator_47 (
    .a(multiplexer_104_out), .b(counter_18_q), .eq(comparator_47_eq));  // open: gt, lt
  Comparator #(.width(8), .mode("unsigned")) comparator_48 (
    .a(multiplexer_104_out), .b(counter_19_q), .eq(comparator_48_eq));  // open: gt, lt
  Comparator #(.width(8), .mode("unsigned")) comparator_49 (
    .a(multiplexer_104_out), .b(counter_20_q), .eq(comparator_49_eq));  // open: gt, lt
  Comparator #(.width(8), .mode("unsigned")) comparator_50 (
    .a(multiplexer_104_out), .b(counter_21_q), .eq(comparator_50_eq));  // open: gt, lt
  Comparator #(.width(8), .mode("unsigned")) comparator_51 (
    .a(multiplexer_105_out), .b(counter_22_q), .eq(comparator_51_eq));  // open: gt, lt
  Comparator #(.width(8), .mode("unsigned")) comparator_52 (
    .a(multiplexer_105_out), .b(counter_23_q), .eq(comparator_52_eq));  // open: gt, lt
  Comparator #(.width(8), .mode("unsigned")) comparator_53 (
    .a(multiplexer_105_out), .b(counter_24_q), .eq(comparator_53_eq));  // open: gt, lt
  Comparator #(.width(8), .mode("unsigned")) comparator_54 (
    .a(multiplexer_105_out), .b(counter_25_q), .eq(comparator_54_eq));  // open: gt, lt
  Comparator #(.width(8), .mode("unsigned")) comparator_55 (
    .a(undriven_33), .b(undriven_29), .gt(comparator_55_gt), .eq(comparator_55_eq));  // open: lt
  Comparator #(.width(8), .mode("unsigned")) comparator_56 (
    .a(undriven_34), .b(undriven_30), .gt(comparator_56_gt), .eq(comparator_56_eq));  // open: lt
  Counter #(.width(8), .max('hff), .ongoal("wrap"), .trigger("rising"), .behavior("new")) counter_29 ();  // open: load, D, count, Q, carry, clk, clr, preset, down
  and and_71 (and_71_out, undriven_27, undriven_35);
  or or_87 (or_87_out, and_71_out, comparator_57_eq);
  and and_72 (and_72_out, register_35_q, not_91_out);
  not not_91 (not_91_out, or_70_out);
  not not_92 (not_92_out, or_88_out);
  or or_88 (or_88_out, comparator_55_gt, comparator_55_eq);
  not not_93 (not_93_out, in_2);
  not not_94 (not_94_out, or_89_out);
  or or_89 (or_89_out, comparator_56_gt, comparator_56_eq);
  not not_95 (not_95_out, in_7);
  Slider #(.width(8), .Direction("left_to_right"), .value('h0)) slider_27 (.out(slider_27_out));
  Slider #(.width(2), .Direction("left_to_right"), .value('h3)) slider_28 ();  // open: out
  or or_90 (or_90_out, or_87_out, and_74_out);
  or or_91 (or_91_out, and_74_out, and_71_out);
  and and_73 (and_73_out, undriven_36, undriven_38);
  or or_92 (or_92_out, and_73_out, comparator_59_eq);
  not not_96 (not_96_out, or_93_out);
  or or_93 (or_93_out, undriven_37, undriven_46);
  Register #(.width(32), .trigger("rising"), .Select("low")) register_133 (
    .D(ram_4_data), .en(and_72_out), .Q(register_133_q), .clk(and_27_out));  // open: clr
  not not_97 (not_97_out, and_27_out);
  not not_98 (not_98_out, in_54);
  Multiplexer #(.select(1), .width(8), .disabled("Z"), .enable("false")) multiplexer_107 (
    .in0(undriven_33), .in1(undriven_29), .sel(not_92_out));  // open: out
  Priority_Encoder #(.select(3), .disabled("Z")) priority_encoder_3 (
    .in0(not_93_out), .in1(not_93_out), .in2(not_93_out), .in3(not_93_out), .in4(comparator_50_eq),
    .in5(comparator_49_eq), .in6(comparator_48_eq), .in7(comparator_47_eq), .out(priority_encoder_3_out));  // open: gs, en_out, en_in
  Slider #(.width(3), .Direction("left_to_right"), .value('h0)) slider_29 (.out(slider_29_out));
  Multiplexer #(.select(1), .width(8), .disabled("Z"), .enable("false")) multiplexer_108 (
    .in0(undriven_34), .in1(undriven_30), .sel(not_94_out));  // open: out
  Priority_Encoder #(.select(3), .disabled("Z")) priority_encoder_4 (
    .in0(not_95_out), .in1(not_95_out), .in2(not_95_out), .in3(not_95_out), .in4(comparator_54_eq),
    .in5(comparator_53_eq), .in6(comparator_52_eq), .in7(comparator_51_eq), .out(priority_encoder_4_out));  // open: gs, en_out, en_in
  Slider #(.width(3), .Direction("left_to_right"), .value('h0)) slider_30 (.out(slider_30_out));
  Counter #(.width(8), .max('hff), .ongoal("wrap"), .trigger("rising"), .behavior("new")) counter_30 (
    .load(comparator_58_eq), .D(slider_27_out), .Q(counter_30_q));  // open: count, carry, clk, clr, preset, down
  Counter #(.width(8), .max('hff), .ongoal("wrap"), .trigger("rising"), .behavior("new")) counter_31 (
    .Q(counter_31_q), .down(undriven_45));  // open: load, D, count, carry, clk, clr, preset
  Counter #(.width(8), .max('hff), .ongoal("wrap"), .trigger("rising"), .behavior("new")) counter_32 (
    .load(or_90_out), .D(undriven_41), .count(undriven_27), .Q(counter_32_q), .clk(undriven_28));  // open: carry, clr, preset, down
  Counter #(.width(8), .max('hff), .ongoal("wrap"), .trigger("rising"), .behavior("new")) counter_33 (
    .load(or_92_out), .D(undriven_42), .count(undriven_36), .Q(counter_33_q), .clk(undriven_43));  // open: carry, clr, preset, down
  Counter #(.width(8), .max('hff), .ongoal("wrap"), .trigger("rising"), .behavior("new")) counter_34 (
    .count(not_96_out), .Q(counter_34_q), .clk(undriven_44));  // open: load, D, carry, clr, preset, down
  Register #(.width(8), .trigger("rising"), .Select("low")) register_134 (
    .D(adder_6_out), .en(not_98_out), .Q(register_134_q), .clk(in_56), .cs(in_52), .preset(in_50));  // open: clr
  Slider #(.width(3), .Direction("left_to_right"), .value('h0)) slider_31 (.out(slider_31_out));
  Priority_Encoder #(.select(3), .disabled("Z")) priority_encoder_5 (
    .in0(in_1), .in1(in_1), .in2(in_1), .in3(in_1), .in4(comparator_36_eq), .in5(comparator_35_eq),
    .in6(comparator_34_eq), .in7(comparator_33_eq), .out(priority_encoder_5_out), .gs(priority_encoder_5_gs));  // open: en_out, en_in
  Multiplexer #(.select(1), .width(3), .disabled("Z"), .enable("false")) multiplexer_109 (
    .in0(priority_encoder_3_out), .in1(slider_29_out), .out(multiplexer_109_out), .sel(priority_encoder_5_gs));
  Slider #(.width(3), .Direction("left_to_right"), .value('h0)) slider_32 (.out(slider_32_out));
  Priority_Encoder #(.select(3), .disabled("Z")) priority_encoder_6 (
    .in0(in_4), .in1(in_4), .in2(in_4), .in3(in_4), .in4(comparator_40_eq), .in5(comparator_39_eq),
    .in6(comparator_38_eq), .in7(comparator_37_eq), .out(priority_encoder_6_out), .gs(priority_encoder_6_gs));  // open: en_out, en_in
  Multiplexer #(.select(1), .width(3), .disabled("Z"), .enable("false")) multiplexer_110 (
    .in0(priority_encoder_4_out), .in1(slider_30_out), .out(multiplexer_110_out), .sel(priority_encoder_6_gs));
  Comparator #(.width(8), .mode("unsigned")) comparator_57 (
    .a(undriven_32), .b(register_135_q), .eq(comparator_57_eq));  // open: gt, lt
  Register #(.width(8), .trigger("rising"), .Select("low")) register_135 (
    .D(undriven_32), .en(or_91_out), .Q(register_135_q), .clk(undriven_28));  // open: clr
  and and_74 (and_74_out, not_101_out, undriven_27, comparator_57_eq);
  Register #(.width(8), .trigger("rising"), .Select("low")) register_136 (
    .D(undriven_39), .en(and_73_out), .Q(register_136_q), .clk(undriven_43));  // open: clr
  Register #(.width(8), .trigger("rising"), .Select("low")) register_137 (
    .D(undriven_40), .en(undriven_46), .Q(register_137_q), .clk(undriven_44));  // open: clr
  Slider #(.width(8), .Direction("left_to_right"), .value('h3)) slider_33 (.out(slider_33_out));
  Multiplexer #(.select(1), .width(3), .disabled("Z"), .enable("false")) multiplexer_111 (
    .in0(slider_31_out), .in1(priority_encoder_5_out), .out(multiplexer_111_out), .sel(priority_encoder_5_gs));
  Slider #(.width(1), .Direction("left_to_right"), .value('h0)) slider_34 (.out(slider_34_out));
  Multiplexer #(.select(1), .width(1), .disabled("Z"), .enable("false")) multiplexer_112 (
    .in0(slider_34_out), .in1(priority_encoder_5_gs), .out(multiplexer_112_out), .sel(multiplexer_97_out));
  not not_99 (not_99_out, multiplexer_112_out);
  Multiplexer #(.select(1), .width(3), .disabled("Z"), .enable("false")) multiplexer_113 (
    .in0(slider_32_out), .in1(priority_encoder_6_out), .out(multiplexer_113_out), .sel(priority_encoder_6_gs));
  Slider #(.width(1), .Direction("left_to_right"), .value('h0)) slider_35 (.out(slider_35_out));
  Multiplexer #(.select(1), .width(1), .disabled("Z"), .enable("false")) multiplexer_114 (
    .in0(slider_35_out), .in1(priority_encoder_6_gs), .out(multiplexer_114_out), .sel(multiplexer_98_out));
  not not_100 (not_100_out, multiplexer_114_out);
  Decoder #(.select(2), .tristate("false"), .disabled("Z"), .enable("false")) decoder_19 (
    .out0(decoder_19_out0), .out1(decoder_19_out1), .out2(decoder_19_out1), .out3(decoder_19_out3),
    .sel(counter_30_q[1:0]));
  Comparator #(.width(2), .mode("unsigned")) comparator_58 (
    .a(counter_30_q[1:0]), .b(counter_31_q[1:0]), .eq(comparator_58_eq));  // open: gt, lt
  Register #(.width(32), .trigger("rising"), .Select("low")) register_138 (
    .D(undriven_47), .en(or_91_out), .Q(register_138_q), .clk(undriven_28));  // open: clr
  not not_101 (not_101_out, register_144_q);
  Comparator #(.width(8), .mode("unsigned")) comparator_59 (
    .a(undriven_39), .b(register_136_q), .eq(comparator_59_eq));  // open: gt, lt
  Register #(.width(32), .trigger("rising"), .Select("low")) register_139 (
    .D(undriven_48), .en(and_73_out), .Q(register_139_q), .clk(undriven_43));  // open: clr
  Comparator #(.width(8), .mode("unsigned")) comparator_60 (
    .a(undriven_40), .b(register_137_q), .eq(comparator_60_eq));  // open: gt, lt
  Register #(.width(32), .trigger("rising"), .Select("low")) register_140 (
    .en(undriven_46), .Q(register_140_q), .clk(undriven_44));  // open: D, clr
  Adder #(.width(8)) adder_6 (.a(register_134_q), .b(slider_33_out), .out(adder_6_out));  // open: cin, cout
  Multiplexer #(.select(3), .width(32), .disabled("Z"), .enable("false")) multiplexer_115 (
    .in4(multiplexer_83_out), .in5(multiplexer_82_out), .in6(multiplexer_81_out), .in7(multiplexer_80_out),
    .out(multiplexer_115_out), .sel(multiplexer_111_out));  // open: in0, in1, in2, in3
  Multiplexer #(.select(3), .width(32), .disabled("Z"), .enable("false")) multiplexer_116 (
    .in4(multiplexer_87_out), .in5(multiplexer_86_out), .in6(multiplexer_85_out), .in7(multiplexer_84_out),
    .out(multiplexer_116_out), .sel(multiplexer_113_out));  // open: in0, in1, in2, in3
  Counter #(.width(8), .max('hff), .ongoal("wrap"), .trigger("rising"), .behavior("new")) counter_35 ();  // open: load, D, count, Q, carry, clk, clr, preset, down
  not not_102 (not_102_out, comparator_58_eq);
  and and_75 (and_75_out, undriven_31, comparator_57_eq);
  not not_103 (not_103_out, and_75_out);
  Multiplexer #(.select(1), .width(32), .disabled("Z"), .enable("false")) multiplexer_117 (
    .in0(undriven_49), .in1(register_138_q), .out(multiplexer_117_out), .sel(comparator_57_eq));
  Multiplexer #(.select(1), .width(32), .disabled("Z"), .enable("false")) multiplexer_118 (
    .in0(undriven_50), .in1(register_139_q), .out(multiplexer_118_out), .sel(comparator_59_eq));
  Multiplexer #(.select(1), .width(32), .disabled("Z"), .enable("false")) multiplexer_119 (
    .in0(undriven_51), .in1(register_140_q), .sel(comparator_60_eq));  // open: out
  Register #(.width(32), .trigger("rising"), .Select("low")) register_141 (
    .en(decoder_19_out1), .Q(register_141_q));  // open: D, clk, clr
  Register #(.width(32), .trigger("rising"), .Select("low")) register_142 (
    .en(decoder_19_out3), .Q(register_142_q));  // open: D, clk, clr
  or or_94 (or_94_out, and_75_out, or_91_out);
  Register #(.width(32), .trigger("rising"), .Select("low")) register_143 (
    .en(decoder_19_out1), .Q(register_143_q));  // open: D, clk, clr
  Register #(.width(1), .trigger("rising"), .Select("low")) register_144 (
    .D(not_103_out), .en(or_94_out), .Q(register_144_q), .clk(undriven_28));  // open: clr
  Multiplexer #(.select(1), .width(32), .disabled("Z"), .enable("false")) multiplexer_120 (
    .in0(multiplexer_115_out), .in1(multiplexer_116_out), .out(multiplexer_120_out),
    .sel(multiplexer_96_out[0]));
  Register #(.width(32), .trigger("rising"), .Select("low")) register_145 (
    .en(decoder_19_out0), .Q(register_145_q));  // open: D, clk, clr
  // Probe on joystick_1_x
  Joystick #(.bits(5)) joystick_1 (.x(joystick_1_x), .y(joystick_1_y));
  // Probe on joystick_1_y
  Multiplexer #(.select(2), .width(32), .disabled("Z"), .enable("false")) multiplexer_121 (
    .in0(register_145_q), .in1(register_143_q), .in2(register_141_q), .in3(register_142_q), .sel(undriven_52));  // open: out
  Clock #(.highDuration(1), .lowDuration(1)) clock_4 (.out(clock_4_out));
  Multiplexer #(.select(1), .width(1), .disabled("Z"), .enable("false")) multiplexer_122 (
    .in0(not_99_out), .in1(not_100_out), .out(multiplexer_122_out), .sel(multiplexer_96_out[0]));
  Slider #(.width(8), .Direction("left_to_right"), .value('h0)) slider_36 (.out(slider_36_out));
  Counter #(.width(8), .max('hff), .ongoal("wrap"), .trigger("rising"), .behavior("new")) counter_36 (
    .load(comparator_61_eq), .D(slider_36_out), .count(\开关启动模拟加入新进程 ), .Q(counter_36_q), .clk(clock_4_out));  // open: carry, clr, preset, down
  Slider #(.width(8), .Direction("left_to_right"), .value('h8)) slider_37 (.out(slider_37_out));
  Comparator #(.width(8), .mode("unsigned")) comparator_61 (
    .a(counter_36_q), .b(slider_37_out), .eq(comparator_61_eq));  // open: gt, lt
  or or_95 (or_95_out, in_72, or_100_out);
  not not_104 (not_104_out, register_146_q);
  not not_105 (not_105_out, register_146_q);
  // NOT_Gate not_106 has open pins: in=in_80, out=open
  Slider #(.width(8), .Direction("left_to_right"), .value('h0)) slider_38 (.out(slider_38_out));
  and and_76 (and_76_out, not_107_out, and_77_out);
  and and_77 (and_77_out, not_108_out, not_104_out);
  or or_96 (or_96_out, not_105_out, or_97_out);
  not not_107 (not_107_out, or_97_out);
  ROM #(.addrWidth(8), .dataWidth(32), .Select("low")) rom_22 ();  // open: addr, data
  not not_108 (not_108_out, not_110_out);
  Register #(.width(1), .trigger("rising"), .Select("low")) register_146 (
    .D(register_147_q), .en(or_96_out), .Q(register_146_q), .clk(clock_6_out));  // open: clr
  Register #(.width(1), .trigger("rising"), .Select("low")) register_147 (
    .D(and_76_out), .en(or_96_out), .Q(register_147_q), .clk(clock_6_out));  // open: clr
  not not_109 (not_109_out, or_97_out);
  or or_97 (or_97_out, register_148_q, or_100_out);
  Clock #(.highDuration(1), .lowDuration(1)) clock_5 (.out(clock_5_out));
  ROM #(.addrWidth(8), .dataWidth(32), .Select("low")) rom_23 (.addr(counter_36_q), .data(rom_23_data));
  Clock #(.highDuration(1), .lowDuration(1)) clock_6 (.out(clock_6_out));
  Register #(.width(1), .trigger("rising"), .Select("low")) register_148 (
    .D(register_146_q), .en(or_98_out), .Q(register_148_q), .clk(clock_6_out));  // open: clr
  or or_98 (or_98_out, not_109_out, or_100_out);
  Counter #(.width(8), .max('hff), .ongoal("wrap"), .trigger("rising"), .behavior("new")) counter_37 (
    .load(comparator_62_eq), .D(slider_39_out), .Q(counter_37_q), .clk(clock_5_out));  // open: count, carry, clr, preset, down
  Slider #(.width(8), .Direction("left_to_right"), .value('h0)) slider_39 (.out(slider_39_out));
  Slider #(.width(8), .Direction("left_to_right"), .value('h14)) slider_40 (.out(slider_40_out));
  Counter #(.width(8), .max('hff), .ongoal("wrap"), .trigger("rising"), .behavior("new")) counter_38 (
    .load(comparator_63_eq), .D(slider_38_out), .count(not_110_out), .Q(counter_38_q), .clk(clock_6_out),
    .down(in_70));  // open: carry, clr, preset
  and and_78 (and_78_out, comparator_63_eq, not_110_out);
  or or_99 (or_99_out, not_110_out, or_95_out);
  Counter #(.width(1), .max('h1), .ongoal("wrap"), .trigger("rising"), .behavior("new")) counter_39 (
    .Q(counter_39_q), .clk(clock_8_out));  // open: load, D, count, carry, clr, preset, down
  or or_100 (or_100_out, or_129_out, or_139_out);
  Slider #(.width(8), .Direction("left_to_right"), .value('h0)) slider_41 (.out(slider_41_out));
  and and_79 (and_79_out, undriven_53, decoder_20_out7);
  or or_101 (or_101_out, and_79_out, comparator_66_eq);
  and and_80 (and_80_out, undriven_53, decoder_20_out6);
  or or_102 (or_102_out, and_80_out, comparator_67_eq);
  and and_81 (and_81_out, undriven_53, decoder_20_out5);
  or or_103 (or_103_out, and_81_out, comparator_68_eq);
  and and_82 (and_82_out, undriven_53, decoder_20_out4);
  or or_104 (or_104_out, and_82_out, comparator_69_eq);
  Comparator #(.width(8), .mode("unsigned")) comparator_62 (
    .a(counter_37_q), .b(slider_42_out), .eq(comparator_62_eq));  // open: gt, lt
  Slider #(.width(8), .Direction("left_to_right"), .value('h3)) slider_42 (.out(slider_42_out));
  or or_105 (or_105_out, \开关启动模拟加入新进程 , in_58);
  or or_106 (or_106_out, \开关启动模拟加入新进程 , in_60);
  Slider #(.width(8), .Direction("left_to_right"), .value('h0)) slider_43 (.out(slider_43_out));
  Clock #(.highDuration(1), .lowDuration(1)) clock_7 (.out(clock_7_out));
  Slider #(.width(8), .Direction("left_to_right"), .value('h0)) slider_44 (.out(slider_44_out));
  Comparator #(.width(8), .mode("unsigned")) comparator_63 (
    .a(slider_40_out), .b(counter_38_q), .eq(comparator_63_eq));  // open: gt, lt
  Register #(.width(1), .trigger("rising"), .Select("low")) register_149 (
    .D(and_78_out), .en(or_99_out), .Q(register_149_q), .clk(clock_6_out));  // open: clr
  not not_110 (not_110_out, register_149_q);
  Slider #(.width(8), .Direction("left_to_right"), .value('h82)) slider_45 (.out(slider_45_out));
  Counter #(.width(8), .max('hff), .ongoal("wrap"), .trigger("rising"), .behavior("new")) counter_40 (
    .Q(counter_40_q), .clk(clock_8_out), .down(not_111_out));  // open: load, D, count, carry, clr, preset
  not not_111 (not_111_out, in_83);
  Clock #(.highDuration(1), .lowDuration(1)) clock_8 (.out(clock_8_out));
  or or_107 (or_107_out, or_101_out, and_83_out);
  Counter #(.width(8), .max('hff), .ongoal("wrap"), .trigger("rising"), .behavior("new")) counter_41 (
    .load(or_107_out), .D(slider_41_out), .count(undriven_53), .Q(counter_41_q), .clk(undriven_59));  // open: carry, clr, preset, down
  or or_108 (or_108_out, and_83_out, and_79_out);
  or or_109 (or_109_out, or_102_out, and_84_out);
  Counter #(.width(8), .max('hff), .ongoal("wrap"), .trigger("rising"), .behavior("new")) counter_42 (
    .load(or_109_out), .D(slider_41_out), .count(undriven_53), .Q(counter_42_q), .clk(undriven_59));  // open: carry, clr, preset, down
  or or_110 (or_110_out, and_84_out, and_80_out);
  or or_111 (or_111_out, or_103_out, and_85_out);
  Counter #(.width(8), .max('hff), .ongoal("wrap"), .trigger("rising"), .behavior("new")) counter_43 (
    .load(or_111_out), .D(slider_41_out), .count(undriven_53), .Q(counter_43_q), .clk(undriven_59));  // open: carry, clr, preset, down
  or or_112 (or_112_out, and_85_out, and_81_out);
  or or_113 (or_113_out, or_104_out, and_86_out);
  Counter #(.width(8), .max('hff), .ongoal("wrap"), .trigger("rising"), .behavior("new")) counter_44 (
    .load(or_113_out), .D(slider_41_out), .count(undriven_53), .Q(counter_44_q), .clk(undriven_59));  // open: carry, clr, preset, down
  or or_114 (or_114_out, and_86_out, and_82_out);
  Counter #(.width(8), .max('hff), .ongoal("wrap"), .trigger("rising"), .behavior("new")) counter_45 (
    .load(comparator_64_eq), .D(slider_43_out), .count(or_106_out), .Q(counter_45_q), .clk(clock_7_out));  // open: carry, clr, preset, down
  Slider #(.width(8), .Direction("left_to_right"), .value('h7)) slider_46 (.out(slider_46_out));
  Counter #(.width(8), .max('hff), .ongoal("wrap"), .trigger("rising"), .behavior("new")) counter_46 (
    .load(comparator_65_eq), .D(slider_44_out), .count(in_65), .Q(counter_46_q), .clk(clock_7_out));  // open: carry, clr, preset, down
  Slider #(.width(8), .Direction("left_to_right"), .value('h3)) slider_47 (.out(slider_47_out));
  Counter #(.width(8), .max('hff), .ongoal("wrap"), .trigger("rising"), .behavior("new")) counter_47 (
    .count(counter_39_q), .Q(counter_47_q), .clk(clock_8_out));  // open: load, D, carry, clr, preset, down
  Slider #(.width(8), .Direction("left_to_right"), .value('h0)) slider_48 (.out(slider_48_out));
  Register #(.width(8), .trigger("rising"), .Select("low")) register_150 (
    .D(undriven_55), .en(or_108_out), .Q(register_150_q), .clk(undriven_59));  // open: clr
  Register #(.width(8), .trigger("rising"), .Select("low")) register_151 (
    .D(undriven_55), .en(or_110_out), .Q(register_151_q), .clk(undriven_59));  // open: clr
  Register #(.width(8), .trigger("rising"), .Select("low")) register_152 (
    .D(undriven_55), .en(or_112_out), .Q(register_152_q), .clk(undriven_59));  // open: clr
  Register #(.width(8), .trigger("rising"), .Select("low")) register_153 (
    .D(undriven_55), .en(or_114_out), .Q(register_153_q), .clk(undriven_59));  // open: clr
  Counter #(.width(8), .max('hff), .ongoal("wrap"), .trigger("rising"), .behavior("new")) counter_48 (
    .count(undriven_56), .Q(counter_48_q));  // open: load, D, carry, clk, clr, preset, down
  not not_112 (not_112_out, or_105_out);
  Comparator #(.width(8), .mode("unsigned")) comparator_64 (
    .a(counter_45_q), .b(slider_46_out), .eq(comparator_64_eq));  // open: gt, lt
  Comparator #(.width(8), .mode("unsigned")) comparator_65 (
    .a(counter_46_q), .b(slider_46_out), .eq(comparator_65_eq));  // open: gt, lt
  Multiplexer #(.select(1), .width(8), .disabled("Z"), .enable("false")) multiplexer_123 (
    .in0(undriven_57), .in1(slider_48_out), .out(multiplexer_123_out), .sel(not_126_out));
  Comparator #(.width(8), .mode("unsigned")) comparator_66 (
    .a(undriven_55), .b(register_150_q), .eq(comparator_66_eq));  // open: gt, lt
  not not_113 (not_113_out, register_159_q);
  and and_83 (and_83_out, not_113_out, undriven_53, comparator_66_eq);
  Comparator #(.width(8), .mode("unsigned")) comparator_67 (
    .a(undriven_55), .b(register_151_q), .eq(comparator_67_eq));  // open: gt, lt
  and and_84 (and_84_out, undriven_53, not_116_out, comparator_67_eq);
  Comparator #(.width(8), .mode("unsigned")) comparator_68 (
    .a(undriven_55), .b(register_152_q), .eq(comparator_68_eq));  // open: gt, lt
  and and_85 (and_85_out, undriven_53, comparator_68_eq, not_114_out);
  not not_114 (not_114_out, register_161_q);
  Comparator #(.width(8), .mode("unsigned")) comparator_69 (
    .a(undriven_55), .b(register_153_q), .eq(comparator_69_eq));  // open: gt, lt
  and and_86 (and_86_out, undriven_53, comparator_69_eq, not_115_out);
  not not_115 (not_115_out, register_162_q);
  Slider #(.width(3), .Direction("left_to_right"), .value('h7)) slider_49 (.out(slider_49_out));
  or or_115 (or_115_out, in_66, comparator_63_eq);
  RAM #(.addrWidth(8), .dataWidth(8), .bus("separate"), .Select("low")) ram_5 (
    .addr(counter_40_q), .din(slider_45_out), .data(ram_5_data), .str(not_111_out), .clk(clock_8_out),
    .ld(in_83));  // open: sel, clr
  RAM #(.addrWidth(8), .dataWidth(32), .bus("separate"), .Select("low")) ram_6 (.addr(counter_47_q));  // open: din, data, str, sel, clk, ld, clr
  Slider #(.width(32), .Direction("left_to_right"), .value('h0)) slider_50 (.out(slider_50_out));
  Multiplexer #(.select(1), .width(32), .disabled("Z"), .enable("false")) multiplexer_124 (
    .in0(slider_50_out), .in1(register_154_q), .out(multiplexer_124_out), .sel(comparator_66_eq));
  Register #(.width(32), .trigger("rising"), .Select("low")) register_154 (
    .D(undriven_60), .en(or_108_out), .Q(register_154_q), .clk(undriven_59));  // open: clr
  Multiplexer #(.select(1), .width(32), .disabled("Z"), .enable("false")) multiplexer_125 (
    .in0(slider_50_out), .in1(register_155_q), .out(multiplexer_125_out), .sel(comparator_67_eq));
  Register #(.width(32), .trigger("rising"), .Select("low")) register_155 (
    .D(undriven_60), .en(or_110_out), .Q(register_155_q), .clk(undriven_59));  // open: clr
  not not_116 (not_116_out, register_160_q);
  Multiplexer #(.select(1), .width(32), .disabled("Z"), .enable("false")) multiplexer_126 (
    .in0(slider_50_out), .in1(register_156_q), .out(multiplexer_126_out), .sel(comparator_68_eq));
  Register #(.width(32), .trigger("rising"), .Select("low")) register_156 (
    .D(undriven_60), .en(or_112_out), .Q(register_156_q), .clk(undriven_59));  // open: clr
  Multiplexer #(.select(1), .width(32), .disabled("Z"), .enable("false")) multiplexer_127 (
    .in0(slider_50_out), .in1(register_157_q), .out(multiplexer_127_out), .sel(comparator_69_eq));
  Register #(.width(32), .trigger("rising"), .Select("low")) register_157 (
    .D(undriven_60), .en(or_114_out), .Q(register_157_q), .clk(undriven_59));  // open: clr
  Multiplexer #(.select(1), .width(3), .disabled("Z"), .enable("false")) multiplexer_128 (
    .in0(counter_48_q[2:0]), .in1(slider_49_out), .out(multiplexer_128_out), .sel(undriven_58));
  Slider #(.width(2), .Direction("left_to_right"), .value('h3)) slider_51 ();  // open: out
  Slider #(.width(3), .Direction("left_to_right"), .value('h7)) slider_52 (.out(slider_52_out));
  Multiplexer #(.select(1), .width(32), .disabled("Z"), .enable("false")) multiplexer_129 (
    .in0(rom_23_data), .in1({register_179_q, register_178_q, multiplexer_137_out_2, register_177_q}),
    .out(multiplexer_129_out), .sel(or_133_out));
  // Probe on ram_5_data
  Register #(.width(8), .trigger("rising"), .Select("low")) register_158 (
    .D(ram_5_data), .Q(register_158_q), .clk(clock_8_out));  // open: en, clr
  Counter #(.width(8), .max('hff), .ongoal("wrap"), .trigger("rising"), .behavior("new")) counter_49 (
    .load(or_129_out), .D(multiplexer_123_out), .count(not_126_out), .Q(counter_49_q), .clk(clock_9_out));  // open: carry, clr, preset, down
  Decoder #(.select(3), .tristate("false"), .disabled("Z"), .enable("false")) decoder_20 (
    .out4(decoder_20_out4), .out5(decoder_20_out5), .out6(decoder_20_out6), .out7(decoder_20_out7),
    .sel(multiplexer_142_out));  // open: out0, out1, out2, out3
  and and_87 (and_87_out, undriven_54, comparator_66_eq);
  not not_117 (not_117_out, and_87_out);
  and and_88 (and_88_out, undriven_54, comparator_67_eq);
  not not_118 (not_118_out, and_88_out);
  and and_89 (and_89_out, undriven_54, comparator_68_eq);
  not not_119 (not_119_out, and_89_out);
  and and_90 (and_90_out, undriven_54, comparator_69_eq);
  not not_120 (not_120_out, and_90_out);
  Decoder #(.select(3), .tristate("false"), .disabled("Z"), .enable("false")) decoder_21 (
    .out0(decoder_21_out0), .out1(decoder_21_out1), .out2(decoder_21_out2), .out3(decoder_21_out3),
    .sel(multiplexer_128_out));  // open: out4, out5, out6, out7
  Multiplexer #(.select(1), .width(3), .disabled("Z"), .enable("false")) multiplexer_130 (
    .in0(counter_45_q[2:0]), .in1(slider_52_out), .out(multiplexer_130_out), .sel(not_112_out));
  // Probe on register_158_q
  Demultiplexer #(.select(3), .width(8), .tristate("false"), .disabled("Z"), .enable("false")) demultiplexer_17 (
    .out0(demultiplexer_17_out0), .out1(demultiplexer_17_out1), .out2(demultiplexer_17_out2),
    .out3(demultiplexer_17_out3), .out4(demultiplexer_17_out4), .out5(demultiplexer_17_out5),
    .out6(demultiplexer_17_out6), .out7(demultiplexer_17_out7), .in(counter_49_q), .sel(demultiplexer_18_out1));
  or or_116 (or_116_out, and_87_out, or_108_out);
  or or_117 (or_117_out, and_88_out, or_110_out);
  or or_118 (or_118_out, and_89_out, or_112_out);
  or or_119 (or_119_out, and_90_out, or_114_out);
  Counter #(.width(8), .max('hff), .ongoal("wrap"), .trigger("rising"), .behavior("new")) counter_50 (
    .count(undriven_62), .Q(counter_50_q), .clk(undriven_63));  // open: load, D, carry, clr, preset, down
  Slider #(.width(8), .Direction("left_to_right"), .value('h3)) slider_53 (.out(slider_53_out));
  Multiplexer #(.select(1), .width(3), .disabled("Z"), .enable("false")) multiplexer_131 (
    .in0(multiplexer_130_out), .in1(counter_55_q), .out(multiplexer_131_out), .sel(or_133_out));
  Slider #(.width(1), .Direction("left_to_right"), .value('h0)) slider_54 (.out(slider_54_out));
  Register #(.width(1), .trigger("rising"), .Select("low")) register_159 (
    .D(not_117_out), .en(or_116_out), .Q(register_159_q), .clk(undriven_59));  // open: clr
  Register #(.width(1), .trigger("rising"), .Select("low")) register_160 (
    .D(not_118_out), .en(or_117_out), .Q(register_160_q), .clk(undriven_59));  // open: clr
  Register #(.width(1), .trigger("rising"), .Select("low")) register_161 (
    .D(not_119_out), .en(or_118_out), .Q(register_161_q), .clk(undriven_59));  // open: clr
  Register #(.width(1), .trigger("rising"), .Select("low")) register_162 (
    .D(not_120_out), .en(or_119_out), .Q(register_162_q), .clk(undriven_59));  // open: clr
  Register #(.width(32), .trigger("rising"), .Select("low")) register_163 (
    .D(undriven_65), .en(decoder_21_out3), .Q(register_163_q), .clk(undriven_61));  // open: clr
  Comparator #(.width(8), .mode("unsigned")) comparator_70 (
    .a(counter_50_q), .b(slider_53_out), .gt(comparator_70_gt));  // open: eq, lt
  Decoder #(.select(3), .tristate("false"), .disabled("Z"), .enable("false")) decoder_22 (
    .out0(decoder_22_out0), .out1(decoder_22_out1), .out2(decoder_22_out2), .out3(decoder_22_out3),
    .out4(decoder_22_out4), .out5(decoder_22_out5), .out6(decoder_22_out6), .sel(multiplexer_131_out));  // open: out7
  Decoder #(.select(3), .tristate("false"), .disabled("Z"), .enable("false")) decoder_23 (
    .out0(decoder_23_out0), .out1(decoder_23_out1), .out2(decoder_23_out2), .out3(decoder_23_out3),
    .out4(decoder_23_out4), .out5(decoder_23_out5), .out6(decoder_23_out6), .out7(decoder_23_out7),
    .sel(demultiplexer_18_out1));
  Multiplexer #(.select(3), .width(1), .disabled("Z"), .enable("false")) multiplexer_132 (
    .in0(slider_54_out), .in1(slider_54_out), .in2(slider_54_out), .in3(slider_54_out), .in4(register_162_q),
    .in5(register_161_q), .in6(register_160_q), .in7(register_159_q), .out(multiplexer_132_out),
    .sel(multiplexer_147_out));
  Register #(.width(32), .trigger("rising"), .Select("low")) register_164 (
    .D(undriven_65), .en(decoder_21_out2), .Q(register_164_q), .clk(undriven_61));  // open: clr
  Register #(.width(32), .trigger("rising"), .Select("low")) register_165 (
    .D(multiplexer_129_out), .en(decoder_22_out6), .Q(register_165_q), .clk(clock_7_out));  // open: clr
  Register #(.width(32), .trigger("rising"), .Select("low")) register_166 (
    .D(multiplexer_129_out), .en(decoder_22_out5), .Q(register_166_q), .clk(clock_7_out));  // open: clr
  Slider #(.width(32), .Direction("left_to_right"), .value('h0)) slider_55 (.out(slider_55_out));
  Register #(.width(32), .trigger("rising"), .Select("low")) register_167 (
    .D(undriven_65), .en(decoder_21_out0), .Q(register_167_q), .clk(undriven_61));  // open: clr
  Register #(.width(32), .trigger("rising"), .Select("low")) register_168 (
    .D(undriven_65), .en(decoder_21_out1), .Q(register_168_q), .clk(undriven_61));  // open: clr
  Counter #(.width(8), .max('hff), .ongoal("wrap"), .trigger("rising"), .behavior("new")) counter_51 (
    .load(comparator_71_eq), .D(counter_50_q), .count(undriven_64), .Q(counter_51_q), .clk(undriven_61));  // open: carry, clr, preset, down
  Counter #(.width(8), .max('hff), .ongoal("wrap"), .trigger("rising"), .behavior("new")) counter_52 (
    .Q(counter_52_q), .clk(undriven_61), .down(undriven_66));  // open: load, D, count, carry, clr, preset
  Register #(.width(32), .trigger("rising"), .Select("low")) register_169 (
    .D(multiplexer_129_out), .en(decoder_22_out4), .Q(register_169_q), .clk(clock_7_out));  // open: clr
  or or_120 (or_120_out, in_102, register_147_q);
  Multiplexer #(.select(2), .width(32), .disabled("Z"), .enable("false")) multiplexer_133 (
    .in0(register_167_q), .in1(register_168_q), .in2(register_164_q), .in3(register_163_q),
    .out({multiplexer_133_out_8, multiplexer_133_out_7, multiplexer_133_out_3[19], multiplexer_133_out_6, multiplexer_133_out_3[15], multiplexer_133_out_5, multiplexer_133_out_3[11], multiplexer_133_out_4, multiplexer_133_out_3[7], multiplexer_133_out_2, multiplexer_133_out}),
    .sel(counter_51_q[1:0]));
  Comparator #(.width(2), .mode("unsigned")) comparator_71 (
    .a(counter_51_q[1:0]), .b(counter_52_q[1:0]), .eq(comparator_71_eq));  // open: gt, lt
  Comparator #(.width(8), .mode("unsigned")) comparator_72 (
    .a(counter_52_q), .b(slider_56_out), .gt(comparator_72_gt));  // open: eq, lt
  Slider #(.width(8), .Direction("left_to_right"), .value('h3)) slider_56 (.out(slider_56_out));
  or or_121 (or_121_out, or_124_out, \开关启动模拟加入新进程 );
  or or_122 (or_122_out, comparator_73_gt, comparator_73_eq);
  Comparator #(.width(8), .mode("unsigned")) comparator_73 (
    .a(counter_41_q), .b(counter_42_q), .gt(comparator_73_gt), .eq(comparator_73_eq));  // open: lt
  or or_123 (or_123_out, comparator_74_gt, comparator_74_eq);
  Comparator #(.width(8), .mode("unsigned")) comparator_74 (
    .a(counter_43_q), .b(counter_44_q), .gt(comparator_74_gt), .eq(comparator_74_eq));  // open: lt
  Register #(.width(32), .trigger("rising"), .Select("low")) register_170 (
    .D(multiplexer_129_out), .en(decoder_22_out3), .Q(register_170_q), .clk(clock_7_out));  // open: clr
  Register #(.width(32), .trigger("rising"), .Select("low")) register_171 (
    .D(multiplexer_129_out), .en(decoder_22_out2), .Q(register_171_q), .clk(clock_7_out));  // open: clr
  or or_124 (or_124_out, comparator_80_eq, or_115_out);
  Register #(.width(1), .trigger("rising"), .Select("low")) register_172 (
    .D(or_121_out), .Q(register_172_q), .clk(clock_7_out));  // open: en, clr
  Multiplexer #(.select(1), .width(8), .disabled("Z"), .enable("false")) multiplexer_134 (
    .in0(counter_41_q), .in1(counter_42_q), .out(multiplexer_134_out), .sel(not_121_out));
  not not_121 (not_121_out, or_122_out);
  or or_125 (or_125_out, comparator_75_gt, comparator_75_eq);
  not not_122 (not_122_out, or_125_out);
  Comparator #(.width(8), .mode("unsigned")) comparator_75 (
    .a(multiplexer_134_out), .b(multiplexer_135_out), .gt(comparator_75_gt), .eq(comparator_75_eq));  // open: lt
  not not_123 (not_123_out, or_123_out);
  Multiplexer #(.select(1), .width(8), .disabled("Z"), .enable("false")) multiplexer_135 (
    .in0(counter_43_q), .in1(counter_44_q), .out(multiplexer_135_out), .sel(not_123_out));
  Register #(.width(32), .trigger("rising"), .Select("low")) register_173 (
    .D(multiplexer_129_out), .en(decoder_22_out1), .Q(register_173_q), .clk(clock_7_out));  // open: clr
  Counter #(.width(8), .max('hff), .ongoal("wrap"), .trigger("rising"), .behavior("new")) counter_53 (
    .load(or_126_out), .D(counter_46_q), .count(or_124_out), .Q(counter_53_q), .clk(clock_7_out));  // open: carry, clr, preset, down
  Counter #(.width(1), .max('h1), .ongoal("wrap"), .trigger("rising"), .behavior("new")) counter_54 (
    .load(in_67), .D(in_68), .count(in_69), .clk(clock_7_out));  // open: Q, carry, clr, preset, down
  Multiplexer #(.select(1), .width(8), .disabled("Z"), .enable("false")) multiplexer_136 (
    .in0(multiplexer_134_out), .in1(multiplexer_135_out), .out(multiplexer_136_out), .sel(not_122_out));
  Register #(.width(32), .trigger("rising"), .Select("low")) register_174 (
    .D(multiplexer_129_out), .en(decoder_22_out0), .Q(register_174_q), .clk(clock_7_out));  // open: clr
  Counter #(.width(8), .max('hff), .ongoal("wrap"), .trigger("rising"), .behavior("new")) counter_55 (
    .load(or_126_out), .D(counter_46_q), .count(or_124_out), .Q({counter_55_q_2, counter_55_q}),
    .clk(clock_7_out));  // open: carry, clr, preset, down
  Priority_Encoder #(.select(3), .disabled("Z")) priority_encoder_7 (
    .in0(in_95), .in1(in_96), .in2(in_97), .in3(in_98), .in4(in_100), .in5(in_101), .in6(in_103),
    .in7(or_120_out), .out(priority_encoder_7_out), .gs(priority_encoder_7_gs));  // open: en_out, en_in
  Slider #(.width(3), .Direction("left_to_right"), .value('h0)) slider_57 (.out(slider_57_out));
  Comparator #(.width(8), .mode("unsigned")) comparator_76 (
    .a(multiplexer_136_out), .b(counter_41_q), .eq(comparator_76_eq));  // open: gt, lt
  Comparator #(.width(8), .mode("unsigned")) comparator_77 (
    .a(multiplexer_136_out), .b(counter_42_q), .eq(comparator_77_eq));  // open: gt, lt
  Comparator #(.width(8), .mode("unsigned")) comparator_78 (
    .a(multiplexer_136_out), .b(counter_43_q), .eq(comparator_78_eq));  // open: gt, lt
  Comparator #(.width(8), .mode("unsigned")) comparator_79 (
    .a(multiplexer_136_out), .b(counter_44_q), .eq(comparator_79_eq));  // open: gt, lt
  Multiplexer #(.select(3), .width(32), .disabled("Z"), .enable("false")) multiplexer_137 (
    .in0(register_174_q), .in1(register_173_q), .in2(register_171_q), .in3(register_170_q),
    .in4(register_169_q), .in5(register_166_q), .in6(register_165_q), .in7(slider_55_out),
    .out({multiplexer_137_out[31:16], multiplexer_137_out_2, multiplexer_137_out[7:0]}), .sel(counter_55_q));
  Comparator #(.width(8), .mode("unsigned")) comparator_80 (
    .a(counter_45_q), .b({counter_55_q_2, counter_55_q}), .eq(comparator_80_eq), .lt(comparator_80_lt));  // open: gt
  ROM #(.addrWidth(8), .dataWidth(32), .Select("low")) rom_24 (.addr(demultiplexer_17_out0), .data(rom_24_data));
  ROM #(.addrWidth(8), .dataWidth(32), .Select("low")) rom_25 (.addr(demultiplexer_17_out1), .data(rom_25_data));
  ROM #(.addrWidth(8), .dataWidth(32), .Select("low")) rom_26 (.addr(demultiplexer_17_out2), .data(rom_26_data));
  ROM #(.addrWidth(8), .dataWidth(32), .Select("low")) rom_27 (.addr(demultiplexer_17_out3), .data(rom_27_data));
  ROM #(.addrWidth(8), .dataWidth(32), .Select("low")) rom_28 (.addr(demultiplexer_17_out4), .data(rom_28_data));
  ROM #(.addrWidth(8), .dataWidth(32), .Select("low")) rom_29 (.addr(demultiplexer_17_out5), .data(rom_29_data));
  ROM #(.addrWidth(8), .dataWidth(32), .Select("low")) rom_30 (.addr(demultiplexer_17_out6), .data(rom_30_data));
  ROM #(.addrWidth(8), .dataWidth(32), .Select("low")) rom_31 (.addr(demultiplexer_17_out7), .data(rom_31_data));
  Slider #(.width(3), .Direction("left_to_right"), .value('h0)) slider_58 (.out(slider_58_out));
  Multiplexer #(.select(1), .width(3), .disabled("Z"), .enable("false")) multiplexer_138 (
    .in0(slider_57_out), .in1(priority_encoder_7_out), .out(multiplexer_138_out), .sel(or_128_out));
  or or_126 (or_126_out, comparator_80_eq, comparator_80_lt);
  Multiplexer #(.select(1), .width(3), .disabled("Z"), .enable("false")) multiplexer_139 (
    .in0(slider_58_out), .in1(multiplexer_138_out), .out(multiplexer_139_out), .sel(not_129_out));
  Clock #(.highDuration(1), .lowDuration(1)) clock_9 (.out(clock_9_out));
  Comparator #(.width(8), .mode("unsigned")) comparator_81 (
    .a(undriven_67), .b(undriven_68), .gt(comparator_81_gt), .eq(comparator_81_eq));  // open: lt
  or or_127 (or_127_out, comparator_81_gt, comparator_81_eq);
  not not_124 (not_124_out, or_127_out);
  not not_125 (not_125_out, in_12);
  Slider #(.width(8), .Direction("left_to_right"), .value('hff)) slider_59 (.out(slider_59_out));
  Slider #(.width(8), .Direction("left_to_right"), .value('hb5)) slider_60 (.out(slider_60_out));
  Slider #(.width(8), .Direction("left_to_right"), .value('h0)) slider_61 (.out(slider_61_out));
  Multiplexer #(.select(3), .width(32), .disabled("Z"), .enable("false")) multiplexer_140 (
    .in0(rom_24_data), .in1(rom_25_data), .in2(rom_26_data), .in3(rom_27_data), .in4(rom_28_data),
    .in5(rom_29_data), .in6(rom_30_data), .in7(rom_31_data),
    .out({multiplexer_140_out_8, multiplexer_140_out_7, multiplexer_140_out_6, multiplexer_140_out_5, multiplexer_140_out_4, multiplexer_140_out_3, multiplexer_140_out_2, multiplexer_140_out}),
    .sel(demultiplexer_18_out1));
  Register #(.width(3), .trigger("rising"), .Select("low")) register_175 (
    .D(multiplexer_139_out), .en(or_128_out), .Q(register_175_q), .clk(clock_9_out));  // open: clr
  and and_91 (and_91_out, not_129_out, priority_encoder_7_gs);
  Multiplexer #(.select(1), .width(8), .disabled("Z"), .enable("false")) multiplexer_141 (
    .in0(undriven_67), .in1(undriven_68), .sel(not_124_out));  // open: out
  Priority_Encoder #(.select(3), .disabled("Z")) priority_encoder_8 (
    .in0(not_125_out), .in1(not_125_out), .in2(not_125_out), .in3(not_125_out), .in4(comparator_79_eq),
    .in5(comparator_78_eq), .in6(comparator_77_eq), .in7(comparator_76_eq), .out(priority_encoder_8_out));  // open: gs, en_out, en_in
  Slider #(.width(3), .Direction("left_to_right"), .value('h0)) slider_62 (.out(slider_62_out));
  Demultiplexer #(.select(1), .width(3), .tristate("false"), .disabled("Z"), .enable("false")) demultiplexer_18 (
    .out1(demultiplexer_18_out1), .in(register_175_q), .sel(not_126_out));  // open: out0
  Register #(.width(1), .trigger("rising"), .Select("low")) register_176 (
    .D(and_91_out), .en(or_128_out), .Q(register_176_q), .clk(clock_9_out));  // open: clr
  not not_126 (not_126_out, not_127_out);
  not not_127 (not_127_out, register_176_q);
  or or_128 (or_128_out, not_127_out, or_129_out);
  Slider #(.width(3), .Direction("left_to_right"), .value('h0)) slider_63 (.out(slider_63_out));
  Priority_Encoder #(.select(3), .disabled("Z")) priority_encoder_9 (
    .in0(in_8), .in1(in_8), .in2(in_8), .in3(in_8), .in4(comparator_69_eq), .in5(comparator_68_eq),
    .in6(comparator_67_eq), .in7(comparator_66_eq), .out(priority_encoder_9_out), .gs(priority_encoder_9_gs));  // open: en_out, en_in
  Multiplexer #(.select(1), .width(3), .disabled("Z"), .enable("false")) multiplexer_142 (
    .in0(priority_encoder_8_out), .in1(slider_62_out), .out(multiplexer_142_out), .sel(priority_encoder_9_gs));
  Slider #(.width(1), .Direction("left_to_right"), .value('h0)) slider_64 (.out(slider_64_out));
  Multiplexer #(.select(1), .width(1), .disabled("Z"), .enable("false")) multiplexer_143 (
    .in0(slider_64_out), .in1(priority_encoder_9_gs), .out(multiplexer_143_out), .sel(multiplexer_132_out));
  not not_128 (not_128_out, multiplexer_143_out);
  Multiplexer #(.select(1), .width(8), .disabled("Z"), .enable("false")) multiplexer_144 (
    .in0(multiplexer_137_out[7:0]), .in1(slider_59_out), .out(multiplexer_144_out), .sel(in_61));
  Multiplexer #(.select(1), .width(8), .disabled("Z"), .enable("false")) multiplexer_145 (
    .in0(multiplexer_137_out[23:16]), .in1(slider_60_out), .out(multiplexer_145_out), .sel(in_62));
  Multiplexer #(.select(1), .width(8), .disabled("Z"), .enable("false")) multiplexer_146 (
    .in0(multiplexer_137_out[31:24]), .in1(slider_61_out), .out(multiplexer_146_out), .sel(in_64));
  or or_129 (or_129_out, in_99, in_122);
  Multiplexer #(.select(1), .width(3), .disabled("Z"), .enable("false")) multiplexer_147 (
    .in0(slider_63_out), .in1(priority_encoder_9_out), .out(multiplexer_147_out), .sel(priority_encoder_9_gs));
  Multiplexer #(.select(3), .width(32), .disabled("Z"), .enable("false")) multiplexer_148 (
    .in4(multiplexer_127_out), .in5(multiplexer_126_out), .in6(multiplexer_125_out),
    .in7(multiplexer_124_out), .out(multiplexer_148_out), .sel(multiplexer_147_out));  // open: in0, in1, in2, in3
  or or_130 (or_130_out, register_172_q, in_61);
  or or_131 (or_131_out, register_172_q, in_62);
  or or_132 (or_132_out, register_172_q, in_64);
  not not_129 (not_129_out, or_129_out);
  Register #(.width(8), .trigger("rising"), .Select("low")) register_177 (
    .D(multiplexer_144_out), .en(or_130_out), .Q(register_177_q), .clk(clock_7_out));  // open: clr
  Register #(.width(8), .trigger("rising"), .Select("low")) register_178 (
    .D(multiplexer_145_out), .en(or_131_out), .Q(register_178_q), .clk(clock_7_out));  // open: clr
  Register #(.width(8), .trigger("rising"), .Select("low")) register_179 (
    .D(multiplexer_146_out), .en(or_132_out), .Q(register_179_q), .clk(clock_7_out));  // open: clr
  Register #(.width(32), .trigger("rising"), .Select("low")) register_180 (
    .D(undriven_69), .Q(register_180_q));  // open: en, clk, clr
  Slider #(.width(4), .Direction("left_to_right"), .value('h1)) slider_65 (.out(slider_65_out));
  Comparator #(.width(4), .mode("unsigned")) comparator_82 (
    .a(multiplexer_140_out_4), .b(slider_65_out), .eq(comparator_82_eq));  // open: gt, lt
  Demultiplexer #(.select(1), .width(32), .tristate("false"), .disabled("Z"), .enable("false")) demultiplexer_19 (
    .out0(demultiplexer_19_out0), .out1(demultiplexer_19_out1),
    .in({multiplexer_140_out_8, multiplexer_140_out_7, multiplexer_140_out_6, multiplexer_140_out_5, multiplexer_140_out_4, multiplexer_140_out_3, multiplexer_140_out_2, multiplexer_140_out}),
    .sel(comparator_82_eq));
  buf or_133 (or_133_out, in_85);  // OR_Gate
  Counter #(.width(8), .max('hff), .ongoal("wrap"), .trigger("rising"), .behavior("new")) counter_56 (
    .load(undriven_70), .D(multiplexer_149_out), .count(or_135_out), .Q(counter_56_q), .clk(undriven_71));  // open: carry, clr, preset, down
  Demultiplexer #(.select(3), .width(8), .tristate("false"), .disabled("Z"), .enable("false")) demultiplexer_20 (
    .out0(demultiplexer_20_out0), .out1(demultiplexer_20_out1), .out2(demultiplexer_20_out2),
    .out3(demultiplexer_20_out3), .out4(demultiplexer_20_out4), .out5(demultiplexer_20_out5),
    .out6(demultiplexer_20_out6), .out7(demultiplexer_20_out7), .in(undriven_72), .sel(undriven_73));
  Decoder #(.select(3), .tristate("false"), .disabled("Z"), .enable("false")) decoder_24 (
    .out0(decoder_24_out0), .out1(decoder_24_out1), .out2(decoder_24_out2), .out3(decoder_24_out3),
    .out4(decoder_24_out4), .out5(decoder_24_out5), .out6(decoder_24_out6), .out7(decoder_24_out7),
    .sel(demultiplexer_21_out1));
  Register #(.width(8), .trigger("rising"), .Select("low")) register_181 (
    .D(demultiplexer_20_out6), .en(decoder_24_out6), .Q(register_181_q));  // open: clk, clr
  Register #(.width(8), .trigger("rising"), .Select("low")) register_182 (
    .D(demultiplexer_20_out7), .en(decoder_24_out7), .Q(register_182_q));  // open: clk, clr
  Register #(.width(3), .trigger("rising"), .Select("low")) register_183 (
    .D(priority_encoder_10_out), .en(or_135_out), .Q(register_183_q));  // open: clk, clr
  Priority_Encoder #(.select(3), .disabled("Z")) priority_encoder_10 (
    .in0(in_104), .in1(in_105), .in2(in_106), .in3(in_107), .in4(in_108), .in5(in_109), .in6(in_110),
    .in7(in_111), .out(priority_encoder_10_out), .gs(priority_encoder_10_gs));  // open: en_out, en_in
  ROM #(.addrWidth(8), .dataWidth(32), .Select("low")) rom_32 (.addr(counter_56_q), .data(rom_32_data));
  Slider #(.width(8), .Direction("left_to_right"), .value('h0)) slider_66 (.out(slider_66_out));
  Slider #(.width(8), .Direction("left_to_right"), .value('h2b)) slider_67 (.out(slider_67_out));
  Slider #(.width(8), .Direction("left_to_right"), .value('h5c)) slider_68 (.out(slider_68_out));
  Slider #(.width(8), .Direction("left_to_right"), .value('h6e)) slider_69 (.out(slider_69_out));
  Slider #(.width(8), .Direction("left_to_right"), .value('h8c)) slider_70 (.out(slider_70_out));
  Slider #(.width(8), .Direction("left_to_right"), .value('hb0)) slider_71 (.out(slider_71_out));
  Demultiplexer #(.select(1), .width(3), .tristate("false"), .disabled("Z"), .enable("false")) demultiplexer_21 (
    .out0(demultiplexer_21_out0), .out1(demultiplexer_21_out1), .in(register_183_q),
    .sel(priority_encoder_10_gs));
  buf or_134 (or_134_out, priority_encoder_10_gs);  // OR_Gate
  Multiplexer #(.select(3), .width(8), .disabled("Z"), .enable("false")) multiplexer_149 (
    .in0(slider_66_out), .in1(slider_67_out), .in2(slider_68_out), .in3(slider_69_out), .in4(slider_70_out),
    .in5(slider_71_out), .in6(register_181_q), .in7(register_182_q), .out(multiplexer_149_out),
    .sel(demultiplexer_21_out1));
  or or_135 (or_135_out, undriven_74, not_130_out);
  Register #(.width(1), .trigger("rising"), .Select("low")) register_184 (
    .D(or_134_out), .en(or_135_out), .Q(register_184_q));  // open: clk, clr
  not not_130 (not_130_out, register_184_q);
  Demultiplexer #(.select(1), .width(32), .tristate("false"), .disabled("Z"), .enable("false")) demultiplexer_22 (
    .out0(demultiplexer_22_out0), .out1(demultiplexer_22_out1), .in(rom_32_data), .sel(rom_32_data[12]));
  Slider #(.width(8), .Direction("left_to_right"), .value('h0)) slider_72 (.out(slider_72_out));
  Multiplexer #(.select(1), .width(8), .disabled("Z"), .enable("false")) multiplexer_150 (
    .in0(multiplexer_152_out), .in1(slider_72_out), .out(multiplexer_150_out), .sel(or_139_out));
  Counter #(.width(8), .max('hff), .ongoal("wrap"), .trigger("rising"), .behavior("new")) counter_57 (
    .load(or_138_out), .D(multiplexer_150_out), .count(not_132_out), .Q(counter_57_q), .clk(clock_10_out));  // open: carry, clr, preset, down
  Demultiplexer #(.select(3), .width(8), .tristate("false"), .disabled("Z"), .enable("false")) demultiplexer_23 (
    .out0(demultiplexer_23_out0), .out1(demultiplexer_23_out1), .out2(demultiplexer_23_out2),
    .out3(demultiplexer_23_out3), .out4(demultiplexer_23_out4), .out5(demultiplexer_23_out5),
    .out6(demultiplexer_23_out6), .out7(demultiplexer_23_out7), .in(undriven_75), .sel(undriven_76));
  Decoder #(.select(3), .tristate("false"), .disabled("Z"), .enable("false")) decoder_25 (
    .out0(decoder_25_out0), .out1(decoder_25_out1), .out2(decoder_25_out2), .out3(decoder_25_out3),
    .out4(decoder_25_out4), .out5(decoder_25_out5), .out6(decoder_25_out6), .out7(decoder_25_out7),
    .sel(undriven_77));
  or or_136 (or_136_out, in_93, register_147_q);
  Priority_Encoder #(.select(3), .disabled("Z")) priority_encoder_11 (
    .in0(in_86), .in1(in_87), .in2(in_88), .in3(in_89), .in4(in_91), .in5(in_92), .in6(in_94),
    .in7(or_136_out), .out(priority_encoder_11_out), .gs(priority_encoder_11_gs));  // open: en_out, en_in
  Slider #(.width(3), .Direction("left_to_right"), .value('h0)) slider_73 (.out(slider_73_out));
  ROM #(.addrWidth(8), .dataWidth(32), .Select("low")) rom_33 (.addr(counter_57_q), .data(rom_33_data));
  Slider #(.width(8), .Direction("left_to_right"), .value('h0)) slider_74 (.out(slider_74_out));
  Slider #(.width(8), .Direction("left_to_right"), .value('h40)) slider_75 (.out(slider_75_out));
  Slider #(.width(8), .Direction("left_to_right"), .value('h7a)) slider_76 (.out(slider_76_out));
  Slider #(.width(8), .Direction("left_to_right"), .value('ha1)) slider_77 (.out(slider_77_out));
  Slider #(.width(8), .Direction("left_to_right"), .value('hc9)) slider_78 (.out(slider_78_out));
  Slider #(.width(8), .Direction("left_to_right"), .value('hd6)) slider_79 (.out(slider_79_out));
  Register #(.width(8), .trigger("rising"), .Select("low")) register_185 (
    .D(demultiplexer_23_out6), .en(decoder_25_out6), .Q(register_185_q));  // open: clk, clr
  Register #(.width(8), .trigger("rising"), .Select("low")) register_186 (
    .D(demultiplexer_23_out7), .en(decoder_25_out7), .Q(register_186_q));  // open: clk, clr
  Slider #(.width(3), .Direction("left_to_right"), .value('h0)) slider_80 (.out(slider_80_out));
  Multiplexer #(.select(1), .width(3), .disabled("Z"), .enable("false")) multiplexer_151 (
    .in0(slider_73_out), .in1(priority_encoder_11_out), .out(multiplexer_151_out), .sel(or_137_out));
  Multiplexer #(.select(3), .width(8), .disabled("Z"), .enable("false")) multiplexer_152 (
    .in0(slider_74_out), .in1(slider_75_out), .in2(slider_76_out), .in3(slider_77_out), .in4(slider_78_out),
    .in5(slider_79_out), .in6(register_185_q), .in7(register_186_q), .out(multiplexer_152_out),
    .sel(demultiplexer_24_out1));
  Multiplexer #(.select(1), .width(3), .disabled("Z"), .enable("false")) multiplexer_153 (
    .in0(slider_80_out), .in1(multiplexer_151_out), .out(multiplexer_153_out), .sel(not_133_out));
  Register #(.width(3), .trigger("rising"), .Select("low")) register_187 (
    .D(multiplexer_153_out), .en(or_137_out), .Q(register_187_q), .clk(clock_10_out));  // open: clr
  Clock #(.highDuration(1), .lowDuration(1)) clock_10 (.out(clock_10_out));
  and and_92 (and_92_out, not_133_out, priority_encoder_11_gs);
  Register #(.width(1), .trigger("rising"), .Select("low")) register_188 (
    .D(and_92_out), .en(or_137_out), .Q(register_188_q), .clk(clock_10_out));  // open: clr
  or or_137 (or_137_out, not_131_out, or_139_out);
  Demultiplexer #(.select(1), .width(3), .tristate("false"), .disabled("Z"), .enable("false")) demultiplexer_24 (
    .out1(demultiplexer_24_out1), .in(register_187_q), .sel(not_132_out));  // open: out0
  not not_131 (not_131_out, register_188_q);
  not not_132 (not_132_out, not_131_out);
  or or_138 (or_138_out, priority_encoder_11_gs, or_139_out);
  or or_139 (or_139_out, in_90, in_112);
  not not_133 (not_133_out, or_139_out);
  or or_140 (or_140_out, in_120, undriven_78);
  Comparator #(.width(4), .mode("unsigned")) comparator_83 (
    .a(rom_33_data[15:12]), .b(slider_81_out), .eq(comparator_83_eq));  // open: gt, lt
  Slider #(.width(4), .Direction("left_to_right"), .value('h1)) slider_81 (.out(slider_81_out));
  Demultiplexer #(.select(1), .width(32), .tristate("false"), .disabled("Z"), .enable("false")) demultiplexer_25 (
    .out0(demultiplexer_25_out0), .out1(demultiplexer_25_out1), .in(rom_33_data), .sel(comparator_83_eq));
  Slider #(.width(3), .Direction("left_to_right"), .value('h0)) slider_82 (.out(slider_82_out));
  Priority_Encoder #(.select(3), .disabled("Z")) priority_encoder_12 (
    .in0(in_113), .in1(in_114), .in2(in_115), .in3(in_116), .in4(in_118), .in5(in_119), .in6(in_121),
    .in7(or_140_out), .out(priority_encoder_12_out), .gs(priority_encoder_12_gs));  // open: en_out, en_in
  Slider #(.width(3), .Direction("left_to_right"), .value('h0)) slider_83 (.out(slider_83_out));
  Multiplexer #(.select(1), .width(3), .disabled("Z"), .enable("false")) multiplexer_154 (
    .in0(slider_83_out), .in1(multiplexer_155_out), .out(multiplexer_154_out), .sel(not_135_out));
  Multiplexer #(.select(1), .width(3), .disabled("Z"), .enable("false")) multiplexer_155 (
    .in0(slider_82_out), .in1(priority_encoder_12_out), .out(multiplexer_155_out),
    .sel(priority_encoder_12_gs));
  Register #(.width(3), .trigger("rising"), .Select("low")) register_189 (
    .D(multiplexer_154_out), .en(priority_encoder_12_gs), .Q(register_189_q), .clk(clock_11_out));  // open: clr
  and and_93 (and_93_out, not_135_out, priority_encoder_12_gs);
  Clock #(.highDuration(1), .lowDuration(1)) clock_11 (.out(clock_11_out));
  Register #(.width(1), .trigger("rising"), .Select("low")) register_190 (
    .D(and_93_out), .en(or_141_out), .Q(register_190_q), .clk(clock_11_out));  // open: clr
  or or_141 (or_141_out, not_134_out, or_142_out);
  Demultiplexer #(.select(1), .width(3), .tristate("false"), .disabled("Z"), .enable("false")) demultiplexer_26 (
    .out1(demultiplexer_26_out1), .in(register_189_q), .sel(register_190_q));  // open: out0
  not not_134 (not_134_out, register_190_q);
  not not_135 (not_135_out, or_142_out);
  or or_142 (or_142_out, in_117, in_123);
  or or_143 (or_143_out, priority_encoder_12_gs, or_142_out);
  // Pins of 1 and 4 bits meet at rom_32_data[15:12]
  // Pins of 3 and 8 bits meet at counter_28_q
  // also tied to GND on the sheet: {slider_14_out[1], slider_14_out[2]}
  // also tied to VCC on the sheet: slider_14_out[0]

  // Notes on the sheet:
  //   contents of rom_1 (hex, n*v repeats v):
  //   0 1 2 3 4 5 6 7 8 9 a b c d e f 9*0 ff 0 ff 0 ff 0 ff 16*0 4*ff 4*1 8*0 1 1 ff ff 1 1 ff ff
  //   contents of rom_2 (hex, n*v repeats v):
  //   16*0 8*1 8*0 8*1 10*0 1 0 0 1 4*0 1 0 0 1 26*0 8*1
  //   contents of rom_3 (hex, n*v repeats v):
  //   8*0 8*1 8*0 8*1
  //   contents of rom_4 (hex, n*v repeats v):
  //   32*0 8*1
  //   contents of rom_5 (hex, n*v repeats v):
  //   88*0 1 0 1 0 1 0 1
  //   contents of rom_6 (hex, n*v repeats v):
  //   0 1 2 3 4 5 6 7 0 1 2 3 4 5 6 7 7 6 5 4 3 2 1 0 0 1 2 3 4 5 6 7 7 6 5 4 3 2 1 11*0 1 0 0 2 4*0 3 0 0
  //   4 0 0 0 1 2 3 4 5 6 7 16*0 1 7 1 7 1 7 1 7
  //   contents of rom_7 (hex, n*v repeats v):
  //   16*0 8*1 8*0 7 6 5 4 3 2 1 0 7 6 5 4 3 2 1 0 0 7 0 0 7 4*0 7 0 0 7 11*0 1 1 2 1 1 2 0 0 6*1 0 0 4 1
  //   4 1 4 1 4 1 7
  //   contents of rom_8 (hex, n*v repeats v):
  //   16*0 7 6 5 4 3 2 1 9*0 7 6 5 4 3 2 1 49*0 2 4 2 5 4*2
  //   contents of rom_9 (hex, n*v repeats v):
  //   16*0 8*1 64*0 1 4 1 4 1 4 1 4
  //   contents of rom_10 (hex, n*v repeats v):
  //   32*0 8*7 9*1 4 2 1 4 2 0 0 1 4 2 1 4 2 10*0 1 4 2 1 4 2 0 0 1 4 2 1 4 2 10*0 5
  //   contents of rom_11 (hex, n*v repeats v):
  //   32*0 32*1 8*0 16*1 8*0 8*1
  //   0-1-7选第几个寄存器存储
  //   0-1-7选第几个指令计算
  //   0-1-7选第几个设备存储
  //   如果是2,就存储数据，接入时钟锁数据，否则寄存器数据被覆盖
  //   1是选择计算数据存储
  //   1是选择拓展寄存器存储
  //   1是选择拓展寄存器读取
  //   1是选择拓展指令运算
  //   1是选择原数据复制粘贴
  //   复制粘贴使用与门控制保护检测，引入状态寄存器控制
  //   和IR寄存器同时钟，ld灭，指令就加载完成，立即进入执行了
  //   中断向量表
  //   把出界后的数据重新导入计数器
  //   改使能非时钟，可跳转成功，使能期间有跳变
  //   利用冗余实现数据不输入，不干扰
  //   运算器
  //   不比较时候刚好相等仍然输出地址
  //   如果是2,就存储数据
  //   选择寄存器
  //   测试数据滑动检测
  //   指令边界检测部分
  //   中断时数据加载
  //   选择寄存器
  //   重整数据流，保留调试按钮遗迹
  //   选择寄存器
  //   8bit段边界寄存器
  //   PC占两个周期
  //   分频不一致可导致指令重复在n=n+a中
  //   00110000，0个寄存器，0设备，11指令，00地址
  //   0时允许接收与复位1时允许接收
  //   8bit段基地址寄存器
  //   手动控制不执行，分割时钟
  //   ld亮，不执行
  //   12218001，1个寄存器，2号设备，21指令，8号复制，1号寄存器
  //   是ff时,数据选择上寄存器，由此数据也参与控制，是条件转移
  //   预留指令选择是否回流
  //   4bit指令区
  //   4bit外设区
  //   4bit指令区
  //   4bit指令区
  //   4bit外设区
  //   4bit指令区
  //   4bit外设区
  //   4bit指令区
  //   4bit指令区
  //   4bit指令区
  //   4bit指令区
  //   4bit指令区
  //   当前指令情况：load 常数，内存-正在,jmp常数 1寄存器,add
  //   8bit指令区
  //   8bit指令区
  //   8bit指令区
  //   8bit指令区
  //   在IR反相后试出来的选择也反相
  //   反相在同时亮发现
  //   8bit指令/加载数据区
  //   8bit数据区
  //   contents of rom_12 (hex, n*v repeats v):
  //   0 10010661 10010772 10010883 10010994 10010aa5 10010bb6 10010cc7 0 10010019 1001002a 1001003b
  //   1001004c 1001005d 1001006e 1001007f 17118001 15*0 20000091 200000a2 200000b3 200000c4 200000d5
  //   200000e6 200000f7 0 20001019 2000101a 2000101b 2000101c 2000101d 2000101e 2000101f 0 30001291
  //   300013a2 300014b3 300015c4 300016d5 300017e6 300011f7 0 12218001 110000 12218002 110002 12218003
  //   110004 12218004 110006 120006 10020009 1002000a 1002000b 1003000c 10010ef1 16088001 0 12218002
  //   130000 12218003 130000 12218004 130000 12218005 130000 140000 10020009 140000 1002000a 140000
  //   1002000b 140000 1002000c 7010070 13*0 7010020 9*0 4*150000 140000 10020001 140000 10020002 140000
  //   10020003 140000 10020004 1006000f 0 0 0 10010411 10010004 15228001 0 10010421 10010014 15228001
  //   10010431 10010024 15228001 13*0 20020
  //   测试纯控制信号
  //   仅按钮启动时复位
  //   2寄存器指令，共用受控制
  //   200010xn,n=n+x
  //   30001cba,c=a+b
  //   选择寄存器
  //   流水线预留，回流数据可置最后，load指令加载数据置后，数据同计数后，解决指令译码执行顺序不同
  //   _0xx0000,xx号指令，受_控制
  //   由点复位按钮后下个时钟复位，且时间上由隔离一个寄存器，不会导致重复读取PC问题
  //   上一步比较产生ff
  //   10010661，1个寄存器，01指令，0x66，1号寄存器
  //   jmp三种参数指令情况
  //   常开
  //   _x00p???,x外部设备指令，pCPU指令。?可选0-3个寄存器，受_控制
  //   PC计数器v2,中断程序执行完自动复位
  //   1寄存器指令，一步跳转，加载数据
  //   0寄存器指令，共用受控制
  //   0寄存器指令，03000000
  //   0寄存器指令，一步写入缓冲区
  //   17118001，1个寄存器，7号设备，11指令，8号复制，1号寄存器
  //   07010099，0个寄存器，7号设备，01指令，99号地址
  //   00040001，启动内核保护，ef寄存器，模拟测试内存保护中断
  //   1bit指令加载立即数在1寄存器指令
  //   先补充电路寄存器选择，随后改复制粘贴成为指令0
  //   比较3bit和再次筛选，增加内存读取并入指令集
  //   1寄存器指令，共用受控制
  //   1寄存器指令，10001007
  //   d0ff0xxn,加载立即数xx到n号寄存器
  //   07020099，0个寄存器，7号设备，02指令，99号地址，同时ROM到RAM选线切换
  //   3寄存器指令，30001777
  //   2寄存器指令，加减，合并至设备
  //   200000xn,复制x号寄存器到n号寄存器,由于硬件对称下的切换，致使决定规定最后一位是目标寄存器
  //   禁用，可拆分27011012，2个寄存器，7号设备，01指令，1号相加，12号寄存器
  //   07030099，0个寄存器，7号设备，03指令，99号地址，中断PC按钮复位，同时ROM到RAM选线切换
  //   通过优先编码器选择jmp指令到某个地址启动中断处理程序，这样中断程序可自定义，在同一个内存里
  //   切换选线RAM，同时复位中断PC,同时启动PC跳转到内存0地址，加强版jmp复位加改寄存器设置状态
  //   只在闪烁时导入中断跳转数据，因为常开导致jmp指令地址被覆盖
  //   延时1时钟
  //   2寄存器指令，20001077
  //   大端存储是高位放低字节处。这样复制粘贴就是大端存储，逆序放置就是小端存储
  //   两个寄存器中间加非门后发现可以存1而不失效
  //   contents of rom_13 (hex, n*v repeats v):
  //   10010c09 16088009 12218001 12218002 12218003 12218004 130000 12218005 12218006 12218007 130000 700d0
  //   开发顺序-关于中断电路-先左下后右上，先合并电路压缩空间后测试时钟，先给时钟跳转后合并电路，先测试时钟延时，意外非门，再发现三状态引入，后再次延时，最后复位
  //   IR寄存器指令
  //   栈计数位置
  //   PC数据
  //   rom的数据还是大端模式，因为数据对不上才发现的
  //   测试发现电路有3个状态，觉得能行
  //   下一个PCB位置，保护模式开关，程序第一次启动等
  //   受位数限制，先测试内核保护不被访问，由两个进程再到多个进程
  //   接非门，计数器变化后中断，其他计数器可计数+1后的数据
  //   仅中断计时，而不是靠时钟启动，因为发现记录位置不对，原来是延迟情况
  //   再延时1时钟，受加载，执行各占一时种导致的屏蔽问题
  //   保护模式连带其他数据同时设置，退化到进程检测内核访问
  //   指令译码
  //   重排后，含义明确的电路，往回是反馈电路，区别与只管亮灭在一个时刻借灯
  //   多余的控制，但是不影响指令，留作标记可新增控制电路
  //   保护模式连带其他数据同时设置
  //   1是禁用，两个非门还原控制信息，与门解决同地址启动多线路情况
  //   2寄存器运算后自动回流进行屏蔽解决方案
  //   改4bit数据线，回流设备选择
  //   可作为立即数流水线兼容运算结果
  //   00040001，启动内核保护，模拟测试内存保护中断
  //   contents of rom_14 (hex, n*v repeats v):
  //   0 1 2 4 8 10 20 40 80 8*0 1 2 4 8 10 20 40 80 8*0 1 2 4 8 10 20 40 80 8*0 1 2 4 8 10 20 40 80
  //   contents of rom_15 (hex, n*v repeats v):
  //   0 1 2 4 8 10 20 40 80 8*0 1 2 4 8 10 20 40 80 8*0 1 2 4 8 10 20 40 80 8*0 1 2 4 8 10 20 40 80 198*0
  //   ff
  //   contents of rom_16 (hex, n*v repeats v):
  //   0 1
  //   地址相同，按钮相同，穷举集合相同，所以需要增加参数区分
  //   中断电路，本质是硬件驱动跳转并设置状态等待复位，硬件加强版jmp
  //   比较功能示波，前两个是比较，后两个默认寄存器复制线
  //   000端口是用于冗余数据
  //   保留设备选择位，为DMA准备
  //   001端口是内存地址
  //   002端口01是写入的内存数据
  //   004端口01是写入内存
  //   005端口ff启动保护模式
  //   007端口跳转数据
  //   此处断线，去与门，于是保护模式就不会影响设备切换
  //   6号设备，栈地址
  //   2寄存器入栈指令
  //   由内存存储区变成的缓冲区数据输入线
  //   006端口81复位中断数据
  //   先送地址到寄存器，随后送数据
  //   load
  //   11-1f号
  //   001端口是内存地址
  //   send
  //   4X4bit
  //   jmp
  //   out %ax， %dx 《穿越操作系统迷雾，从零实现操作系统》得到提示
  //   out %ax， %dx 两个寄存器，有可能两个地址，一个时钟，只是寄存器直连地址
  //   时钟1
  //   004端口01是写入内存
  //   004端口ff是读取内存
  //   00120006，0个寄存器，0设备，12指令，06地址读取内存至缓冲区
  //   10020009，1个寄存器，0设备，02指令，缓冲区0号寄存器至09寄存器
  //   10030009，1个寄存器，0设备，02指令，缓冲区1号寄存器至09寄存器
  //   10040009，1个寄存器，0设备，02指令，缓冲区2号寄存器至09寄存器
  //   10050009，1个寄存器，0设备，02指令，缓冲区3号寄存器至09寄存器
  //   16088001，1个寄存器，6设备，08指令，01寄存器至栈寄存器
  //   004端口ff是读取内存
  //   005端口01启动跳转
  //   002端口01是写入的内存数据
  //   先送地址到寄存器，随后送数据
  //   jmp
  //   4bit分一组转8个开关
  //   用于以PC基地址偏移，或debug模式可用，由中断驱动
  //   栈地址读取，对于14个寄存器
  //   栈地址写入，对于栈寄存器
  //   jmp出RAM
  //   jmp回ROM
  //   pop
  //   不单独控制
  //   0x41，42，43，44，45，46，47，48，对应ABCDEFGH
  //   字符刷新计数器，是5个点阵读取完才加一
  //   send
  //   push
  //   立即数，条件jmp
  //   get
  //   PC入栈
  //   数据也是控制，在jmp出RAM
  //   去掉与门，直接受CPU控制写数，本质是寄存器是1的时候允许增加数据
  //   第一个寄存器没啥用原来是之前测试一直留存纪念到现在
  //   机器码
  //   写入丢数据，暂停到13行，看线，发现一开始数据控制线是0，可知漏掉数据于是从0开始而不是从1开始
  //   ASCII码减去数据得到点阵起点地址
  //   ASCII码减去数据得到点阵起点地址，改直接查表得起点地址
  //   contents of rom_18 (hex, n*v repeats v):
  //   66*0 5 a f 14 19 1e 23
  //   写完数据清空为0
  //   内存读取示波，查数据
  //   内存写入示波，查数据
  //   一个字符占五列，每个字符要查连续5个地址
  //   分频，5：1，点阵与字符地址
  //   读写内存数据共用了地址寄存器
  //   兼容PC默认读取，0PC
  //   通过手动点击按钮记录顺序产生存储数据指令
  //   去除一个寄存器看看时钟会减少，会不会在PC不增加时读取数据
  //   CPU控制外部设备的示波记录
  //   偏移1，因为出BUG了，原来第0地址也是点
  //   第二个计数器模拟USB芯片时钟
  //   点阵码
  //   点阵库
  //   contents of rom_20 (hex, n*v repeats v):
  //   1f 28 48 28 1f ff 49 49 49 36 1c 22 41 41 22 7f 41 41 22 1c ff 4*49 ff 48 48 48 40 1c 22 49 49 26 ff
  //   8 8 8 ff 6*0 10 5*0 40 20 6*0 40 20 10 4*0 80 40 20 0 0 40 20 10 8 4 2 1 0 40 20 10 8 4 2 1 0 40 20
  //   10 8 4 2 1 0 40 20 10 8 4 2 1 0 40 20 10 8 4 2 1 0 40 20 10 8 4 2 1 0 40 20 10 8 4 2 1 0 40 20 10 8
  //   4 2 1 0 40 20 10 8 4 2 1 0 40 20 10 8 4 2 1 0 40 20 10 8 4 2 1 0 40 20 10 8 4 2 1 0 40 20 10 8 4 2 1
  //   0 40 20 10 8 4 2 1 0 40 20 10 8 4 2 1 0 40 20 10 8 4 2 1 0 40 20 10 8 4 2 1 0 40 20 10 8 4 2 1 0 40
  //   20 10 8 4 2 1
  //   追加脏位dirty bit控制
  //   替换最少使用者
  //   32bit 2组4路组相联映射cache共8块
  //   仅仅复位用，不作延时
  //   仅仅复位用，不作延时，又去除一个寄存器，执行完毕后复位
  //   在更新IR寄存器时启动，CPU不执行，此时写入缓冲寄存器清空，清空记号会在CPU执行后紧接着下个时钟输出，所以不会干扰CPU下个数据连续写入
  //   显示器
  //   写入，命中替换
  //   读取分线
  //   数据分线
  //   地址分线
  //   写回分线
  //   靠中断按钮执行多时钟
  //   最低位地址控制
  //   原上地址线改为加载数据线为dirty bit更新
  //   优先级数据覆盖默认0
  //   写完数据清空存储区为0
  //   读取，命中旧替换，不命中也替换
  //   写入，再次读取时写入内存再替换
  //   读取时，并且没选中，加一
  //   点亮时，取消默认进入第一设备，同一时配套地址与数据
  //   32bit数据
  //   PC突然中断，立即保存，或可另一寄存器
  //   入栈载数+1，出栈载数-1，刚好差1地址，于是追加出栈寄存器
  //   入栈地址-1，出栈地址+1，先写数据再-1，地址由高往低生长
  //   写入丢数据，暂停到13行，看线，发现一开始数据控制线是0，可知漏掉数据于是从0开始而不是从1开始
  //   逐帧观察发现执行两次，改指令控制时钟
  //   增加栈数据回流
  //   读数据与cache，后续会增加中断进行断线重连仿真速度差距
  //   替换最少使用者
  //   替换最少使用者
  //   替换最少使用者
  //   替换最少使用者
  //   替换最少使用者
  //   替换最少使用者
  //   读数据
  //   PC启动读指令
  //   8bit地址
  //   8bit地址
  //   8bit地址
  //   8bit地址
  //   8bit地址
  //   8bit地址
  //   8bit地址
  //   8bit地址
  //   PC，默认
  //   和IR同相，和ld反相
  //   参考缓冲区时钟取反
  //   追加脏位dirty bit控制
  //   排线
  //   选线亮说明要覆盖数据了
  //   32bit数据
  //   32bit数据
  //   32bit数据
  //   32bit数据
  //   选线亮说明要覆盖数据了
  //   32bit数据
  //   32bit数据
  //   32bit数据
  //   32bit数据
  //   中断，在飞线后产生切换设备指令5508880情况下，此部件退化为切换选线，切换到中断向量查找ROM
  //   没有料到会震荡，于是换到了寄存器线接入
  //   读指令，前周期读与后周期读，原来可以直接受时钟分频后控制，就是一时钟读，一时钟写，直接改分频时钟非原始时钟
  //   显示器
  //   写完数据清空为0
  //   来自中断cache的反馈控制或门
  //   采用原始按bit控制，可接入按地址控制发展历程，重复旧故事
  //   接入不同设备，一套地址数据控制
  //   入栈打开选线
  //   追加脏位，数据被修改就是0，说明不是最新数据
  //   注意在数据更新同时脏位设置为1说明是靠谱最新数据
  //   追加脏位，数据被修改就是0，说明不是最新数据
  //   注意在数据更新同时脏位设置为1说明是靠谱最新数据
  //   接入不同设备，一套地址数据控制
  //   显示器
  //   集成地址数据选择后发现分离RAM，发现数据源控制
  //   测试填充虚假数据0模拟其他都不行
  //   命中后查dirty bit 决定是否撤回读取
  //   32bit 全相联映射cache
  //   测试填充虚假数据0模拟其他都不行
  //   命中后查dirty bit 决定是否撤回读取
  //   缓存与内存
  //   显示器时钟适配CPU 高频改低频显示
  //   写入丢数据，暂停到13行，看线，发现一开始数据控制线是0，可知漏掉数据于是从0开始而不是从1开始
  //   比较地址发现命中，同时输出数据与状态
  //   比较地址发现命中，同时输出数据与状态
  //   读指令，前周期读与后周期读
  //   读指令
  //   读指令，和IR寄存器反相，记录上一个状态就得有数据，又发现RAM时钟
  //   两两比较电路，数值大的出来，就是复位少的出来
  //   两两比较电路，数值大的出来，就是复位少的出来
  //   只在加载数据时检测命中，则产生数据cache
  //   程序计时器-现在是哪个进程
  //   计数模型
  //   比较最大数，并和原寄存器比较后输出对应编码找到所在寄存器
  //   比较最大数，并和原寄存器比较后输出对应编码找到所在寄存器
  //   程序上限计时器-有多少个进程
  //   三个版本测试
  //   替换最少使用者
  //   替换最少使用者
  //   8bit地址
  //   8bit地址
  //   反相时钟解决入栈与ld同时亮问题
  //   32bit数据
  //   32bit数据
  //   32bit数据
  //   断线后瞪电路发现直接屏蔽发现分别控制于是接入只判断命中否
  //   断线后瞪电路发现直接屏蔽发现分别控制于是接入只判断命中否
  //   比较出1后立即取消最大数查找，切换到冗余
  //   比较出1后立即取消最大数查找，切换到冗余
  //   下一个程序寄存器-如果新加入进程对应第几个寄存器
  //   记录切换前的数据
  //   命中后查dirty bit 决定是否撤回读取，没有命中是0，撤回操作也是0，如此实现启动写回，不增加额外控制电路如或门之类
  //   追加脏位控制数据，草稿纸上安排后发现可以通过“反悔”，或者撤回操作
  //   命中后查dirty bit 决定是否撤回读取，没有命中是0，撤回操作也是0，如此实现启动写回，不增加额外控制电路如或门之类
  //   追加脏位控制数据，草稿纸上安排后发现可以通过“反悔”，或者撤回操作
  //   追加脏位，数据被修改就是0，说明不是最新数据
  //   注意在数据更新同时脏位设置为1说明是靠谱最新数据
  //   锁存复位0屏蔽外输入，产生一个信号，长时间转单脉冲
  //   PCB修改状态，避免第一次出栈
  //   PCB修改栈数字，记录入栈后数据，PCB记录是否存储CPU寄存器，PCB记录PC数字，程序停留到哪一步了
  //   PC2+1+SP2+1+0+0,每次执行程序都要跑恢复ROM片程序还原寄存器，第一次执行程序栈穿底弹出所以不能第一次出栈，要控制
  //   追加默认0数据选线，解决不命中导致脏位输出乱码引起后续数据爆红
  //   追加默认0数据选线，解决不命中导致脏位输出乱码引起后续数据爆红
  //   连接cache输送，控制，反馈电路后屏蔽指令寄存相同数据导致意外乱码
  //   先亮，一个寄存器，然后复位，发现不行，再追加复位，线并入，改正反，发现真能完事
  //   00187111，00086111，00085111，00084111，00083111
  //   00187111，00186111，00185111，00184111，00183111
  //   50080000，跳转复位，控制位不兼容，改出入栈
  //   00080007，00186007，00081607，00081507，合并三位到最后一位
  //   50180000，跳转复位，6518000，65180010，带第二计数器复位，77180010
  //   00080000，00080111，00080111，000781111，00781111，00187111
  //   但是直接接入新电路，读取缓冲数据模拟USB数据接收南北桥芯片
  //   启动中断时停止计数，切换完进程开始计数
  //   靠冗余实现指令失效，没有对应数据可读于是不读取出界数据
  //   进程数据，别管怎么来的，先造一点数据检测电路
  //   出界返回，0到11共4个数字轮流，所谓指针的强行实体化
  //   锁死，时间片到，处理中断程序不计数，待复位按钮
  //   时间片
  //   contents of rom_22 (hex, n*v repeats v):
  //   80111
  //   出界返回，0到11共4个数字轮流，所谓指针的强行实体化
  //   下一个程序寄存器-如果新加入进程对应第几个寄存器
  //   下一个程序寄存器-如果新加入进程对应第几个寄存器
  //   contents of rom_23 (hex, n*v repeats v):
  //   11223344 34522344 55555544 55667788 22225555 aaafffc 77777777 66669555
  //   删除一个寄存器还能跑
  //   锁存复位0屏蔽外输入，产生一个信号
  //   中断信号，程序中断脉冲
  //   下一轮程序寄存器-如果旧进程结束，第二轮起点寄存器会不一样
  //   替换最少使用者
  //   替换最少使用者
  //   替换最少使用者
  //   下一轮程序寄存器-如果旧进程结束，第二轮起点寄存器会不一样
  //   8bit地址
  //   8bit地址
  //   8bit地址
  //   PC计数器v2,中断程序执行完自动复位
  //   8bit地址
  //   选线亮说明要覆盖数据了
  //   32bit数据
  //   32bit数据
  //   32bit数据
  //   32bit数据
  //   加载，写回
  //   追加脏位dirty bit控制
  //   加载，冗余，写回
  //   还原现场出栈
  //   N个中断源，按线路上下位置选程序，但优先级还是副作用，不考虑优先级，仅仅是选择程序，于是还得想办法屏蔽优先级两个按钮同时亮情况
  //   追加脏位，数据被修改就是0，说明不是最新数据
  //   注意在数据更新同时脏位设置为1说明是靠谱最新数据
  //   程序计时器-现在是哪个进程
  //   参考自RAM读取的四个缓冲寄存器
  //   发现0时程序不入，重返后，读加载程序发现需要寄存器于是产生一个时钟延时，于是追加延时，重启载入
  //   应该是计数后锁死，然后复位还要一个时钟，所以4不能复位，增加一个情况亮，发现原来顶上是0会屏蔽输入数据，那cache跑起来原来是读取是启动1所以没有BUG，是意外连线整好没法意识到BUG旧解禁BUG
  //   4 个进程控制信息 寄存器
  //   应该是计数后锁死，然后复位还要一个时钟，所以4不能复位
  //   32bit 全相联映射cache共四块
  //   测试填充虚假数据0模拟其他都不行
  //   命中后查dirty bit 决定是否撤回读取
  //   程序上限计时器-最多有多少个进程
  //   进程出界提示
  //   PC计数器v2，主要由于目前没来的及发现更多参考文献，直接用另一个计数器启动程序，来解决执行指令，但是保护现场和PC计数器情况
  //   比较地址发现命中，同时输出数据与状态
  //   应该是计数后锁死，然后复位还要一个时钟，所以4不能复位，增加一个情况亮，发现原来顶上是0会屏蔽输入数据
  //   7 个进程控制信息 寄存器
  //   程序计时器-现在是哪个进程
  //   以及由时间片进程运行不见代码，网上搜索出时钟中断，考虑到主时钟保留地址，决意追加第三PC计数器
  //   绿色线亮表示进入到哪个中断处理程序，仅仅标识用，实际没啥功能，可以去掉
  //   应该是计数后锁死，然后复位还要一个时钟，所以4不能复位，增加一个情况亮，发现原来顶上是0会屏蔽输入数据，那cache跑起来原来是读取是启动1所以没有BUG，是意外连线整好没法意识到BUG旧解禁BUG
  //   两两比较电路，数值大的出来，就是复位少的出来
  //   中断向量查询与中断处理程序
  //   比较最大数，并和原寄存器比较后输出对应编码找到所在寄存器
  //   0是冗余指令表示没有中断，其实是执行无效指令
  //   最早在蝴蝶中断器中出现的两个选择器堆叠
  //   冗余，以后可能用到
  //   存储PC计数器的寄存器
  //   参考自网络提到的栈，进行实体化
  //   0时允许接收与复位1时允许接收
  //   PCB状态，012，防止0时无栈数据而继续出栈
  //   存储现场地址的栈的寄存器
  //   接中断处理指令集
  //   仅按钮启动时复位
  //   存储兼容指令意外发现需要合并数据选择器
  //   断线后瞪电路发现直接屏蔽发现分别控制于是接入只判断命中否
  //   比较出1后立即取消最大数查找，切换到冗余
  //   与门或门启动数据与解除屏蔽实现复位
  //   命中后查dirty bit 决定是否撤回读取，没有命中是0，撤回操作也是0，如此实现启动写回，不增加额外控制电路如或门之类
  //   追加默认0数据选线，解决不命中导致脏位输出乱码引起后续数据爆红
  //   追加脏位控制数据，草稿纸上安排后发现可以通过“反悔”，或者撤回操作
  //   这四位没想好咋用
  //   进程控制队列，数据包含栈存寄存器现场保护，进程PC，进程控制位避免第一次就出栈
  //   PCB写回更新需求而产生的寄存器，似乎可以不用
  //   这一位处理栈，0-7，8，9，10，11，12，13
  //   这一位启动拓展寄存器
  //   这一位选择寄存器
  //   这一位控制切换CPU指令集，0是CPU用
  //   参考自cache命中读取优先编码器
  //   接CPU指令集输出寄存器
  //   写回按钮
  //   这四位没想好咋用
  //   这一位控制切换CPU指令集
  //   这一位处理栈，0-7，8，9，10，11，12，13
  //   这一位启动拓展寄存器
  //   这一位选择寄存器
  //   PC计数器v2,中断程序执行完自动复位
  //   中断向量查询与中断处理程序——集成一片版，半成品中断注册
  //   PC计数器v2，主要由于目前没来的及发现更多参考文献，直接用另一个计数器启动程序，来解决执行指令，但是保护现场和PC计数器情况
  //   N个中断源，按线路上下位置选程序，但优先级还是副作用，不考虑优先级，仅仅是选择程序，于是还得想办法屏蔽优先级两个按钮同时亮情况
  //   中断处理程序，集成到一个片里了，ROM改RAM的话需要增加写入和注册功能（电路追加
  //   替换成跳转地址，再替换常量，就成为可注册自定义中断处理程序入口地址
  //   锁死记录与复位
  //   0是冗余指令表示没有中断，其实是执行无效指令
  //   移植回原版本，发现复位有BUG后在原版改成功
  //   接中断处理指令集
  //   接CPU指令集输出寄存器
  //   这四位没想好咋用
  //   这一位控制切换CPU指令集，0是CPU用
  //   参考自cache命中读取优先编码器
  //   这一位处理栈，0-7，8，9，10，11，12，13
  //   这一位启动拓展寄存器
  //   这一位选择寄存器
  //   这四位没想好咋用
  //   这一位处理栈，0-7，8，9，10，11，12，13
  //   这一位启动拓展寄存器
  //   这一位选择寄存器
  //   这一位控制切换CPU指令集
  //   PC计数器v2,中断程序执行完自动复位
  //   猜想以后可以PCv2退化为PCv1,但是需要寄存器存储原PC数据且一中断就锁死，等待手动记录复位
  //   PC计数器v2，主要由于目前没来的及发现更多参考文献，直接用另一个计数器启动程序，来解决执行指令，但是保护现场和PC计数器情况
  //   中断向量查询与中断处理程序——集成一片版，半成品中断注册，实现复位与地址选线
  //   解决情况，在注册中断程序情况下，自定义自己中断，需要回到原来的RAM片，就直接使用原来的PC计数器而不是PCv2这样实现自定义中断
  //   0是冗余指令表示没有中断，其实是执行无效指令
  //   仅按钮启动时复位
  //   0时允许接收与复位1时允许接收
  //   接中断处理指令集
  //   这四位没想好咋用
  //   这一位处理栈，0-7，8，9，10，11，12，13
  //   这一位启动拓展寄存器
  //   这一位选择寄存器
  //   这一位控制切换CPU指令集，0是CPU用
  //   参考自cache命中读取优先编码器
  //   接CPU指令集输出寄存器
  //   重排后，含义明确的电路，往回是反馈电路，区别与只管亮灭在一个时刻借灯
  //   0时允许接收与复位1时允许接收
  //   这四位没想好咋用
  //   仅按钮启动时复位
  //   这一位启动拓展寄存器
  //   这一位控制切换CPU指令集
  //   这一位处理栈，0-7，8，9，10，11，12，13
  //   这一位选择寄存器
endmodule
